// Logisim project luiz_gabriel_antunes_sena_novo_16bits.circ as structural Verilog: 22 circuits, main circuit soma_1b
module main (
);

  wire adapter_display_1_d_clk, adapter_display_1_d_write, adapter_keyboard_1_clk_keyboard,
       adapter_keyboard_1_e_keyboard, data_address, e_clk, flags_reg_1_a_maior_out, flags_reg_1_carry_out,
       flags_reg_1_iguais_out, flags_reg_1_zero_out, input_output, or_1_out, s_clk, uc_struct_1_bus_1,
       uc_struct_1_enable_acc, uc_struct_1_enable_iar, uc_struct_1_enable_r0, uc_struct_1_enable_r1,
       uc_struct_1_enable_r2, uc_struct_1_enable_r3, uc_struct_1_enable_ram, uc_struct_1_init,
       uc_struct_1_set_acc, uc_struct_1_set_flags, uc_struct_1_set_iar, uc_struct_1_set_ir,
       uc_struct_1_set_mar, uc_struct_1_set_r0, uc_struct_1_set_r1, uc_struct_1_set_r2, uc_struct_1_set_r3,
       uc_struct_1_set_ram, uc_struct_1_set_tmp, ula_1_a_maior, ula_1_c_out, ula_1_iguais, ula_1_zero;
  wire [2:0] uc_struct_1_to_ula;
  wire [5:0] uc_struct_1_step;
  wire [6:0] adapter_display_1_data_display, keyboard_1_data;
  wire [15:0] ACC_q, bus1_out_3, controlled_buffer_1_out, IAR_q, IR_q, MAR_q, R0_q, R1_q, R2_q, R3_q, TMP_q,
       ula_1_s;

  // Probe on controlled_buffer_1_out
  assign controlled_buffer_1_out = uc_struct_1_enable_r0 ? R0_q : 16'bz;  // Controlled_Buffer controlled_buffer_1
  Register #(.width(16)) R0 (.D(controlled_buffer_1_out), .Q(R0_q), .clk(uc_struct_1_set_r0));  // open: en, clr
  Register #(.width(16)) TMP (.D(controlled_buffer_1_out), .Q(TMP_q), .clk(uc_struct_1_set_tmp));  // open: en, clr
  assign controlled_buffer_1_out = uc_struct_1_enable_r1 ? R1_q : 16'bz;  // Controlled_Buffer controlled_buffer_2
  Register #(.width(16)) R1 (.D(controlled_buffer_1_out), .Q(R1_q), .clk(uc_struct_1_set_r1));  // open: en, clr
  bus_1 bus1 (.in_1(TMP_q), .in_2(uc_struct_1_bus_1), .out_3(bus1_out_3));
  assign controlled_buffer_1_out = uc_struct_1_enable_r2 ? R2_q : 16'bz;  // Controlled_Buffer controlled_buffer_3
  Register #(.width(16)) R2 (.D(controlled_buffer_1_out), .Q(R2_q), .clk(uc_struct_1_set_r2));  // open: en, clr
  ula ula_1 (
    .A(controlled_buffer_1_out), .B(bus1_out_3), .op(uc_struct_1_to_ula), .s(ula_1_s), .c_out(ula_1_c_out),
    .a_maior(ula_1_a_maior), .iguais(ula_1_iguais), .zero(ula_1_zero));
  assign controlled_buffer_1_out = uc_struct_1_enable_r3 ? R3_q : 16'bz;  // Controlled_Buffer controlled_buffer_4
  Register #(.width(16)) R3 (.D(controlled_buffer_1_out), .Q(R3_q), .clk(uc_struct_1_set_r3));  // open: en, clr
  flags_reg flags_reg_1 (
    .carry(ula_1_c_out), .a_maior(ula_1_a_maior), .iguais(ula_1_iguais), .zero(ula_1_zero),
    .in_5(uc_struct_1_set_flags), .carry_out(flags_reg_1_carry_out), .a_maior_out(flags_reg_1_a_maior_out),
    .iguais_out(flags_reg_1_iguais_out), .zero_out(flags_reg_1_zero_out));
  Register #(.width(16)) ACC (.D(ula_1_s), .Q(ACC_q), .clk(uc_struct_1_set_acc));  // open: en, clr
  assign controlled_buffer_1_out = uc_struct_1_enable_acc ? ACC_q : 16'bz;  // Controlled_Buffer controlled_buffer_5
  uc_struct uc_struct_1 (
    .carry_out_flag(flags_reg_1_carry_out), .a_larger_flag(flags_reg_1_a_maior_out),
    .equal_flag(flags_reg_1_iguais_out), .zero_flag(flags_reg_1_zero_out), .ir(IR_q),
    .data_address(data_address), .input_output(input_output), .init(uc_struct_1_init),
    .set_R0(uc_struct_1_set_r0), .set_R1(uc_struct_1_set_r1), .set_R2(uc_struct_1_set_r2),
    .set_R3(uc_struct_1_set_r3), .set_IR(uc_struct_1_set_ir), .set_MAR(uc_struct_1_set_mar),
    .set_IAR(uc_struct_1_set_iar), .set_ACC(uc_struct_1_set_acc), .set_RAM(uc_struct_1_set_ram),
    .set_TMP(uc_struct_1_set_tmp), .set_FLAGS(uc_struct_1_set_flags), .set_IO_clk(s_clk),
    .enable_R0(uc_struct_1_enable_r0), .enable_R1(uc_struct_1_enable_r1), .enable_R2(uc_struct_1_enable_r2),
    .enable_R3(uc_struct_1_enable_r3), .bus_1(uc_struct_1_bus_1), .enable_IAR(uc_struct_1_enable_iar),
    .enable_RAM(uc_struct_1_enable_ram), .enable_ACC(uc_struct_1_enable_acc), .enable_IO_clk(e_clk),
    .to_ULA(uc_struct_1_to_ula), .step(uc_struct_1_step));
  Register #(.width(16)) MAR (.D(controlled_buffer_1_out), .Q(MAR_q), .clk(uc_struct_1_set_mar));  // open: en, clr
  // LedBar #(.inputtype("row"), .matrixcols(6)) ledbar_1: pin names not known; wires that end beside it: uc_struct_1_step
  RAM #(.addrWidth(16), .dataWidth(16), .databus("bidir")) ram_1 (
    .addr(MAR_q), .we(uc_struct_1_set_ram), .oe(uc_struct_1_enable_ram), .clk(or_1_out));  // open: data
  or or_1 (or_1_out, uc_struct_1_set_ram, uc_struct_1_enable_ram);
  LED led_1 (.in(uc_struct_1_init));
  Register #(.width(16)) IR (.D(controlled_buffer_1_out), .Q(IR_q), .clk(uc_struct_1_set_ir));  // open: en, clr
  Register #(.width(16)) IAR (.D(controlled_buffer_1_out), .Q(IAR_q), .clk(uc_struct_1_set_iar));  // open: en, clr
  assign controlled_buffer_1_out = uc_struct_1_enable_iar ? IAR_q : 16'bz;  // Controlled_Buffer controlled_buffer_6
  adapter_keyboard adapter_keyboard_1 (
    .e_clk(e_clk), .data_address(data_address), .input_output(input_output), .s_clk(s_clk),
    .data_keyboard(keyboard_1_data), .barramento(controlled_buffer_1_out),
    .clk_keyboard(adapter_keyboard_1_clk_keyboard), .e_keyboard(adapter_keyboard_1_e_keyboard));
  Keyboard keyboard_1 (
    .clk(adapter_keyboard_1_clk_keyboard), .re(adapter_keyboard_1_e_keyboard), .data(keyboard_1_data));  // open: clr, avail
  adapter_display adapter_display_1 (
    .data_address(data_address), .input_output(input_output), .s_clk(s_clk),
    .barramento(controlled_buffer_1_out), .d_clk(adapter_display_1_d_clk),
    .d_write(adapter_display_1_d_write), .data_display(adapter_display_1_data_display));
  TTY tty_1 (
    .data(adapter_display_1_data_display), .clk(adapter_display_1_d_clk), .we(adapter_display_1_d_write));  // open: clr

  // Notes on the sheet:
  //   Luiz Gabriel Antunes Sena
endmodule

module soma_1b (
  input  c_in,
  input  a,
  input  b,
  output s,
  output c_out
);

  wire and_1_out, and_2_out, and_3_out, xor_1_out;

  xor xor_1 (xor_1_out, a, b);
  and and_1 (and_1_out, a, b);
  and and_2 (and_2_out, c_in, a);
  and and_3 (and_3_out, c_in, b);
  xor xor_2 (s, xor_1_out, c_in);
  or or_1 (c_out, and_1_out, and_2_out, and_3_out);
endmodule

module soma_8b (
  input  [15:0] A,
  input  c_in,
  input  [15:0] B,
  output [15:0] S,
  output c_out
);

  wire soma_1b_1_c_out, soma_1b_2_c_out, soma_1b_3_c_out, soma_1b_4_c_out, soma_1b_5_c_out, soma_1b_6_c_out,
       soma_1b_7_c_out, soma_1b_8_c_out, soma_1b_9_c_out, soma_1b_10_c_out, soma_1b_11_c_out,
       soma_1b_12_c_out, soma_1b_13_c_out, soma_1b_14_c_out, soma_1b_15_c_out;

  soma_1b soma_1b_1 (.a(A[0]), .b(B[0]), .c_in(c_in), .c_out(soma_1b_1_c_out), .s(S[0]));
  soma_1b soma_1b_2 (.a(A[1]), .b(B[1]), .c_in(soma_1b_1_c_out), .c_out(soma_1b_2_c_out), .s(S[1]));
  soma_1b soma_1b_3 (.a(A[2]), .b(B[2]), .c_in(soma_1b_2_c_out), .c_out(soma_1b_3_c_out), .s(S[2]));
  soma_1b soma_1b_4 (.a(A[3]), .b(B[3]), .c_in(soma_1b_3_c_out), .c_out(soma_1b_4_c_out), .s(S[3]));
  soma_1b soma_1b_5 (.a(A[4]), .b(B[4]), .c_in(soma_1b_4_c_out), .c_out(soma_1b_5_c_out), .s(S[4]));
  soma_1b soma_1b_6 (.a(A[5]), .b(B[5]), .c_in(soma_1b_5_c_out), .c_out(soma_1b_6_c_out), .s(S[5]));
  soma_1b soma_1b_7 (.a(A[6]), .b(B[6]), .c_in(soma_1b_6_c_out), .c_out(soma_1b_7_c_out), .s(S[6]));
  soma_1b soma_1b_8 (.a(A[7]), .b(B[7]), .c_in(soma_1b_7_c_out), .c_out(soma_1b_8_c_out), .s(S[7]));
  soma_1b soma_1b_9 (.a(A[8]), .b(B[8]), .c_in(soma_1b_8_c_out), .c_out(soma_1b_9_c_out), .s(S[8]));
  soma_1b soma_1b_10 (.a(A[9]), .b(B[9]), .c_in(soma_1b_9_c_out), .c_out(soma_1b_10_c_out), .s(S[9]));
  soma_1b soma_1b_11 (.a(A[10]), .b(B[10]), .c_in(soma_1b_10_c_out), .c_out(soma_1b_11_c_out), .s(S[10]));
  soma_1b soma_1b_12 (.a(A[11]), .b(B[11]), .c_in(soma_1b_11_c_out), .c_out(soma_1b_12_c_out), .s(S[11]));
  soma_1b soma_1b_13 (.a(A[12]), .b(B[12]), .c_in(soma_1b_12_c_out), .c_out(soma_1b_13_c_out), .s(S[12]));
  soma_1b soma_1b_14 (.a(A[13]), .b(B[13]), .c_in(soma_1b_13_c_out), .c_out(soma_1b_14_c_out), .s(S[13]));
  soma_1b soma_1b_15 (.a(A[14]), .b(B[14]), .c_in(soma_1b_14_c_out), .c_out(soma_1b_15_c_out), .s(S[14]));
  soma_1b soma_1b_16 (.a(A[15]), .b(B[15]), .c_in(soma_1b_15_c_out), .c_out(c_out), .s(S[15]));
endmodule

module memoria_1b (
  input  i,
  input  s,
  output d
);

  wire nand_1_out, nand_2_out, nand_4_out;

  nand nand_1 (nand_1_out, i, s);
  nand nand_2 (nand_2_out, nand_1_out, s);
  nand nand_3 (d, nand_1_out, nand_4_out);
  nand nand_4 (nand_4_out, d, nand_2_out);
endmodule

module memoria_8b (
  input  [7:0] i,
  input  s,
  output [7:0] d
);

  memoria_1b memoria_1b_1 (.i(i[0]), .s(s), .d(d[0]));
  memoria_1b memoria_1b_2 (.i(i[1]), .s(s), .d(d[1]));
  memoria_1b memoria_1b_3 (.i(i[2]), .s(s), .d(d[2]));
  memoria_1b memoria_1b_4 (.i(i[3]), .s(s), .d(d[3]));
  memoria_1b memoria_1b_5 (.i(i[4]), .s(s), .d(d[4]));
  memoria_1b memoria_1b_6 (.i(i[5]), .s(s), .d(d[5]));
  memoria_1b memoria_1b_7 (.i(i[6]), .s(s), .d(d[6]));
  memoria_1b memoria_1b_8 (.i(i[7]), .s(s), .d(d[7]));
endmodule

module registrador_set_enable (
  input  [7:0] i,
  input  set,
  input  enable,
  output [7:0] d
);

  wire [7:0] bit_extender_1_out, memoria_8b_1_d;

  memoria_8b memoria_8b_1 (.i(i), .s(set), .d(memoria_8b_1_d));
  assign bit_extender_1_out = {{7{enable}}, enable};  // Bit_Extender bit_extender_1
  assign d = memoria_8b_1_d & bit_extender_1_out;  // AND_Gate and_1, 8 bits wide
endmodule

// ULA
module ula (
  input  [2:0] op,
  input  [15:0] A,
  input  [15:0] B,
  output [15:0] s,
  output c_out,
  output a_maior,
  output iguais,
  output zero
);

  wire shift_l_1_c_out, shift_r_1_c_out, soma_8b_1_c_out;
  wire [15:0] and_1_out, comp_8b_1_c, not_1_out, or_1_out, shift_l_1_d, shift_r_1_d, soma_8b_1_s, xor_1_out;

  assign not_1_out = ~B;  // NOT_Gate not_1, 16 bits wide
  soma_8b soma_8b_1 (.A(A), .B(B), .c_out(soma_8b_1_c_out), .S(soma_8b_1_s));  // open: c_in
  shift_r shift_r_1 (.i(B), .c_out(shift_r_1_c_out), .d(shift_r_1_d));  // open: c_in
  shift_l shift_l_1 (.i(B), .c_out(shift_l_1_c_out), .d(shift_l_1_d));  // open: c_in
  assign and_1_out = A & B;  // AND_Gate and_1, 16 bits wide
  assign or_1_out = A | B;  // OR_Gate or_1, 16 bits wide
  assign xor_1_out = A ^ B;  // XOR_Gate xor_1, 16 bits wide
  comp_8b comp_8b_1 (.A(A), .B(B), .C(comp_8b_1_c), .a_maior(a_maior), .iguais(iguais));
  Multiplexer #(.select(3), .width(16)) multiplexer_1 (
    .in0(soma_8b_1_s), .in1(shift_r_1_d), .in2(shift_l_1_d), .in3(not_1_out), .in4(and_1_out),
    .in5(or_1_out), .in6(xor_1_out), .in7(comp_8b_1_c), .out(s), .sel(op));
  Multiplexer #(.select(3)) multiplexer_2 (
    .in0(soma_8b_1_c_out), .in1(shift_r_1_c_out), .in2(shift_l_1_c_out), .in3(1'b0), .in4(1'b0), .in5(1'b0),
    .in6(1'b0), .in7(1'b0), .out(c_out), .sel(op));
  nor nor_1 (zero, s[0], s[1], s[2], s[3], s[4], s[5], s[6], s[7], s[8], s[9], s[10], s[11], s[12], s[13], s[14], s[15]);
endmodule

module shift_r (
  input  c_in,
  input  [15:0] i,
  output [15:0] d,
  output c_out
);


  assign c_out = i[0];
  assign d = {c_in, i[15:1]};
endmodule

module shift_l (
  input  c_in,
  input  [15:0] i,
  output [15:0] d,
  output c_out
);


  assign c_out = i[15];
  assign d = {i[14:0], c_in};
endmodule

module comp_1b (
  input  iguais_ant,
  input  a_maior_ant,
  input  a,
  input  b,
  output c,
  output iguais,
  output a_maior
);

  wire and_2_out;

  xor xor_1 (c, a, b);
  and and_1 (iguais, ~c, iguais_ant);  // AND_Gate
  and and_2 (and_2_out, a, iguais_ant, c);
  or or_1 (a_maior, and_2_out, a_maior_ant);
endmodule

module comp_8b (
  input  [15:0] A,
  input  [15:0] B,
  output [15:0] C,
  output a_maior,
  output iguais
);

  wire comp_1b_1_a_maior, comp_1b_1_iguais, comp_1b_2_a_maior, comp_1b_2_iguais, comp_1b_3_a_maior,
       comp_1b_3_iguais, comp_1b_4_a_maior, comp_1b_4_iguais, comp_1b_5_a_maior, comp_1b_5_iguais,
       comp_1b_6_a_maior, comp_1b_6_iguais, comp_1b_7_a_maior, comp_1b_7_iguais, comp_1b_8_a_maior,
       comp_1b_8_iguais, comp_1b_9_a_maior, comp_1b_9_iguais, comp_1b_10_a_maior, comp_1b_10_iguais,
       comp_1b_11_a_maior, comp_1b_11_iguais, comp_1b_12_a_maior, comp_1b_12_iguais, comp_1b_13_a_maior,
       comp_1b_13_iguais, comp_1b_14_a_maior, comp_1b_14_iguais, comp_1b_15_a_maior, comp_1b_15_iguais;

  comp_1b comp_1b_1 (
    .a(A[0]), .b(B[0]), .iguais_ant(1'b1), .a_maior_ant(1'b0), .iguais(comp_1b_1_iguais),
    .a_maior(comp_1b_1_a_maior), .c(C[0]));
  comp_1b comp_1b_2 (
    .a(A[1]), .b(B[1]), .iguais_ant(comp_1b_1_iguais), .a_maior_ant(comp_1b_1_a_maior),
    .iguais(comp_1b_2_iguais), .a_maior(comp_1b_2_a_maior), .c(C[1]));
  comp_1b comp_1b_3 (
    .a(A[2]), .b(B[2]), .iguais_ant(comp_1b_2_iguais), .a_maior_ant(comp_1b_2_a_maior),
    .iguais(comp_1b_3_iguais), .a_maior(comp_1b_3_a_maior), .c(C[2]));
  comp_1b comp_1b_4 (
    .a(A[3]), .b(B[3]), .iguais_ant(comp_1b_3_iguais), .a_maior_ant(comp_1b_3_a_maior),
    .iguais(comp_1b_4_iguais), .a_maior(comp_1b_4_a_maior), .c(C[3]));
  comp_1b comp_1b_5 (
    .a(A[4]), .b(B[4]), .iguais_ant(comp_1b_4_iguais), .a_maior_ant(comp_1b_4_a_maior),
    .iguais(comp_1b_5_iguais), .a_maior(comp_1b_5_a_maior), .c(C[4]));
  comp_1b comp_1b_6 (
    .a(A[5]), .b(B[5]), .iguais_ant(comp_1b_5_iguais), .a_maior_ant(comp_1b_5_a_maior),
    .iguais(comp_1b_6_iguais), .a_maior(comp_1b_6_a_maior), .c(C[5]));
  comp_1b comp_1b_7 (
    .a(A[6]), .b(B[6]), .iguais_ant(comp_1b_6_iguais), .a_maior_ant(comp_1b_6_a_maior),
    .iguais(comp_1b_7_iguais), .a_maior(comp_1b_7_a_maior), .c(C[6]));
  comp_1b comp_1b_8 (
    .a(A[7]), .b(B[7]), .iguais_ant(comp_1b_7_iguais), .a_maior_ant(comp_1b_7_a_maior),
    .iguais(comp_1b_8_iguais), .a_maior(comp_1b_8_a_maior), .c(C[7]));
  comp_1b comp_1b_9 (
    .a(A[8]), .b(B[8]), .iguais_ant(comp_1b_8_iguais), .a_maior_ant(comp_1b_8_a_maior),
    .iguais(comp_1b_9_iguais), .a_maior(comp_1b_9_a_maior), .c(C[8]));
  comp_1b comp_1b_10 (
    .a(A[9]), .b(B[9]), .iguais_ant(comp_1b_9_iguais), .a_maior_ant(comp_1b_9_a_maior),
    .iguais(comp_1b_10_iguais), .a_maior(comp_1b_10_a_maior), .c(C[9]));
  comp_1b comp_1b_11 (
    .a(A[10]), .b(B[10]), .iguais_ant(comp_1b_10_iguais), .a_maior_ant(comp_1b_10_a_maior),
    .iguais(comp_1b_11_iguais), .a_maior(comp_1b_11_a_maior), .c(C[10]));
  comp_1b comp_1b_12 (
    .a(A[11]), .b(B[11]), .iguais_ant(comp_1b_11_iguais), .a_maior_ant(comp_1b_11_a_maior),
    .iguais(comp_1b_12_iguais), .a_maior(comp_1b_12_a_maior), .c(C[11]));
  comp_1b comp_1b_13 (
    .a(A[12]), .b(B[12]), .iguais_ant(comp_1b_12_iguais), .a_maior_ant(comp_1b_12_a_maior),
    .iguais(comp_1b_13_iguais), .a_maior(comp_1b_13_a_maior), .c(C[12]));
  comp_1b comp_1b_14 (
    .a(A[13]), .b(B[13]), .iguais_ant(comp_1b_13_iguais), .a_maior_ant(comp_1b_13_a_maior),
    .iguais(comp_1b_14_iguais), .a_maior(comp_1b_14_a_maior), .c(C[13]));
  comp_1b comp_1b_15 (
    .a(A[14]), .b(B[14]), .iguais_ant(comp_1b_14_iguais), .a_maior_ant(comp_1b_14_a_maior),
    .iguais(comp_1b_15_iguais), .a_maior(comp_1b_15_a_maior), .c(C[14]));
  comp_1b comp_1b_16 (
    .a(A[15]), .b(B[15]), .iguais_ant(comp_1b_15_iguais), .a_maior_ant(comp_1b_15_a_maior), .iguais(iguais),
    .a_maior(a_maior), .c(C[15]));
endmodule

module bus_1 (
  input  [15:0] in_1,
  input  in_2,
  output [15:0] out_3
);

  Multiplexer #(.width(16)) multiplexer_1 (.in0(in_1), .in1(16'h1), .out(out_3), .sel(in_2));
endmodule

module uc (
  input  [7:0] IR,
  output enable_BUS_1,
  output enable_IAR,
  output enable_RAM,
  output enable_ACC,
  output enable_IO_clk_e,
  output set_IR,
  output set_MAR,
  output set_IAR,
  output set_ACC,
  output set_RAM,
  output set_TMP,
  output set_FLAGS,
  output set_R0,
  output enable_R0,
  output set_R1,
  output enable_R1,
  output set_R2,
  output enable_R2,
  output set_R3,
  output enable_R3,
  output [2:0] to_ULA
);

  wire and_5_out, and_6_out, and_7_out, and_8_out, and_9_out, and_10_out, and_11_out, and_12_out, and_16_out,
       and_17_out, and_18_out, and_19_out, and_20_out, and_21_out, and_22_out, and_23_out, and_24_out,
       and_25_out, and_26_out, and_27_out, and_28_out, and_29_out, and_30_out, and_31_out, and_32_out,
       clock_stepper_1_enable, clock_stepper_1_s1, clock_stepper_1_s2, clock_stepper_1_s3,
       clock_stepper_1_s4, clock_stepper_1_s5, clock_stepper_1_set, decoder_1_out0, decoder_1_out1,
       decoder_1_out2, decoder_1_out3, decoder_2_out0, decoder_2_out1, decoder_2_out2, decoder_2_out3,
       decoder_4_out0, decoder_4_out1, decoder_4_out2, decoder_4_out3, not_1_out, or_6_out, or_7_out,
       or_8_out, or_9_out, or_10_out, undriven, undriven_2;
  wire [7:0] decoder_3_out0;

  or or_1 (enable_R0, and_5_out, and_9_out);
  or or_2 (enable_R1, and_6_out, and_10_out);
  or or_3 (enable_R2, and_7_out, and_11_out);
  or or_4 (enable_R3, and_8_out, and_12_out);
  and and_1 (enable_IAR, clock_stepper_1_enable, or_6_out);
  and and_2 (enable_RAM, clock_stepper_1_enable, or_7_out);
  and and_3 (enable_ACC, clock_stepper_1_enable, or_8_out);
  and and_4 (enable_IO_clk_e, clock_stepper_1_enable, undriven);
  and and_5 (and_5_out, clock_stepper_1_enable, or_9_out, decoder_1_out0);
  and and_6 (and_6_out, clock_stepper_1_enable, or_9_out, decoder_1_out1);
  and and_7 (and_7_out, clock_stepper_1_enable, or_9_out, decoder_1_out2);
  and and_8 (and_8_out, clock_stepper_1_enable, or_9_out, decoder_1_out3);
  and and_9 (and_9_out, clock_stepper_1_enable, or_10_out, decoder_2_out0);
  and and_10 (and_10_out, clock_stepper_1_enable, or_10_out, decoder_2_out1);
  and and_11 (and_11_out, clock_stepper_1_enable, or_10_out, decoder_2_out2);
  and and_12 (and_12_out, clock_stepper_1_enable, or_10_out, decoder_2_out3);
  buf or_5 (enable_BUS_1, clock_stepper_1_s1);  // OR_Gate
  buf or_6 (or_6_out, clock_stepper_1_s1);  // OR_Gate
  buf or_7 (or_7_out, clock_stepper_1_s2);  // OR_Gate
  buf or_8 (or_8_out, clock_stepper_1_s3);  // OR_Gate
  buf or_9 (or_9_out, and_16_out);  // OR_Gate
  or or_10 (or_10_out, and_19_out, and_17_out);
  Decoder #(.select(2)) decoder_1 (
    .out0(decoder_1_out0), .out1(decoder_1_out1), .out2(decoder_1_out2), .out3(decoder_1_out3), .sel(IR[7:6]));  // open: en
  Decoder #(.select(2)) decoder_2 (
    .out0(decoder_2_out0), .out1(decoder_2_out1), .out2(decoder_2_out2), .out3(decoder_2_out3), .sel(IR[5:4]));  // open: en
  Decoder #(.select(3)) decoder_3 (
    .out0(decoder_3_out0[0]), .out1(decoder_3_out0[1]), .out2(decoder_3_out0[2]), .out3(decoder_3_out0[3]),
    .out4(decoder_3_out0[4]), .out5(decoder_3_out0[5]), .out6(decoder_3_out0[6]), .out7(decoder_3_out0[7]),
    .sel(IR[3:1]));  // open: en
  and and_13 (to_ULA[2], clock_stepper_1_s5, IR[0], IR[3]);
  and and_14 (to_ULA[1], clock_stepper_1_s5, IR[0], IR[2]);
  and and_15 (to_ULA[0], clock_stepper_1_s5, IR[0], IR[1]);
  clock_stepper clock_stepper_1 (
    .enable(clock_stepper_1_enable), .set(clock_stepper_1_set), .s1(clock_stepper_1_s1),
    .s2(clock_stepper_1_s2), .s3(clock_stepper_1_s3), .s4(clock_stepper_1_s4), .s5(clock_stepper_1_s5));  // open: s6, init
  not not_1 (not_1_out, IR[0]);
  and and_16 (and_16_out, clock_stepper_1_s4, IR[0]);
  and and_17 (and_17_out, clock_stepper_1_s4, and_18_out);
  and and_18 (and_18_out, not_1_out, decoder_3_out0[0]);
  and and_19 (and_19_out, clock_stepper_1_s4, and_20_out);
  and and_20 (and_20_out, not_1_out, decoder_3_out0[1]);
  and and_21 (and_21_out, clock_stepper_1_s4, and_22_out);
  and and_22 (and_22_out, not_1_out, decoder_3_out0[2]);
  and and_23 (and_23_out, clock_stepper_1_s4, and_24_out);
  and and_24 (and_24_out, not_1_out, decoder_3_out0[3]);
  and and_25 (and_25_out, clock_stepper_1_s4, and_26_out);
  and and_26 (and_26_out, not_1_out, decoder_3_out0[4]);
  and and_27 (and_27_out, clock_stepper_1_s4, and_28_out);
  and and_28 (and_28_out, not_1_out, decoder_3_out0[5]);
  and and_29 (and_29_out, clock_stepper_1_s4, and_30_out);
  and and_30 (and_30_out, not_1_out, decoder_3_out0[6]);
  and and_31 (and_31_out, clock_stepper_1_s4, and_32_out);
  and and_32 (and_32_out, not_1_out, decoder_3_out0[7]);
  Decoder #(.select(2)) decoder_4 (
    .out0(decoder_4_out0), .out1(decoder_4_out1), .out2(decoder_4_out2), .out3(decoder_4_out3), .sel(IR[7:6]));  // open: en
  buf and_33 (set_IR, clock_stepper_1_set);  // AND_Gate
  buf and_34 (set_MAR, clock_stepper_1_set);  // AND_Gate
  buf and_35 (set_IAR, clock_stepper_1_set);  // AND_Gate
  buf and_36 (set_ACC, clock_stepper_1_set);  // AND_Gate
  buf and_37 (set_RAM, clock_stepper_1_set);  // AND_Gate
  buf and_38 (set_TMP, clock_stepper_1_set);  // AND_Gate
  buf and_39 (set_FLAGS, clock_stepper_1_set);  // AND_Gate
  and and_40 (set_R0, clock_stepper_1_set, undriven_2, decoder_4_out0);
  and and_41 (set_R1, clock_stepper_1_set, undriven_2, decoder_4_out1);
  and and_42 (set_R2, clock_stepper_1_set, undriven_2, decoder_4_out2);
  and and_43 (set_R3, clock_stepper_1_set, undriven_2, decoder_4_out3);
endmodule

module stepper (
  input  clk,
  output out_2,
  output s1,
  output s2,
  output s3,
  output s4,
  output s5,
  output s6
);

  wire decoder_1_out7;
  wire [2:0] counter_1_q;

  Counter #(.max('h7), .width(3)) counter_1 (
    .D(counter_1_q), .Q(counter_1_q), .clk(clk), .clr(decoder_1_out7));  // open: load, count, carry, up
  Decoder #(.select(3)) decoder_1 (
    .out0(out_2), .out1(s1), .out2(s2), .out3(s3), .out4(s4), .out5(s5), .out6(s6), .out7(decoder_1_out7),
    .sel(counter_1_q));  // open: en
endmodule

module clock_set_enable (
  output clk_e,
  output clk_s
);

  wire clock_1_out, not_1_out, t_ff_1_q;

  Clock clock_1 (.out(clock_1_out));
  T_Flip_Flop t_ff_1 (.clk(clock_1_out), .T(1'b1), .Q(t_ff_1_q));  // open: Qn, preset, reset
  not not_1 (not_1_out, clock_1_out);
  or or_1 (clk_e, clock_1_out, t_ff_1_q);
  and and_1 (clk_s, t_ff_1_q, not_1_out);
endmodule

module clock_stepper (
  output enable,
  output set,
  output init,
  output s1,
  output s2,
  output s3,
  output s4,
  output s5,
  output s6
);

  clock_set_enable clock_set_enable_1 (.clk_e(enable), .clk_s(set));
  stepper stepper_1 (.clk(enable), .s1(s1), .s2(s2), .s3(s3), .s4(s4), .s5(s5), .s6(s6), .out_2(init));
endmodule

// UC
module uc_struct (
  input  carry_out_flag,
  input  a_larger_flag,
  input  equal_flag,
  input  zero_flag,
  input  [15:0] ir,
  output init,
  output [5:0] step,
  output set_IR,
  output bus_1,
  output set_MAR,
  output enable_IAR,
  output set_IAR,
  output enable_RAM,
  output set_ACC,
  output enable_ACC,
  output set_RAM,
  output set_TMP,
  output enable_IO_clk,
  output set_FLAGS,
  output set_IO_clk,
  output set_R0,
  output enable_R0,
  output set_R1,
  output enable_R1,
  output set_R2,
  output enable_R2,
  output set_R3,
  output enable_R3,
  output data_address,
  output input_output,
  output [2:0] to_ULA
);

  wire A_out, and_5_out, and_6_out, and_7_out, and_8_out, and_9_out, and_10_out, and_11_out, and_12_out,
       and_16_out, and_17_out, and_18_out, and_19_out, and_20_out, and_21_out, and_22_out, and_23_out,
       and_24_out, and_25_out, and_26_out, and_27_out, and_28_out, and_29_out, and_30_out, and_31_out,
       and_32_out, and_33_out, and_34_out, and_35_out, and_36_out, and_37_out, and_38_out, and_39_out,
       and_40_out, and_41_out, and_42_out, C_out, clock_stepper_1_enable, clock_stepper_1_set,
       decoder_1_out0, decoder_1_out1, decoder_1_out2, decoder_1_out3, decoder_2_out0, decoder_2_out1,
       decoder_2_out2, decoder_2_out3, decoder_4_out0, decoder_4_out1, decoder_4_out2, decoder_4_out3, E_out,
       nand_1_out, not_1_out, not_2_out, or_6_out, or_7_out, or_8_out, or_9_out, or_10_out, or_11_out,
       or_12_out, or_13_out, REG_A_out, REG_B_2_out, REG_B_out, Z_out;
  wire [7:0] decoder_3_out7;

  or or_1 (enable_R0, and_5_out, and_9_out);
  or or_2 (enable_R1, and_6_out, and_10_out);
  or or_3 (enable_R2, and_7_out, and_11_out);
  or or_4 (enable_R3, and_8_out, and_12_out);
  and and_1 (enable_IAR, clock_stepper_1_enable, or_6_out);
  and and_2 (enable_RAM, clock_stepper_1_enable, or_7_out);
  and and_3 (enable_ACC, clock_stepper_1_enable, or_8_out);
  and and_4 (enable_IO_clk, clock_stepper_1_enable, and_39_out);
  and and_5 (and_5_out, clock_stepper_1_enable, REG_B_out, decoder_1_out0);
  and and_6 (and_6_out, clock_stepper_1_enable, REG_B_out, decoder_1_out1);
  and and_7 (and_7_out, clock_stepper_1_enable, REG_B_out, decoder_1_out2);
  and and_8 (and_8_out, clock_stepper_1_enable, REG_B_out, decoder_1_out3);
  and and_9 (and_9_out, clock_stepper_1_enable, REG_A_out, decoder_2_out0);
  and and_10 (and_10_out, clock_stepper_1_enable, REG_A_out, decoder_2_out1);
  and and_11 (and_11_out, clock_stepper_1_enable, REG_A_out, decoder_2_out2);
  and and_12 (and_12_out, clock_stepper_1_enable, REG_A_out, decoder_2_out3);
  or or_5 (bus_1, step[0], and_29_out, and_27_out, and_21_out);
  or or_6 (or_6_out, step[0], and_21_out, and_25_out, and_27_out);
  or or_7 (or_7_out, step[1], and_42_out, and_37_out, and_36_out, and_34_out);
  or or_8 (or_8_out, step[2], and_38_out, and_41_out, and_40_out);
  or REG_B (REG_B_out, and_16_out, and_35_out, and_23_out, and_31_out);
  or REG_A (REG_A_out, and_19_out, and_17_out, and_33_out);
  Decoder #(.select(2)) decoder_1 (
    .out0(decoder_1_out0), .out1(decoder_1_out1), .out2(decoder_1_out2), .out3(decoder_1_out3), .sel(ir[1:0]));  // open: en
  Decoder #(.select(2)) decoder_2 (
    .out0(decoder_2_out0), .out1(decoder_2_out1), .out2(decoder_2_out2), .out3(decoder_2_out3), .sel(ir[3:2]));  // open: en
  and and_13 (to_ULA[0], step[4], ir[15], ir[12]);
  and and_14 (to_ULA[1], step[4], ir[15], ir[13]);
  and and_15 (to_ULA[2], step[4], ir[15], ir[14]);
  clock_stepper clock_stepper_1 (
    .enable(clock_stepper_1_enable), .set(clock_stepper_1_set), .s1(step[0]), .s2(step[1]), .s3(step[2]),
    .s4(step[3]), .s5(step[4]), .s6(step[5]), .init(init));
  not not_1 (not_1_out, ir[15]);
  Decoder #(.select(3)) decoder_3 (
    .out0(decoder_3_out7[7]), .out1(decoder_3_out7[6]), .out2(decoder_3_out7[5]), .out3(decoder_3_out7[4]),
    .out4(decoder_3_out7[3]), .out5(decoder_3_out7[2]), .out6(decoder_3_out7[1]), .out7(decoder_3_out7[0]),
    .sel(ir[14:12]));  // open: en
  and and_16 (and_16_out, step[3], ir[15]);
  and and_17 (and_17_out, step[3], and_18_out);
  and and_18 (and_18_out, not_1_out, decoder_3_out7[7]);
  and and_19 (and_19_out, step[3], and_20_out);
  and and_20 (and_20_out, not_1_out, decoder_3_out7[6]);
  and and_21 (and_21_out, step[3], and_22_out);
  and and_22 (and_22_out, not_1_out, decoder_3_out7[5]);
  and and_23 (and_23_out, step[3], and_24_out);
  and and_24 (and_24_out, not_1_out, decoder_3_out7[4]);
  and and_25 (and_25_out, step[3], and_26_out);
  and and_26 (and_26_out, not_1_out, decoder_3_out7[3]);
  and and_27 (and_27_out, step[3], and_28_out);
  and and_28 (and_28_out, not_1_out, decoder_3_out7[2]);
  and and_29 (and_29_out, step[3], and_30_out);
  and and_30 (and_30_out, not_1_out, decoder_3_out7[1]);
  and and_31 (and_31_out, step[3], and_32_out, ir[3]);
  and and_32 (and_32_out, not_1_out, decoder_3_out7[0]);
  not not_2 (not_2_out, ir[3]);
  and C (C_out, ir[3], carry_out_flag);
  and A (A_out, ir[2], a_larger_flag);
  and E (E_out, ir[1], equal_flag);
  and Z (Z_out, ir[0], zero_flag);
  nand nand_1 (nand_1_out, ir[14], ir[13], ir[12]);
  and and_33 (and_33_out, step[4], ir[15]);
  and and_34 (and_34_out, step[4], and_18_out);
  and and_35 (and_35_out, step[4], and_20_out);
  and and_36 (and_36_out, step[4], and_22_out);
  and and_37 (and_37_out, step[4], and_26_out);
  and and_38 (and_38_out, step[4], and_28_out);
  and and_39 (and_39_out, step[4], and_32_out, not_2_out);
  or or_9 (or_9_out, C_out, A_out, E_out, Z_out);
  and and_40 (and_40_out, step[5], ir[15], nand_1_out);
  and and_41 (and_41_out, step[5], and_22_out);
  and and_42 (and_42_out, step[5], and_28_out, or_9_out);
  or or_10 (or_10_out, step[0], and_21_out, and_27_out, and_17_out, and_19_out, and_25_out);
  or or_11 (or_11_out, step[2], and_23_out, and_37_out, and_38_out, and_41_out, and_42_out);
  or or_12 (or_12_out, step[0], and_21_out, and_27_out, and_33_out);
  or or_13 (or_13_out, and_29_out, and_33_out);
  or REG_B_2 (REG_B_2_out, and_34_out, and_40_out, and_36_out, and_39_out);
  Decoder #(.select(2)) decoder_4 (
    .out0(decoder_4_out0), .out1(decoder_4_out1), .out2(decoder_4_out2), .out3(decoder_4_out3), .sel(ir[1:0]));  // open: en
  and and_43 (set_IR, clock_stepper_1_set, step[1]);
  and and_44 (set_MAR, clock_stepper_1_set, or_10_out);
  and and_45 (set_IAR, clock_stepper_1_set, or_11_out);
  and and_46 (set_ACC, clock_stepper_1_set, or_12_out);
  and and_47 (set_RAM, clock_stepper_1_set, and_35_out);
  and and_48 (set_TMP, clock_stepper_1_set, and_16_out);
  and and_49 (set_FLAGS, clock_stepper_1_set, or_13_out);
  and and_50 (set_IO_clk, clock_stepper_1_set, and_31_out);
  and and_51 (set_R0, clock_stepper_1_set, REG_B_2_out, decoder_4_out0);
  and and_52 (set_R1, clock_stepper_1_set, REG_B_2_out, decoder_4_out1);
  and and_53 (set_R2, clock_stepper_1_set, REG_B_2_out, decoder_4_out2);
  and and_54 (set_R3, clock_stepper_1_set, REG_B_2_out, decoder_4_out3);

  assign data_address = ir[2];
  assign input_output = ir[3];
endmodule

module uc_test (
);

  uc_fetch_IR uc_fetch_ir_1 ();  // open: s1, s2, s3, bus_1, set_MAR, enable_IAR, set_ACC, enable_RAM, set_IR, enable_ACC, set_IAR
endmodule

module uc_fetch_IR (
  input  s1,
  input  s2,
  input  s3,
  output bus_1,
  output set_MAR,
  output enable_IAR,
  output set_ACC,
  output enable_RAM,
  output set_IR,
  output enable_ACC,
  output set_IAR
);


  assign bus_1 = s1;
  assign enable_ACC = s3;
  assign enable_IAR = s1;
  assign enable_RAM = s2;
  assign set_ACC = s1;
  assign set_IAR = s3;
  assign set_IR = s2;
  assign set_MAR = s1;
endmodule

module flags_reg (
  input  carry,
  input  a_maior,
  input  iguais,
  input  zero,
  input  in_5,
  output carry_out,
  output a_maior_out,
  output iguais_out,
  output zero_out
);

  Register #(.width(4)) register_1 (
    .D({zero, iguais, a_maior, carry}), .Q({zero_out, iguais_out, a_maior_out, carry_out}), .clk(in_5));  // open: en, clr
endmodule

module adapter_keyboard (
  input  e_clk,
  input  data_address,
  input  input_output,
  input  s_clk,
  input  [6:0] data_keyboard,
  output [15:0] barramento,
  output clk_keyboard,
  output e_keyboard
);

  wire and_1_out, comparator_1_eq;
  wire [15:0] bit_extender_1_out;

  Comparator #(.width(16)) comparator_1 (.a(barramento), .b({16{1'b1}}), .eq(comparator_1_eq));  // open: gt, lt
  and and_1 (and_1_out, data_address, input_output, s_clk);
  T_Flip_Flop t_ff_1 (.clk(e_clk), .T(1'b1), .Qn(clk_keyboard));  // open: Q, preset, reset
  Register #(.width(1)) register_1 (.D(comparator_1_eq), .Q(e_keyboard), .clk(and_1_out));  // open: en, clr
  assign barramento = e_clk ? bit_extender_1_out : 16'bz;  // Controlled_Buffer controlled_buffer_1
  assign bit_extender_1_out = {{9{1'b0}}, data_keyboard};  // Bit_Extender bit_extender_1
endmodule

module adapter_display (
  input  [15:0] barramento,
  input  data_address,
  input  input_output,
  input  s_clk,
  output d_clk,
  output d_write,
  output [6:0] data_display
);

  wire and_1_out, comparator_1_eq;

  Comparator #(.width(16)) comparator_1 (.a(barramento), .b(16'hfffe), .eq(comparator_1_eq));  // open: gt, lt
  and and_1 (and_1_out, data_address, input_output, s_clk);
  Register #(.width(1)) register_1 (.D(comparator_1_eq), .Q(d_write), .clk(and_1_out));  // open: en, clr
  Bit_Extender #(.in_width(16), .out_width(7), .\type ("zero")) bit_extender_1 (.in(barramento), .out(data_display));

  assign d_clk = s_clk;
endmodule
