// Logisim project luiz_gabriel_antunes_sena.circ as structural Verilog: 29 circuits, main circuit main
module main (
  input  in_1,
  input  in_2,
  input  in_3,
  input  in_4,
  input  in_5,
  input  in_6,
  input  in_7,
  input  in_8,
  input  in_9,
  input  in_10,
  input  in_11,
  input  in_12,
  input  [7:0] in_13,
  input  [7:0] in_14,
  input  in_15,
  input  in_16
);

  wire [7:0] adder_8bit_exp_1_s0, reg_8bit_exp_1_out_11, register_1_q, register_2_q, register_3_q,
       ula_exp_1_d0;

  Adder_8Bit_Exp adder_8bit_exp_1 (
    .A7(in_13[7]), .A2(in_13[2]), .A1(in_13[1]), .A0(in_13[0]), .B7(in_14[7]), .A6(in_13[6]), .B6(in_14[6]),
    .B5(in_14[5]), .B4(in_14[4]), .B3(in_14[3]), .B2(in_14[2]), .B1(in_14[1]), .B0(in_14[0]), .A5(in_13[5]),
    .A4(in_13[4]), .A3(in_13[3]), .S0(adder_8bit_exp_1_s0[0]), .S1(adder_8bit_exp_1_s0[1]),
    .S2(adder_8bit_exp_1_s0[2]), .S3(adder_8bit_exp_1_s0[3]), .S4(adder_8bit_exp_1_s0[4]),
    .S5(adder_8bit_exp_1_s0[5]), .S6(adder_8bit_exp_1_s0[6]), .S7(adder_8bit_exp_1_s0[7]));  // open: C_out
  // Probe on reg_8bit_exp_1_out_11
  Reg_8Bit_Exp reg_8bit_exp_1 (
    .in_1(reg_8bit_exp_1_out_11[0]), .in_2(reg_8bit_exp_1_out_11[1]), .in_3(reg_8bit_exp_1_out_11[2]),
    .in_4(reg_8bit_exp_1_out_11[3]), .in_5(reg_8bit_exp_1_out_11[4]), .in_6(reg_8bit_exp_1_out_11[5]),
    .in_7(reg_8bit_exp_1_out_11[6]), .in_8(reg_8bit_exp_1_out_11[7]), .Setter(in_2), .Enable(in_7),
    .out_11(reg_8bit_exp_1_out_11[0]), .out_12(reg_8bit_exp_1_out_11[1]), .out_13(reg_8bit_exp_1_out_11[2]),
    .out_14(reg_8bit_exp_1_out_11[3]), .out_15(reg_8bit_exp_1_out_11[4]), .out_16(reg_8bit_exp_1_out_11[5]),
    .out_17(reg_8bit_exp_1_out_11[6]), .out_18(reg_8bit_exp_1_out_11[7]));
  Register register_1 (.D(reg_8bit_exp_1_out_11), .clk(in_15), .Q(register_1_q));  // open: en, clr
  Reg_8Bit_Exp reg_8bit_exp_2 (
    .in_1(reg_8bit_exp_1_out_11[0]), .in_2(reg_8bit_exp_1_out_11[1]), .in_3(reg_8bit_exp_1_out_11[2]),
    .in_4(reg_8bit_exp_1_out_11[3]), .in_5(reg_8bit_exp_1_out_11[4]), .in_6(reg_8bit_exp_1_out_11[5]),
    .in_7(reg_8bit_exp_1_out_11[6]), .in_8(reg_8bit_exp_1_out_11[7]), .Setter(in_3), .Enable(in_8),
    .out_11(reg_8bit_exp_1_out_11[0]), .out_12(reg_8bit_exp_1_out_11[1]), .out_13(reg_8bit_exp_1_out_11[2]),
    .out_14(reg_8bit_exp_1_out_11[3]), .out_15(reg_8bit_exp_1_out_11[4]), .out_16(reg_8bit_exp_1_out_11[5]),
    .out_17(reg_8bit_exp_1_out_11[6]), .out_18(reg_8bit_exp_1_out_11[7]));
  ULA_Exp ula_exp_1 (
    .A5(register_1_q[5]), .A4(register_1_q[4]), .A3(register_1_q[3]), .A2(register_1_q[2]),
    .A1(register_1_q[1]), .A0(register_1_q[0]), .B7(reg_8bit_exp_1_out_11[7]), .B6(reg_8bit_exp_1_out_11[6]),
    .B5(reg_8bit_exp_1_out_11[5]), .B4(reg_8bit_exp_1_out_11[4]), .B3(reg_8bit_exp_1_out_11[3]),
    .B2(reg_8bit_exp_1_out_11[2]), .B1(reg_8bit_exp_1_out_11[1]), .B0(reg_8bit_exp_1_out_11[0]),
    .A7(register_1_q[7]), .A6(register_1_q[6]), .D0(ula_exp_1_d0[0]), .D1(ula_exp_1_d0[1]),
    .D2(ula_exp_1_d0[2]), .D3(ula_exp_1_d0[3]), .D4(ula_exp_1_d0[4]), .D5(ula_exp_1_d0[5]),
    .D6(ula_exp_1_d0[6]), .D7(ula_exp_1_d0[7]));  // open: Op, c_in, a_more_than_b, a_equals_b, res_zero, c_out
  Reg_8Bit_Exp reg_8bit_exp_3 (
    .in_1(reg_8bit_exp_1_out_11[0]), .in_2(reg_8bit_exp_1_out_11[1]), .in_3(reg_8bit_exp_1_out_11[2]),
    .in_4(reg_8bit_exp_1_out_11[3]), .in_5(reg_8bit_exp_1_out_11[4]), .in_6(reg_8bit_exp_1_out_11[5]),
    .in_7(reg_8bit_exp_1_out_11[6]), .in_8(reg_8bit_exp_1_out_11[7]), .Setter(in_4), .Enable(in_9),
    .out_11(reg_8bit_exp_1_out_11[0]), .out_12(reg_8bit_exp_1_out_11[1]), .out_13(reg_8bit_exp_1_out_11[2]),
    .out_14(reg_8bit_exp_1_out_11[3]), .out_15(reg_8bit_exp_1_out_11[4]), .out_16(reg_8bit_exp_1_out_11[5]),
    .out_17(reg_8bit_exp_1_out_11[6]), .out_18(reg_8bit_exp_1_out_11[7]));
  Register register_2 (.D(ula_exp_1_d0), .clk(in_12), .Q(register_2_q));  // open: en, clr
  Reg_8Bit_Exp reg_8bit_exp_4 (
    .in_1(reg_8bit_exp_1_out_11[0]), .in_2(reg_8bit_exp_1_out_11[1]), .in_3(reg_8bit_exp_1_out_11[2]),
    .in_4(reg_8bit_exp_1_out_11[3]), .in_5(reg_8bit_exp_1_out_11[4]), .in_6(reg_8bit_exp_1_out_11[5]),
    .in_7(reg_8bit_exp_1_out_11[6]), .in_8(reg_8bit_exp_1_out_11[7]), .Setter(in_5), .Enable(in_10),
    .out_11(reg_8bit_exp_1_out_11[0]), .out_12(reg_8bit_exp_1_out_11[1]), .out_13(reg_8bit_exp_1_out_11[2]),
    .out_14(reg_8bit_exp_1_out_11[3]), .out_15(reg_8bit_exp_1_out_11[4]), .out_16(reg_8bit_exp_1_out_11[5]),
    .out_17(reg_8bit_exp_1_out_11[6]), .out_18(reg_8bit_exp_1_out_11[7]));
  assign reg_8bit_exp_1_out_11 = in_16 ? register_2_q : 8'bz;  // Controlled_Buffer controlled_buffer_1
  Register register_3 (.D(reg_8bit_exp_1_out_11), .clk(in_1), .Q(register_3_q));  // open: en, clr
  RAM #(.databus("bidir")) ram_1 (
    .addr(register_3_q), .we(in_6), .oe(in_11), .clk(in_11), .data(reg_8bit_exp_1_out_11));

  // Notes on the sheet:
  //   2. O resultado fica armazenado
  //    nesse barramento
  //   1. Aqui são os dois bytes que serão somados
  //   Luiz Gabriel Antunes Sena - 22401905
  //   3. Barramento principal com o resultado do registrador escolhido
  //   S: Setar valor do barramento para registrador
  //   E: Habilitar saída do registrador para barramento principal´
endmodule

module Adder_Bin_Full (
  input  Carry_In,
  input  Bit_A,
  input  Bit_B,
  output Carry_Out,
  output Result
);

  wire adder_bin_half_1_carry_out, adder_bin_half_1_result, adder_bin_half_2_carry_out;

  Adder_Bin_Half adder_bin_half_1 (
    .Bit_A(Bit_A), .Bit_B(Bit_B), .Carry_out(adder_bin_half_1_carry_out), .Result(adder_bin_half_1_result));
  or or_1 (Carry_Out, adder_bin_half_1_carry_out, adder_bin_half_2_carry_out);
  Adder_Bin_Half adder_bin_half_2 (
    .Bit_A(adder_bin_half_1_result), .Bit_B(Carry_In), .Carry_out(adder_bin_half_2_carry_out), .Result(Result));
endmodule

// ha
module Adder_Bin_Half (
  input  Bit_A,
  input  Bit_B,
  output Carry_out,
  output Result
);

  and and_1 (Carry_out, Bit_A, Bit_B);
  xor xor_1 (Result, Bit_A, Bit_B);
endmodule

module Adder_2Bit (
  input  [1:0] Word_A,
  input  [1:0] Word_B,
  input  Carry_In,
  output Carry_Out,
  output [1:0] Result
);

  wire adder_bin_full_2_carry_out;

  Adder_Bin_Full adder_bin_full_1 (
    .Bit_A(Word_A[1]), .Bit_B(Word_B[1]), .Carry_In(adder_bin_full_2_carry_out), .Carry_Out(Carry_Out),
    .Result(Result[1]));
  Adder_Bin_Full adder_bin_full_2 (
    .Bit_A(Word_A[0]), .Bit_B(Word_B[0]), .Carry_In(Carry_In), .Carry_Out(adder_bin_full_2_carry_out),
    .Result(Result[0]));
endmodule

module Adder_4Bit (
  input  [3:0] Word_A,
  input  [3:0] Word_B,
  input  Carry_In,
  output Carry_Out,
  output [3:0] Result
);

  wire adder_2bit_2_carry_out;

  Adder_2Bit adder_2bit_1 (
    .Word_A(Word_A[3:2]), .Word_B(Word_B[3:2]), .Carry_In(adder_2bit_2_carry_out), .Carry_Out(Carry_Out),
    .Result(Result[3:2]));
  Adder_2Bit adder_2bit_2 (
    .Word_A(Word_A[1:0]), .Word_B(Word_B[1:0]), .Carry_In(Carry_In), .Carry_Out(adder_2bit_2_carry_out),
    .Result(Result[1:0]));
endmodule

module Adder_8Bit_Deprecated (
  input  [7:0] Word_A,
  input  [7:0] Word_B,
  input  Carry_In,
  output Carry_Out,
  output [7:0] Result
);

  wire adder_4bit_2_carry_out;

  Adder_4Bit adder_4bit_1 (
    .Word_A(Word_A[7:4]), .Word_B(Word_B[7:4]), .Carry_In(adder_4bit_2_carry_out), .Carry_Out(Carry_Out),
    .Result(Result[7:4]));
  Adder_4Bit adder_4bit_2 (
    .Word_A(Word_A[3:0]), .Word_B(Word_B[3:0]), .Carry_In(Carry_In), .Carry_Out(adder_4bit_2_carry_out),
    .Result(Result[3:0]));
endmodule

module Adder_8Bit (
  input  [7:0] Word_A,
  input  [7:0] Word_B,
  output [7:0] out_3,
  output out_4
);

  wire adder_bin_full_1_carry_out, adder_bin_full_2_carry_out, adder_bin_full_3_carry_out,
       adder_bin_full_4_carry_out, adder_bin_full_5_carry_out, adder_bin_full_6_carry_out,
       adder_bin_full_7_carry_out;

  Adder_Bin_Full adder_bin_full_1 (
    .Bit_A(Word_A[0]), .Bit_B(Word_B[0]), .Carry_In(1'b0), .Carry_Out(adder_bin_full_1_carry_out),
    .Result(out_3[0]));
  Adder_Bin_Full adder_bin_full_2 (
    .Bit_A(Word_A[1]), .Bit_B(Word_B[1]), .Carry_In(adder_bin_full_1_carry_out),
    .Carry_Out(adder_bin_full_2_carry_out), .Result(out_3[1]));
  Adder_Bin_Full adder_bin_full_3 (
    .Bit_A(Word_A[2]), .Bit_B(Word_B[2]), .Carry_In(adder_bin_full_2_carry_out),
    .Carry_Out(adder_bin_full_3_carry_out), .Result(out_3[2]));
  Adder_Bin_Full adder_bin_full_4 (
    .Bit_A(Word_A[3]), .Bit_B(Word_B[3]), .Carry_In(adder_bin_full_3_carry_out),
    .Carry_Out(adder_bin_full_4_carry_out), .Result(out_3[3]));
  Adder_Bin_Full adder_bin_full_5 (
    .Bit_A(Word_A[4]), .Bit_B(Word_B[4]), .Carry_In(adder_bin_full_4_carry_out),
    .Carry_Out(adder_bin_full_5_carry_out), .Result(out_3[4]));
  Adder_Bin_Full adder_bin_full_6 (
    .Bit_A(Word_A[5]), .Bit_B(Word_B[5]), .Carry_In(adder_bin_full_5_carry_out),
    .Carry_Out(adder_bin_full_6_carry_out), .Result(out_3[5]));
  Adder_Bin_Full adder_bin_full_7 (
    .Bit_A(Word_A[6]), .Bit_B(Word_B[6]), .Carry_In(adder_bin_full_6_carry_out),
    .Carry_Out(adder_bin_full_7_carry_out), .Result(out_3[6]));
  Adder_Bin_Full adder_bin_full_8 (
    .Bit_A(Word_A[7]), .Bit_B(Word_B[7]), .Carry_In(adder_bin_full_7_carry_out), .Carry_Out(out_4),
    .Result(out_3[7]));
endmodule

module Adder_8Bit_Exp (
  input  A7,
  input  A6,
  input  A5,
  input  A4,
  input  A3,
  input  A2,
  input  A1,
  input  A0,
  input  B7,
  input  B6,
  input  B5,
  input  B4,
  input  B3,
  input  B2,
  input  B1,
  input  B0,
  output S0,
  output S1,
  output S2,
  output S3,
  output S4,
  output S5,
  output S6,
  output S7,
  output C_out
);

  wire adder_bin_full_1_carry_out, adder_bin_full_2_carry_out, adder_bin_full_3_carry_out,
       adder_bin_full_4_carry_out, adder_bin_full_5_carry_out, adder_bin_full_6_carry_out,
       adder_bin_full_7_carry_out;

  Adder_Bin_Full adder_bin_full_1 (
    .Bit_A(B0), .Bit_B(A0), .Carry_In(1'b0), .Carry_Out(adder_bin_full_1_carry_out), .Result(S0));
  Adder_Bin_Full adder_bin_full_2 (
    .Bit_A(B1), .Bit_B(A1), .Carry_In(adder_bin_full_1_carry_out), .Carry_Out(adder_bin_full_2_carry_out),
    .Result(S1));
  Adder_Bin_Full adder_bin_full_3 (
    .Bit_A(B2), .Bit_B(A2), .Carry_In(adder_bin_full_2_carry_out), .Carry_Out(adder_bin_full_3_carry_out),
    .Result(S2));
  Adder_Bin_Full adder_bin_full_4 (
    .Bit_A(B3), .Bit_B(A3), .Carry_In(adder_bin_full_3_carry_out), .Carry_Out(adder_bin_full_4_carry_out),
    .Result(S3));
  Adder_Bin_Full adder_bin_full_5 (
    .Bit_A(B4), .Bit_B(A4), .Carry_In(adder_bin_full_4_carry_out), .Carry_Out(adder_bin_full_5_carry_out),
    .Result(S4));
  Adder_Bin_Full adder_bin_full_6 (
    .Bit_A(B5), .Bit_B(A5), .Carry_In(adder_bin_full_5_carry_out), .Carry_Out(adder_bin_full_6_carry_out),
    .Result(S5));
  Adder_Bin_Full adder_bin_full_7 (
    .Bit_A(B6), .Bit_B(A6), .Carry_In(adder_bin_full_6_carry_out), .Carry_Out(adder_bin_full_7_carry_out),
    .Result(S6));
  Adder_Bin_Full adder_bin_full_8 (
    .Bit_A(B7), .Bit_B(A7), .Carry_In(adder_bin_full_7_carry_out), .Carry_Out(C_out), .Result(S7));
  LED led_1 (.in(S0));
  LED led_2 (.in(S1));
  LED led_3 (.in(S2));
  LED led_4 (.in(S3));
  LED led_5 (.in(S4));
  LED led_6 (.in(S5));
  LED led_7 (.in(S6));
  LED led_8 (.in(S7));
endmodule

// M
module Memory_1Bit (
  input  Input_Bin,
  input  Setter,
  output Value
);

  wire multiplexer_1_out, nand_1_out, nand_2_out, nand_4_out, por_1_out;

  POR #(.PorHighDuration(1), .porsize(2)) por_1 (.out(por_1_out));
  Multiplexer multiplexer_1 (.in0(Setter), .in1(por_1_out), .out(multiplexer_1_out), .sel(por_1_out));
  nand nand_1 (nand_1_out, Input_Bin, multiplexer_1_out);
  nand nand_2 (nand_2_out, nand_1_out, multiplexer_1_out);
  nand nand_3 (Value, nand_1_out, nand_4_out);
  nand nand_4 (nand_4_out, Value, nand_2_out);

  // Notes on the sheet:
  //   Dispositivo para previnir valor invalido no primeiro estado
endmodule

module Memory_8Bit (
  input  [7:0] in_1,
  input  in_2,
  output [7:0] out_3
);

  Memory_1Bit memory_1bit_1 (.Input_Bin(in_1[0]), .Setter(in_2), .Value(out_3[0]));
  Memory_1Bit memory_1bit_2 (.Input_Bin(in_1[1]), .Setter(in_2), .Value(out_3[1]));
  Memory_1Bit memory_1bit_3 (.Input_Bin(in_1[2]), .Setter(in_2), .Value(out_3[2]));
  Memory_1Bit memory_1bit_4 (.Input_Bin(in_1[3]), .Setter(in_2), .Value(out_3[3]));
  Memory_1Bit memory_1bit_5 (.Input_Bin(in_1[4]), .Setter(in_2), .Value(out_3[4]));
  Memory_1Bit memory_1bit_6 (.Input_Bin(in_1[5]), .Setter(in_2), .Value(out_3[5]));
  Memory_1Bit memory_1bit_7 (.Input_Bin(in_1[6]), .Setter(in_2), .Value(out_3[6]));
  Memory_1Bit memory_1bit_8 (.Input_Bin(in_1[7]), .Setter(in_2), .Value(out_3[7]));
endmodule

// Mem_8
module Memory_8Bit_Exp (
  input  in_1,
  input  in_2,
  input  in_3,
  input  in_4,
  input  in_5,
  input  in_6,
  input  in_7,
  input  in_8,
  input  in_9,
  output out_10,
  output out_11,
  output out_12,
  output out_13,
  output out_14,
  output out_15,
  output out_16,
  output out_17
);

  Memory_1Bit memory_1bit_1 (.Input_Bin(in_1), .Setter(in_9), .Value(out_10));
  Memory_1Bit memory_1bit_2 (.Input_Bin(in_2), .Setter(in_9), .Value(out_11));
  Memory_1Bit memory_1bit_3 (.Input_Bin(in_3), .Setter(in_9), .Value(out_12));
  Memory_1Bit memory_1bit_4 (.Input_Bin(in_4), .Setter(in_9), .Value(out_13));
  Memory_1Bit memory_1bit_5 (.Input_Bin(in_5), .Setter(in_9), .Value(out_14));
  Memory_1Bit memory_1bit_6 (.Input_Bin(in_6), .Setter(in_9), .Value(out_15));
  Memory_1Bit memory_1bit_7 (.Input_Bin(in_7), .Setter(in_9), .Value(out_16));
  Memory_1Bit memory_1bit_8 (.Input_Bin(in_8), .Setter(in_9), .Value(out_17));
endmodule

module Reg_8Bit (
  input  [7:0] in_1,
  input  Setter,
  input  Enable,
  output [7:0] out_4
);

  wire [7:0] memory_8bit_1_out_3;

  Memory_8Bit memory_8bit_1 (.in_1(in_1), .in_2(Setter), .out_3(memory_8bit_1_out_3));
  assign out_4 = Enable ? memory_8bit_1_out_3 : 8'bz;  // Controlled_Buffer controlled_buffer_1
endmodule

// Reg_8
module Reg_8Bit_Exp (
  input  in_1,
  input  in_2,
  input  in_3,
  input  in_4,
  input  in_5,
  input  in_6,
  input  in_7,
  input  in_8,
  input  Setter,
  input  Enable,
  output out_11,
  output out_12,
  output out_13,
  output out_14,
  output out_15,
  output out_16,
  output out_17,
  output out_18
);

  wire memory_8bit_exp_1_out_10, memory_8bit_exp_1_out_11, memory_8bit_exp_1_out_12,
       memory_8bit_exp_1_out_13, memory_8bit_exp_1_out_14, memory_8bit_exp_1_out_15,
       memory_8bit_exp_1_out_16, memory_8bit_exp_1_out_17;

  Memory_8Bit_Exp memory_8bit_exp_1 (
    .in_1(in_1), .in_2(in_2), .in_3(in_3), .in_4(in_4), .in_5(in_5), .in_6(in_6), .in_7(in_7), .in_8(in_8),
    .in_9(Setter), .out_10(memory_8bit_exp_1_out_10), .out_11(memory_8bit_exp_1_out_11),
    .out_12(memory_8bit_exp_1_out_12), .out_13(memory_8bit_exp_1_out_13), .out_14(memory_8bit_exp_1_out_14),
    .out_15(memory_8bit_exp_1_out_15), .out_16(memory_8bit_exp_1_out_16), .out_17(memory_8bit_exp_1_out_17));
  assign out_11 = Enable ? memory_8bit_exp_1_out_10 : 1'bz;  // Controlled_Buffer controlled_buffer_1
  assign out_12 = Enable ? memory_8bit_exp_1_out_11 : 1'bz;  // Controlled_Buffer controlled_buffer_2
  assign out_13 = Enable ? memory_8bit_exp_1_out_12 : 1'bz;  // Controlled_Buffer controlled_buffer_3
  assign out_14 = Enable ? memory_8bit_exp_1_out_13 : 1'bz;  // Controlled_Buffer controlled_buffer_4
  assign out_15 = Enable ? memory_8bit_exp_1_out_14 : 1'bz;  // Controlled_Buffer controlled_buffer_5
  assign out_16 = Enable ? memory_8bit_exp_1_out_15 : 1'bz;  // Controlled_Buffer controlled_buffer_6
  assign out_17 = Enable ? memory_8bit_exp_1_out_16 : 1'bz;  // Controlled_Buffer controlled_buffer_7
  assign out_18 = Enable ? memory_8bit_exp_1_out_17 : 1'bz;  // Controlled_Buffer controlled_buffer_8
endmodule

module teste (
  input  in_1,
  input  in_2,
  input  in_3,
  input  in_4,
  input  in_5,
  input  in_6,
  input  in_7,
  input  in_8,
  input  [7:0] in_9,
  input  [7:0] in_10,
  input  in_11,
  input  in_12,
  output out_13
);

  wire [7:0] adder_8bit_1_p2, controlled_buffer_1_out, reg_8bit_exp_1_out_11, reg_8bit_exp_2_out_11,
       reg_8bit_exp_3_out_11, reg_8bit_exp_4_out_11;

  // Adder_8Bit adder_8bit_1: pin names not known; wires that end beside it: in_9, adder_8bit_1_p2, in_10
  // Probe on controlled_buffer_1_out
  Reg_8Bit_Exp reg_8bit_exp_1 (
    .in_1(adder_8bit_1_p2[0]), .in_2(adder_8bit_1_p2[1]), .in_3(adder_8bit_1_p2[2]),
    .in_4(adder_8bit_1_p2[3]), .in_5(adder_8bit_1_p2[4]), .in_6(adder_8bit_1_p2[5]),
    .in_7(adder_8bit_1_p2[6]), .in_8(adder_8bit_1_p2[7]), .Setter(in_1), .Enable(in_5),
    .out_11(reg_8bit_exp_1_out_11[0]), .out_12(reg_8bit_exp_1_out_11[1]), .out_13(reg_8bit_exp_1_out_11[2]),
    .out_14(reg_8bit_exp_1_out_11[3]), .out_15(reg_8bit_exp_1_out_11[4]), .out_16(reg_8bit_exp_1_out_11[5]),
    .out_17(reg_8bit_exp_1_out_11[6]), .out_18(reg_8bit_exp_1_out_11[7]));
  assign controlled_buffer_1_out = in_5 ? reg_8bit_exp_1_out_11 : 8'bz;  // Controlled_Buffer controlled_buffer_1
  assign controlled_buffer_1_out = in_6 ? reg_8bit_exp_2_out_11 : 8'bz;  // Controlled_Buffer controlled_buffer_2
  Reg_8Bit_Exp reg_8bit_exp_2 (
    .in_1(adder_8bit_1_p2[0]), .in_2(adder_8bit_1_p2[1]), .in_3(adder_8bit_1_p2[2]),
    .in_4(adder_8bit_1_p2[3]), .in_5(adder_8bit_1_p2[4]), .in_6(adder_8bit_1_p2[5]),
    .in_7(adder_8bit_1_p2[6]), .in_8(adder_8bit_1_p2[7]), .Setter(in_2), .Enable(in_6),
    .out_11(reg_8bit_exp_2_out_11[0]), .out_12(reg_8bit_exp_2_out_11[1]), .out_13(reg_8bit_exp_2_out_11[2]),
    .out_14(reg_8bit_exp_2_out_11[3]), .out_15(reg_8bit_exp_2_out_11[4]), .out_16(reg_8bit_exp_2_out_11[5]),
    .out_17(reg_8bit_exp_2_out_11[6]), .out_18(reg_8bit_exp_2_out_11[7]));
  assign controlled_buffer_1_out = in_7 ? reg_8bit_exp_3_out_11 : 8'bz;  // Controlled_Buffer controlled_buffer_3
  Reg_8Bit_Exp reg_8bit_exp_3 (
    .in_1(adder_8bit_1_p2[0]), .in_2(adder_8bit_1_p2[1]), .in_3(adder_8bit_1_p2[2]),
    .in_4(adder_8bit_1_p2[3]), .in_5(adder_8bit_1_p2[4]), .in_6(adder_8bit_1_p2[5]),
    .in_7(adder_8bit_1_p2[6]), .in_8(adder_8bit_1_p2[7]), .Setter(in_3), .Enable(in_7),
    .out_11(reg_8bit_exp_3_out_11[0]), .out_12(reg_8bit_exp_3_out_11[1]), .out_13(reg_8bit_exp_3_out_11[2]),
    .out_14(reg_8bit_exp_3_out_11[3]), .out_15(reg_8bit_exp_3_out_11[4]), .out_16(reg_8bit_exp_3_out_11[5]),
    .out_17(reg_8bit_exp_3_out_11[6]), .out_18(reg_8bit_exp_3_out_11[7]));
  assign controlled_buffer_1_out = in_8 ? reg_8bit_exp_4_out_11 : 8'bz;  // Controlled_Buffer controlled_buffer_4
  Reg_8Bit_Exp reg_8bit_exp_4 (
    .in_1(adder_8bit_1_p2[0]), .in_2(adder_8bit_1_p2[1]), .in_3(adder_8bit_1_p2[2]),
    .in_4(adder_8bit_1_p2[3]), .in_5(adder_8bit_1_p2[4]), .in_6(adder_8bit_1_p2[5]),
    .in_7(adder_8bit_1_p2[6]), .in_8(adder_8bit_1_p2[7]), .Setter(in_4), .Enable(in_8),
    .out_11(reg_8bit_exp_4_out_11[0]), .out_12(reg_8bit_exp_4_out_11[1]), .out_13(reg_8bit_exp_4_out_11[2]),
    .out_14(reg_8bit_exp_4_out_11[3]), .out_15(reg_8bit_exp_4_out_11[4]), .out_16(reg_8bit_exp_4_out_11[5]),
    .out_17(reg_8bit_exp_4_out_11[6]), .out_18(reg_8bit_exp_4_out_11[7]));
  assign out_13 = in_12 ? in_11 : 1'bz;  // Controlled_Buffer controlled_buffer_5
endmodule

// 2x4
module Deco_2x4 (
  input  Input_0,
  input  Input_1,
  output Output_0,
  output Output_1,
  output Output_2,
  output Output_3
);

  and and_1 (Output_0, ~Input_0, ~Input_1);  // AND_Gate
  and and_2 (Output_1, Input_0, ~Input_1);  // AND_Gate
  and and_3 (Output_2, ~Input_0, Input_1);  // AND_Gate
  and and_4 (Output_3, Input_0, Input_1);
endmodule

module Deco_3x8 (
  input  Input_0,
  input  Input_1,
  input  Input_2,
  output Output_0,
  output Output_1,
  output Output_2,
  output Output_3,
  output Output_4,
  output Output_5,
  output Output_6,
  output Output_7
);

  and and_1 (Output_0, ~Input_0, ~Input_1, ~Input_2);  // AND_Gate
  and and_2 (Output_1, Input_0, ~Input_1, ~Input_2);  // AND_Gate
  and and_3 (Output_2, ~Input_0, Input_1, ~Input_2);  // AND_Gate
  and and_4 (Output_3, Input_0, Input_1, ~Input_2);  // AND_Gate
  and and_5 (Output_4, ~Input_0, ~Input_1, Input_2);  // AND_Gate
  and and_6 (Output_5, Input_0, ~Input_1, Input_2);  // AND_Gate
  and and_7 (Output_6, ~Input_0, Input_1, Input_2);  // AND_Gate
  and and_8 (Output_7, Input_0, Input_1, Input_2);
endmodule

module Deco_4x16 (
  input  Input_0,
  input  Input_1,
  input  Input_2,
  input  Input_3,
  output Output_0,
  output Output_1,
  output Output_2,
  output Output_3,
  output Output_4,
  output Output_5,
  output Output_6,
  output Output_7,
  output Output_8,
  output Output_9,
  output Output_10,
  output Output_11,
  output Output_12,
  output Output_13,
  output Output_14,
  output Output_15
);

  and and_1 (Output_0, ~Input_0, ~Input_1, ~Input_2, ~Input_3);  // AND_Gate
  and and_2 (Output_1, Input_0, ~Input_1, ~Input_2, ~Input_3);  // AND_Gate
  and and_3 (Output_2, ~Input_0, Input_1, ~Input_2, ~Input_3);  // AND_Gate
  and and_4 (Output_3, Input_0, Input_1, ~Input_2, ~Input_3);  // AND_Gate
  and and_5 (Output_4, ~Input_0, ~Input_1, Input_2, ~Input_3);  // AND_Gate
  and and_6 (Output_5, Input_0, ~Input_1, Input_2, ~Input_3);  // AND_Gate
  and and_7 (Output_6, ~Input_0, Input_1, Input_2, ~Input_3);  // AND_Gate
  and and_8 (Output_7, Input_0, Input_1, Input_2, ~Input_3);  // AND_Gate
  and and_9 (Output_8, ~Input_0, ~Input_1, ~Input_2, Input_3);  // AND_Gate
  and and_10 (Output_9, Input_0, ~Input_1, ~Input_2, Input_3);  // AND_Gate
  and and_11 (Output_10, ~Input_0, Input_1, ~Input_2, Input_3);  // AND_Gate
  and and_12 (Output_11, Input_0, Input_1, ~Input_2, Input_3);  // AND_Gate
  and and_13 (Output_12, ~Input_0, ~Input_1, Input_2, Input_3);  // AND_Gate
  and and_14 (Output_13, Input_0, ~Input_1, Input_2, Input_3);  // AND_Gate
  and and_15 (Output_14, ~Input_0, Input_1, Input_2, Input_3);  // AND_Gate
  and and_16 (Output_15, Input_0, Input_1, Input_2, Input_3);
endmodule
module RAM_Mem_256_NAO_ABRIR (
  input  [7:0] Address,
  input  Enable_addr,
  input  [7:0] Data,
  input  Write_Data,
  input  Enable_Data
);

  wire and_1_out, and_2_out, and_3_out, and_4_out, and_5_out, and_6_out, and_7_out, and_8_out, and_9_out,
       and_10_out, and_11_out, and_12_out, and_13_out, and_14_out, and_15_out, and_16_out, and_17_out,
       and_18_out, and_19_out, and_20_out, and_21_out, and_22_out, and_23_out, and_24_out, and_25_out,
       and_26_out, and_27_out, and_28_out, and_29_out, and_30_out, and_31_out, and_32_out, and_33_out,
       and_34_out, and_35_out, and_36_out, and_37_out, and_38_out, and_39_out, and_40_out, and_41_out,
       and_42_out, and_43_out, and_44_out, and_45_out, and_46_out, and_47_out, and_48_out, and_49_out,
       and_50_out, and_51_out, and_52_out, and_53_out, and_54_out, and_55_out, and_56_out, and_57_out,
       and_58_out, and_59_out, and_60_out, and_61_out, and_62_out, and_63_out, and_64_out, and_65_out,
       and_66_out, and_67_out, and_68_out, and_69_out, and_70_out, and_71_out, and_72_out, and_73_out,
       and_74_out, and_75_out, and_76_out, and_77_out, and_78_out, and_79_out, and_80_out, and_81_out,
       and_82_out, and_83_out, and_84_out, and_85_out, and_86_out, and_87_out, and_88_out, and_89_out,
       and_90_out, and_91_out, and_92_out, and_93_out, and_94_out, and_95_out, and_96_out, and_97_out,
       and_98_out, and_99_out, and_100_out, and_101_out, and_102_out, and_103_out, and_104_out, and_105_out,
       and_106_out, and_107_out, and_108_out, and_109_out, and_110_out, and_111_out, and_112_out,
       and_113_out, and_114_out, and_115_out, and_116_out, and_117_out, and_118_out, and_119_out,
       and_120_out, and_121_out, and_122_out, and_123_out, and_124_out, and_125_out, and_126_out,
       and_127_out, and_128_out, and_129_out, and_130_out, and_131_out, and_132_out, and_133_out,
       and_134_out, and_135_out, and_136_out, and_137_out, and_138_out, and_139_out, and_140_out,
       and_141_out, and_142_out, and_143_out, and_144_out, and_145_out, and_146_out, and_147_out,
       and_148_out, and_149_out, and_150_out, and_151_out, and_152_out, and_153_out, and_154_out,
       and_155_out, and_156_out, and_157_out, and_158_out, and_159_out, and_160_out, and_161_out,
       and_162_out, and_163_out, and_164_out, and_165_out, and_166_out, and_167_out, and_168_out,
       and_169_out, and_170_out, and_171_out, and_172_out, and_173_out, and_174_out, and_175_out,
       and_176_out, and_177_out, and_178_out, and_179_out, and_180_out, and_181_out, and_182_out,
       and_183_out, and_184_out, and_185_out, and_186_out, and_187_out, and_188_out, and_189_out,
       and_190_out, and_191_out, and_192_out, and_193_out, and_194_out, and_195_out, and_196_out,
       and_197_out, and_198_out, and_199_out, and_200_out, and_201_out, and_202_out, and_203_out,
       and_204_out, and_205_out, and_206_out, and_207_out, and_208_out, and_209_out, and_210_out,
       and_211_out, and_212_out, and_213_out, and_214_out, and_215_out, and_216_out, and_217_out,
       and_218_out, and_219_out, and_220_out, and_221_out, and_222_out, and_223_out, and_224_out,
       and_225_out, and_226_out, and_227_out, and_228_out, and_229_out, and_230_out, and_231_out,
       and_232_out, and_233_out, and_234_out, and_235_out, and_236_out, and_237_out, and_238_out,
       and_239_out, and_240_out, and_241_out, and_242_out, and_243_out, and_244_out, and_245_out,
       and_246_out, and_247_out, and_248_out, and_249_out, and_250_out, and_251_out, and_252_out,
       and_253_out, and_254_out, and_255_out, and_256_out, and_257_out, and_258_out, and_259_out,
       and_260_out, and_261_out, and_262_out, and_263_out, and_264_out, and_265_out, and_266_out,
       and_267_out, and_268_out, and_269_out, and_270_out, and_271_out, and_272_out, and_273_out,
       and_274_out, and_275_out, and_276_out, and_277_out, and_278_out, and_279_out, and_280_out,
       and_281_out, and_282_out, and_283_out, and_284_out, and_285_out, and_286_out, and_287_out,
       and_288_out, and_289_out, and_290_out, and_291_out, and_292_out, and_293_out, and_294_out,
       and_295_out, and_296_out, and_297_out, and_298_out, and_299_out, and_300_out, and_301_out,
       and_302_out, and_303_out, and_304_out, and_305_out, and_306_out, and_307_out, and_308_out,
       and_309_out, and_310_out, and_311_out, and_312_out, and_313_out, and_314_out, and_315_out,
       and_316_out, and_317_out, and_318_out, and_319_out, and_320_out, and_321_out, and_322_out,
       and_323_out, and_324_out, and_325_out, and_326_out, and_327_out, and_328_out, and_329_out,
       and_330_out, and_331_out, and_332_out, and_333_out, and_334_out, and_335_out, and_336_out,
       and_337_out, and_338_out, and_339_out, and_340_out, and_341_out, and_342_out, and_343_out,
       and_344_out, and_345_out, and_346_out, and_347_out, and_348_out, and_349_out, and_350_out,
       and_351_out, and_352_out, and_353_out, and_354_out, and_355_out, and_356_out, and_357_out,
       and_358_out, and_359_out, and_360_out, and_361_out, and_362_out, and_363_out, and_364_out,
       and_365_out, and_366_out, and_367_out, and_368_out, and_369_out, and_370_out, and_371_out,
       and_372_out, and_373_out, and_374_out, and_375_out, and_376_out, and_377_out, and_378_out,
       and_379_out, and_380_out, and_381_out, and_382_out, and_383_out, and_384_out, and_385_out,
       and_386_out, and_387_out, and_388_out, and_389_out, and_390_out, and_391_out, and_392_out,
       and_393_out, and_394_out, and_395_out, and_396_out, and_397_out, and_398_out, and_399_out,
       and_400_out, and_401_out, and_402_out, and_403_out, and_404_out, and_405_out, and_406_out,
       and_407_out, and_408_out, and_409_out, and_410_out, and_411_out, and_412_out, and_413_out,
       and_414_out, and_415_out, and_416_out, and_417_out, and_418_out, and_419_out, and_420_out,
       and_421_out, and_422_out, and_423_out, and_424_out, and_425_out, and_426_out, and_427_out,
       and_428_out, and_429_out, and_430_out, and_431_out, and_432_out, and_433_out, and_434_out,
       and_435_out, and_436_out, and_437_out, and_438_out, and_439_out, and_440_out, and_441_out,
       and_442_out, and_443_out, and_444_out, and_445_out, and_446_out, and_447_out, and_448_out,
       and_449_out, and_450_out, and_451_out, and_452_out, and_453_out, and_454_out, and_455_out,
       and_456_out, and_457_out, and_458_out, and_459_out, and_460_out, and_461_out, and_462_out,
       and_463_out, and_464_out, and_465_out, and_466_out, and_467_out, and_468_out, and_469_out,
       and_470_out, and_471_out, and_472_out, and_473_out, and_474_out, and_475_out, and_476_out,
       and_477_out, and_478_out, and_479_out, and_480_out, and_481_out, and_482_out, and_483_out,
       and_484_out, and_485_out, and_486_out, and_487_out, and_488_out, and_489_out, and_490_out,
       and_491_out, and_492_out, and_493_out, and_494_out, and_495_out, and_496_out, and_497_out,
       and_498_out, and_499_out, and_500_out, and_501_out, and_502_out, and_503_out, and_504_out,
       and_505_out, and_506_out, and_507_out, and_508_out, and_509_out, and_510_out, and_511_out,
       and_512_out, and_513_out, and_514_out, and_515_out, and_516_out, and_517_out, and_518_out,
       and_519_out, and_520_out, and_521_out, and_522_out, and_523_out, and_524_out, and_525_out,
       and_526_out, and_527_out, and_528_out, and_529_out, and_530_out, and_531_out, and_532_out,
       and_533_out, and_534_out, and_535_out, and_536_out, and_537_out, and_538_out, and_539_out,
       and_540_out, and_541_out, and_542_out, and_543_out, and_544_out, and_545_out, and_546_out,
       and_547_out, and_548_out, and_549_out, and_550_out, and_551_out, and_552_out, and_553_out,
       and_554_out, and_555_out, and_556_out, and_557_out, and_558_out, and_559_out, and_560_out,
       and_561_out, and_562_out, and_563_out, and_564_out, and_565_out, and_566_out, and_567_out,
       and_568_out, and_569_out, and_570_out, and_571_out, and_572_out, and_573_out, and_574_out,
       and_575_out, and_576_out, and_577_out, and_578_out, and_579_out, and_580_out, and_581_out,
       and_582_out, and_583_out, and_584_out, and_585_out, and_586_out, and_587_out, and_588_out,
       and_589_out, and_590_out, and_591_out, and_592_out, and_593_out, and_594_out, and_595_out,
       and_596_out, and_597_out, and_598_out, and_599_out, and_600_out, and_601_out, and_602_out,
       and_603_out, and_604_out, and_605_out, and_606_out, and_607_out, and_608_out, and_609_out,
       and_610_out, and_611_out, and_612_out, and_613_out, and_614_out, and_615_out, and_616_out,
       and_617_out, and_618_out, and_619_out, and_620_out, and_621_out, and_622_out, and_623_out,
       and_624_out, and_625_out, and_626_out, and_627_out, and_628_out, and_629_out, and_630_out,
       and_631_out, and_632_out, and_633_out, and_634_out, and_635_out, and_636_out, and_637_out,
       and_638_out, and_639_out, and_640_out, and_641_out, and_642_out, and_643_out, and_644_out,
       and_645_out, and_646_out, and_647_out, and_648_out, and_649_out, and_650_out, and_651_out,
       and_652_out, and_653_out, and_654_out, and_655_out, and_656_out, and_657_out, and_658_out,
       and_659_out, and_660_out, and_661_out, and_662_out, and_663_out, and_664_out, and_665_out,
       and_666_out, and_667_out, and_668_out, and_669_out, and_670_out, and_671_out, and_672_out,
       and_673_out, and_674_out, and_675_out, and_676_out, and_677_out, and_678_out, and_679_out,
       and_680_out, and_681_out, and_682_out, and_683_out, and_684_out, and_685_out, and_686_out,
       and_687_out, and_688_out, and_689_out, and_690_out, and_691_out, and_692_out, and_693_out,
       and_694_out, and_695_out, and_696_out, and_697_out, and_698_out, and_699_out, and_700_out,
       and_701_out, and_702_out, and_703_out, and_704_out, and_705_out, and_706_out, and_707_out,
       and_708_out, and_709_out, and_710_out, and_711_out, and_712_out, and_713_out, and_714_out,
       and_715_out, and_716_out, and_717_out, and_718_out, and_719_out, and_720_out, and_721_out,
       and_722_out, and_723_out, and_724_out, and_725_out, and_726_out, and_727_out, and_728_out,
       and_729_out, and_730_out, and_731_out, and_732_out, and_733_out, and_734_out, and_735_out,
       and_736_out, and_737_out, and_738_out, and_739_out, and_740_out, and_741_out, and_742_out,
       and_743_out, and_744_out, and_745_out, and_746_out, and_747_out, and_748_out, and_749_out,
       and_750_out, and_751_out, and_752_out, and_753_out, and_754_out, and_755_out, and_756_out,
       and_757_out, and_758_out, and_759_out, and_760_out, and_761_out, and_762_out, and_763_out,
       and_764_out, and_765_out, and_766_out, and_767_out, and_768_out, deco_4x16_1_output_0,
       deco_4x16_1_output_1, deco_4x16_1_output_2, deco_4x16_1_output_3, deco_4x16_1_output_4,
       deco_4x16_1_output_5, deco_4x16_1_output_6, deco_4x16_1_output_7, deco_4x16_1_output_8,
       deco_4x16_1_output_9, deco_4x16_1_output_10, deco_4x16_1_output_11, deco_4x16_1_output_12,
       deco_4x16_1_output_13, deco_4x16_1_output_14, deco_4x16_1_output_15, deco_4x16_2_output_0,
       deco_4x16_2_output_1, deco_4x16_2_output_2, deco_4x16_2_output_3, deco_4x16_2_output_4,
       deco_4x16_2_output_5, deco_4x16_2_output_6, deco_4x16_2_output_7, deco_4x16_2_output_8,
       deco_4x16_2_output_9, deco_4x16_2_output_10, deco_4x16_2_output_11, deco_4x16_2_output_12,
       deco_4x16_2_output_13, deco_4x16_2_output_14;
  wire [7:0] memory_8bit_1_out_3;

  Memory_8Bit memory_8bit_1 (.in_1(Address), .in_2(Enable_addr), .out_3(memory_8bit_1_out_3));
  Deco_4x16 deco_4x16_1 (
    .Input_0(memory_8bit_1_out_3[4]), .Input_1(memory_8bit_1_out_3[5]), .Input_2(memory_8bit_1_out_3[6]),
    .Input_3(memory_8bit_1_out_3[7]), .Output_0(deco_4x16_1_output_0), .Output_1(deco_4x16_1_output_1),
    .Output_2(deco_4x16_1_output_2), .Output_3(deco_4x16_1_output_3), .Output_4(deco_4x16_1_output_4),
    .Output_5(deco_4x16_1_output_5), .Output_6(deco_4x16_1_output_6), .Output_7(deco_4x16_1_output_7),
    .Output_8(deco_4x16_1_output_8), .Output_9(deco_4x16_1_output_9), .Output_10(deco_4x16_1_output_10),
    .Output_11(deco_4x16_1_output_11), .Output_12(deco_4x16_1_output_12), .Output_13(deco_4x16_1_output_13),
    .Output_14(deco_4x16_1_output_14), .Output_15(deco_4x16_1_output_15));
  and and_1 (and_1_out, deco_4x16_1_output_15, deco_4x16_1_output_0);
  and and_2 (and_2_out, Write_Data, and_1_out);
  and and_3 (and_3_out, and_1_out, Enable_Data);
  buf and_4 (and_4_out, deco_4x16_1_output_15);  // AND_Gate
  and and_5 (and_5_out, Write_Data, and_4_out);
  and and_6 (and_6_out, and_4_out, Enable_Data);
  buf and_7 (and_7_out, deco_4x16_1_output_15);  // AND_Gate
  and and_8 (and_8_out, Write_Data, and_7_out);
  and and_9 (and_9_out, and_7_out, Enable_Data);
  buf and_10 (and_10_out, deco_4x16_1_output_15);  // AND_Gate
  and and_11 (and_11_out, Write_Data, and_10_out);
  and and_12 (and_12_out, and_10_out, Enable_Data);
  buf and_13 (and_13_out, deco_4x16_1_output_15);  // AND_Gate
  and and_14 (and_14_out, Write_Data, and_13_out);
  and and_15 (and_15_out, and_13_out, Enable_Data);
  buf and_16 (and_16_out, deco_4x16_1_output_15);  // AND_Gate
  and and_17 (and_17_out, Write_Data, and_16_out);
  and and_18 (and_18_out, and_16_out, Enable_Data);
  buf and_19 (and_19_out, deco_4x16_1_output_15);  // AND_Gate
  and and_20 (and_20_out, Write_Data, and_19_out);
  and and_21 (and_21_out, and_19_out, Enable_Data);
  buf and_22 (and_22_out, deco_4x16_1_output_15);  // AND_Gate
  and and_23 (and_23_out, Write_Data, and_22_out);
  and and_24 (and_24_out, and_22_out, Enable_Data);
  buf and_25 (and_25_out, deco_4x16_1_output_15);  // AND_Gate
  and and_26 (and_26_out, Write_Data, and_25_out);
  and and_27 (and_27_out, and_25_out, Enable_Data);
  buf and_28 (and_28_out, deco_4x16_1_output_15);  // AND_Gate
  and and_29 (and_29_out, Write_Data, and_28_out);
  and and_30 (and_30_out, and_28_out, Enable_Data);
  buf and_31 (and_31_out, deco_4x16_1_output_15);  // AND_Gate
  and and_32 (and_32_out, Write_Data, and_31_out);
  and and_33 (and_33_out, and_31_out, Enable_Data);
  buf and_34 (and_34_out, deco_4x16_1_output_15);  // AND_Gate
  and and_35 (and_35_out, Write_Data, and_34_out);
  and and_36 (and_36_out, and_34_out, Enable_Data);
  buf and_37 (and_37_out, deco_4x16_1_output_15);  // AND_Gate
  and and_38 (and_38_out, Write_Data, and_37_out);
  and and_39 (and_39_out, and_37_out, Enable_Data);
  buf and_40 (and_40_out, deco_4x16_1_output_15);  // AND_Gate
  and and_41 (and_41_out, Write_Data, and_40_out);
  and and_42 (and_42_out, and_40_out, Enable_Data);
  buf and_43 (and_43_out, deco_4x16_1_output_15);  // AND_Gate
  and and_44 (and_44_out, Write_Data, and_43_out);
  and and_45 (and_45_out, and_43_out, Enable_Data);
  buf and_46 (and_46_out, deco_4x16_1_output_15);  // AND_Gate
  and and_47 (and_47_out, Write_Data, and_46_out);
  and and_48 (and_48_out, and_46_out, Enable_Data);
  and and_49 (and_49_out, deco_4x16_2_output_14, deco_4x16_1_output_0);
  Reg_8Bit reg_8bit_1 (.in_1(Data), .Setter(and_2_out), .Enable(and_3_out), .out_4(Data));
  and and_50 (and_50_out, deco_4x16_2_output_14, deco_4x16_1_output_1);
  Reg_8Bit reg_8bit_2 (.in_1(Data), .Setter(and_5_out), .Enable(and_6_out), .out_4(Data));
  and and_51 (and_51_out, deco_4x16_2_output_14, deco_4x16_1_output_2);
  Reg_8Bit reg_8bit_3 (.in_1(Data), .Setter(and_8_out), .Enable(and_9_out), .out_4(Data));
  and and_52 (and_52_out, deco_4x16_2_output_14, deco_4x16_1_output_3);
  Reg_8Bit reg_8bit_4 (.in_1(Data), .Setter(and_11_out), .Enable(and_12_out), .out_4(Data));
  and and_53 (and_53_out, deco_4x16_2_output_14, deco_4x16_1_output_4);
  Reg_8Bit reg_8bit_5 (.in_1(Data), .Setter(and_14_out), .Enable(and_15_out), .out_4(Data));
  and and_54 (and_54_out, deco_4x16_2_output_14, deco_4x16_1_output_5);
  Reg_8Bit reg_8bit_6 (.in_1(Data), .Setter(and_17_out), .Enable(and_18_out), .out_4(Data));
  and and_55 (and_55_out, deco_4x16_2_output_14, deco_4x16_1_output_6);
  Reg_8Bit reg_8bit_7 (.in_1(Data), .Setter(and_20_out), .Enable(and_21_out), .out_4(Data));
  and and_56 (and_56_out, deco_4x16_2_output_14, deco_4x16_1_output_7);
  Reg_8Bit reg_8bit_8 (.in_1(Data), .Setter(and_23_out), .Enable(and_24_out), .out_4(Data));
  and and_57 (and_57_out, deco_4x16_2_output_14, deco_4x16_1_output_8);
  Reg_8Bit reg_8bit_9 (.in_1(Data), .Setter(and_26_out), .Enable(and_27_out), .out_4(Data));
  and and_58 (and_58_out, deco_4x16_2_output_14, deco_4x16_1_output_9);
  Reg_8Bit reg_8bit_10 (.in_1(Data), .Setter(and_29_out), .Enable(and_30_out), .out_4(Data));
  and and_59 (and_59_out, deco_4x16_2_output_14, deco_4x16_1_output_10);
  Reg_8Bit reg_8bit_11 (.in_1(Data), .Setter(and_32_out), .Enable(and_33_out), .out_4(Data));
  and and_60 (and_60_out, deco_4x16_2_output_14, deco_4x16_1_output_11);
  Reg_8Bit reg_8bit_12 (.in_1(Data), .Setter(and_35_out), .Enable(and_36_out), .out_4(Data));
  and and_61 (and_61_out, deco_4x16_2_output_14, deco_4x16_1_output_12);
  Reg_8Bit reg_8bit_13 (.in_1(Data), .Setter(and_38_out), .Enable(and_39_out), .out_4(Data));
  and and_62 (and_62_out, deco_4x16_2_output_14, deco_4x16_1_output_13);
  Reg_8Bit reg_8bit_14 (.in_1(Data), .Setter(and_41_out), .Enable(and_42_out), .out_4(Data));
  and and_63 (and_63_out, deco_4x16_2_output_14, deco_4x16_1_output_14);
  Reg_8Bit reg_8bit_15 (.in_1(Data), .Setter(and_44_out), .Enable(and_45_out), .out_4(Data));
  and and_64 (and_64_out, deco_4x16_2_output_14, deco_4x16_1_output_15);
  Reg_8Bit reg_8bit_16 (.in_1(Data), .Setter(and_47_out), .Enable(and_48_out), .out_4(Data));
  and and_65 (and_65_out, Write_Data, and_49_out);
  Reg_8Bit reg_8bit_17 (.in_1(Data), .Setter(and_65_out), .Enable(and_66_out), .out_4(Data));
  and and_66 (and_66_out, and_49_out, Enable_Data);
  and and_67 (and_67_out, Write_Data, and_50_out);
  Reg_8Bit reg_8bit_18 (.in_1(Data), .Setter(and_67_out), .Enable(and_68_out), .out_4(Data));
  and and_68 (and_68_out, and_50_out, Enable_Data);
  and and_69 (and_69_out, Write_Data, and_51_out);
  Reg_8Bit reg_8bit_19 (.in_1(Data), .Setter(and_69_out), .Enable(and_70_out), .out_4(Data));
  and and_70 (and_70_out, and_51_out, Enable_Data);
  and and_71 (and_71_out, Write_Data, and_52_out);
  Reg_8Bit reg_8bit_20 (.in_1(Data), .Setter(and_71_out), .Enable(and_72_out), .out_4(Data));
  and and_72 (and_72_out, and_52_out, Enable_Data);
  and and_73 (and_73_out, Write_Data, and_53_out);
  Reg_8Bit reg_8bit_21 (.in_1(Data), .Setter(and_73_out), .Enable(and_74_out), .out_4(Data));
  and and_74 (and_74_out, and_53_out, Enable_Data);
  and and_75 (and_75_out, Write_Data, and_54_out);
  Reg_8Bit reg_8bit_22 (.in_1(Data), .Setter(and_75_out), .Enable(and_76_out), .out_4(Data));
  and and_76 (and_76_out, and_54_out, Enable_Data);
  and and_77 (and_77_out, Write_Data, and_55_out);
  Reg_8Bit reg_8bit_23 (.in_1(Data), .Setter(and_77_out), .Enable(and_78_out), .out_4(Data));
  and and_78 (and_78_out, and_55_out, Enable_Data);
  and and_79 (and_79_out, Write_Data, and_56_out);
  Reg_8Bit reg_8bit_24 (.in_1(Data), .Setter(and_79_out), .Enable(and_80_out), .out_4(Data));
  and and_80 (and_80_out, and_56_out, Enable_Data);
  and and_81 (and_81_out, Write_Data, and_57_out);
  Reg_8Bit reg_8bit_25 (.in_1(Data), .Setter(and_81_out), .Enable(and_82_out), .out_4(Data));
  and and_82 (and_82_out, and_57_out, Enable_Data);
  and and_83 (and_83_out, Write_Data, and_58_out);
  Reg_8Bit reg_8bit_26 (.in_1(Data), .Setter(and_83_out), .Enable(and_84_out), .out_4(Data));
  and and_84 (and_84_out, and_58_out, Enable_Data);
  and and_85 (and_85_out, Write_Data, and_59_out);
  Reg_8Bit reg_8bit_27 (.in_1(Data), .Setter(and_85_out), .Enable(and_86_out), .out_4(Data));
  and and_86 (and_86_out, and_59_out, Enable_Data);
  and and_87 (and_87_out, Write_Data, and_60_out);
  Reg_8Bit reg_8bit_28 (.in_1(Data), .Setter(and_87_out), .Enable(and_88_out), .out_4(Data));
  and and_88 (and_88_out, and_60_out, Enable_Data);
  and and_89 (and_89_out, Write_Data, and_61_out);
  Reg_8Bit reg_8bit_29 (.in_1(Data), .Setter(and_89_out), .Enable(and_90_out), .out_4(Data));
  and and_90 (and_90_out, and_61_out, Enable_Data);
  and and_91 (and_91_out, Write_Data, and_62_out);
  Reg_8Bit reg_8bit_30 (.in_1(Data), .Setter(and_91_out), .Enable(and_92_out), .out_4(Data));
  and and_92 (and_92_out, and_62_out, Enable_Data);
  and and_93 (and_93_out, Write_Data, and_63_out);
  Reg_8Bit reg_8bit_31 (.in_1(Data), .Setter(and_93_out), .Enable(and_94_out), .out_4(Data));
  and and_94 (and_94_out, and_63_out, Enable_Data);
  and and_95 (and_95_out, Write_Data, and_64_out);
  Reg_8Bit reg_8bit_32 (.in_1(Data), .Setter(and_95_out), .Enable(and_96_out), .out_4(Data));
  and and_96 (and_96_out, and_64_out, Enable_Data);
  and and_97 (and_97_out, deco_4x16_2_output_13, deco_4x16_1_output_0);
  and and_98 (and_98_out, deco_4x16_2_output_13, deco_4x16_1_output_1);
  buf and_99 (and_99_out, deco_4x16_2_output_13);  // AND_Gate
  and and_100 (and_100_out, deco_4x16_2_output_13, deco_4x16_1_output_3);
  and and_101 (and_101_out, deco_4x16_2_output_13, deco_4x16_1_output_4);
  and and_102 (and_102_out, deco_4x16_2_output_13, deco_4x16_1_output_5);
  and and_103 (and_103_out, deco_4x16_2_output_13, deco_4x16_1_output_6);
  and and_104 (and_104_out, deco_4x16_2_output_13, deco_4x16_1_output_7);
  and and_105 (and_105_out, deco_4x16_2_output_13, deco_4x16_1_output_8);
  and and_106 (and_106_out, deco_4x16_2_output_13, deco_4x16_1_output_9);
  buf and_107 (and_107_out, deco_4x16_2_output_13);  // AND_Gate
  and and_108 (and_108_out, deco_4x16_2_output_13, deco_4x16_1_output_11);
  and and_109 (and_109_out, deco_4x16_2_output_13, deco_4x16_1_output_12);
  and and_110 (and_110_out, deco_4x16_2_output_13, deco_4x16_1_output_13);
  and and_111 (and_111_out, deco_4x16_2_output_13, deco_4x16_1_output_14);
  and and_112 (and_112_out, deco_4x16_2_output_13, deco_4x16_1_output_15);
  and and_113 (and_113_out, Write_Data, and_97_out);
  Reg_8Bit reg_8bit_33 (.in_1(Data), .Setter(and_113_out), .Enable(and_114_out), .out_4(Data));
  and and_114 (and_114_out, and_97_out, Enable_Data);
  and and_115 (and_115_out, Write_Data, and_98_out);
  Reg_8Bit reg_8bit_34 (.in_1(Data), .Setter(and_115_out), .Enable(and_116_out), .out_4(Data));
  and and_116 (and_116_out, and_98_out, Enable_Data);
  and and_117 (and_117_out, Write_Data, and_99_out);
  Reg_8Bit reg_8bit_35 (.in_1(Data), .Setter(and_117_out), .Enable(and_118_out), .out_4(Data));
  and and_118 (and_118_out, and_99_out, Enable_Data);
  and and_119 (and_119_out, Write_Data, and_100_out);
  Reg_8Bit reg_8bit_36 (.in_1(Data), .Setter(and_119_out), .Enable(and_120_out), .out_4(Data));
  and and_120 (and_120_out, and_100_out, Enable_Data);
  and and_121 (and_121_out, Write_Data, and_101_out);
  Reg_8Bit reg_8bit_37 (.in_1(Data), .Setter(and_121_out), .Enable(and_122_out), .out_4(Data));
  and and_122 (and_122_out, and_101_out, Enable_Data);
  and and_123 (and_123_out, Write_Data, and_102_out);
  Reg_8Bit reg_8bit_38 (.in_1(Data), .Setter(and_123_out), .Enable(and_124_out), .out_4(Data));
  and and_124 (and_124_out, and_102_out, Enable_Data);
  and and_125 (and_125_out, Write_Data, and_103_out);
  Reg_8Bit reg_8bit_39 (.in_1(Data), .Setter(and_125_out), .Enable(and_126_out), .out_4(Data));
  and and_126 (and_126_out, and_103_out, Enable_Data);
  and and_127 (and_127_out, Write_Data, and_104_out);
  Reg_8Bit reg_8bit_40 (.in_1(Data), .Setter(and_127_out), .Enable(and_128_out), .out_4(Data));
  and and_128 (and_128_out, and_104_out, Enable_Data);
  and and_129 (and_129_out, Write_Data, and_105_out);
  Reg_8Bit reg_8bit_41 (.in_1(Data), .Setter(and_129_out), .Enable(and_130_out), .out_4(Data));
  and and_130 (and_130_out, and_105_out, Enable_Data);
  and and_131 (and_131_out, Write_Data, and_106_out);
  Reg_8Bit reg_8bit_42 (.in_1(Data), .Setter(and_131_out), .Enable(and_132_out), .out_4(Data));
  and and_132 (and_132_out, and_106_out, Enable_Data);
  and and_133 (and_133_out, Write_Data, and_107_out);
  Reg_8Bit reg_8bit_43 (.in_1(Data), .Setter(and_133_out), .Enable(and_134_out), .out_4(Data));
  and and_134 (and_134_out, and_107_out, Enable_Data);
  and and_135 (and_135_out, Write_Data, and_108_out);
  Reg_8Bit reg_8bit_44 (.in_1(Data), .Setter(and_135_out), .Enable(and_136_out), .out_4(Data));
  and and_136 (and_136_out, and_108_out, Enable_Data);
  and and_137 (and_137_out, Write_Data, and_109_out);
  Reg_8Bit reg_8bit_45 (.in_1(Data), .Setter(and_137_out), .Enable(and_138_out), .out_4(Data));
  and and_138 (and_138_out, and_109_out, Enable_Data);
  and and_139 (and_139_out, Write_Data, and_110_out);
  Reg_8Bit reg_8bit_46 (.in_1(Data), .Setter(and_139_out), .Enable(and_140_out), .out_4(Data));
  and and_140 (and_140_out, and_110_out, Enable_Data);
  and and_141 (and_141_out, Write_Data, and_111_out);
  Reg_8Bit reg_8bit_47 (.in_1(Data), .Setter(and_141_out), .Enable(and_142_out), .out_4(Data));
  and and_142 (and_142_out, and_111_out, Enable_Data);
  and and_143 (and_143_out, Write_Data, and_112_out);
  Reg_8Bit reg_8bit_48 (.in_1(Data), .Setter(and_143_out), .Enable(and_144_out), .out_4(Data));
  and and_144 (and_144_out, and_112_out, Enable_Data);
  and and_145 (and_145_out, deco_4x16_2_output_12, deco_4x16_1_output_0);
  and and_146 (and_146_out, Write_Data, and_145_out);
  and and_147 (and_147_out, and_145_out, Enable_Data);
  and and_148 (and_148_out, deco_4x16_2_output_12, deco_4x16_1_output_1);
  and and_149 (and_149_out, Write_Data, and_148_out);
  and and_150 (and_150_out, and_148_out, Enable_Data);
  buf and_151 (and_151_out, deco_4x16_2_output_12);  // AND_Gate
  and and_152 (and_152_out, Write_Data, and_151_out);
  and and_153 (and_153_out, and_151_out, Enable_Data);
  and and_154 (and_154_out, deco_4x16_2_output_12, deco_4x16_1_output_3);
  and and_155 (and_155_out, Write_Data, and_154_out);
  and and_156 (and_156_out, and_154_out, Enable_Data);
  and and_157 (and_157_out, deco_4x16_2_output_12, deco_4x16_1_output_4);
  and and_158 (and_158_out, Write_Data, and_157_out);
  and and_159 (and_159_out, and_157_out, Enable_Data);
  and and_160 (and_160_out, deco_4x16_2_output_12, deco_4x16_1_output_5);
  and and_161 (and_161_out, Write_Data, and_160_out);
  and and_162 (and_162_out, and_160_out, Enable_Data);
  and and_163 (and_163_out, deco_4x16_2_output_12, deco_4x16_1_output_6);
  and and_164 (and_164_out, Write_Data, and_163_out);
  and and_165 (and_165_out, and_163_out, Enable_Data);
  and and_166 (and_166_out, deco_4x16_2_output_12, deco_4x16_1_output_7);
  and and_167 (and_167_out, Write_Data, and_166_out);
  and and_168 (and_168_out, and_166_out, Enable_Data);
  and and_169 (and_169_out, deco_4x16_2_output_12, deco_4x16_1_output_8);
  and and_170 (and_170_out, Write_Data, and_169_out);
  and and_171 (and_171_out, and_169_out, Enable_Data);
  and and_172 (and_172_out, deco_4x16_2_output_12, deco_4x16_1_output_9);
  and and_173 (and_173_out, Write_Data, and_172_out);
  and and_174 (and_174_out, and_172_out, Enable_Data);
  buf and_175 (and_175_out, deco_4x16_2_output_12);  // AND_Gate
  and and_176 (and_176_out, Write_Data, and_175_out);
  and and_177 (and_177_out, and_175_out, Enable_Data);
  and and_178 (and_178_out, deco_4x16_2_output_12, deco_4x16_1_output_11);
  and and_179 (and_179_out, Write_Data, and_178_out);
  and and_180 (and_180_out, and_178_out, Enable_Data);
  and and_181 (and_181_out, deco_4x16_2_output_12, deco_4x16_1_output_12);
  and and_182 (and_182_out, Write_Data, and_181_out);
  and and_183 (and_183_out, and_181_out, Enable_Data);
  and and_184 (and_184_out, deco_4x16_2_output_12, deco_4x16_1_output_13);
  and and_185 (and_185_out, Write_Data, and_184_out);
  and and_186 (and_186_out, and_184_out, Enable_Data);
  and and_187 (and_187_out, deco_4x16_2_output_12, deco_4x16_1_output_14);
  and and_188 (and_188_out, Write_Data, and_187_out);
  and and_189 (and_189_out, and_187_out, Enable_Data);
  and and_190 (and_190_out, deco_4x16_2_output_12, deco_4x16_1_output_15);
  and and_191 (and_191_out, Write_Data, and_190_out);
  and and_192 (and_192_out, and_190_out, Enable_Data);
  Reg_8Bit reg_8bit_49 (.in_1(Data), .Setter(and_146_out), .Enable(and_147_out), .out_4(Data));
  Reg_8Bit reg_8bit_50 (.in_1(Data), .Setter(and_149_out), .Enable(and_150_out), .out_4(Data));
  Reg_8Bit reg_8bit_51 (.in_1(Data), .Setter(and_152_out), .Enable(and_153_out), .out_4(Data));
  Reg_8Bit reg_8bit_52 (.in_1(Data), .Setter(and_155_out), .Enable(and_156_out), .out_4(Data));
  Reg_8Bit reg_8bit_53 (.in_1(Data), .Setter(and_158_out), .Enable(and_159_out), .out_4(Data));
  Reg_8Bit reg_8bit_54 (.in_1(Data), .Setter(and_161_out), .Enable(and_162_out), .out_4(Data));
  Reg_8Bit reg_8bit_55 (.in_1(Data), .Setter(and_164_out), .Enable(and_165_out), .out_4(Data));
  Reg_8Bit reg_8bit_56 (.in_1(Data), .Setter(and_167_out), .Enable(and_168_out), .out_4(Data));
  Reg_8Bit reg_8bit_57 (.in_1(Data), .Setter(and_170_out), .Enable(and_171_out), .out_4(Data));
  Reg_8Bit reg_8bit_58 (.in_1(Data), .Setter(and_173_out), .Enable(and_174_out), .out_4(Data));
  Reg_8Bit reg_8bit_59 (.in_1(Data), .Setter(and_176_out), .Enable(and_177_out), .out_4(Data));
  Reg_8Bit reg_8bit_60 (.in_1(Data), .Setter(and_179_out), .Enable(and_180_out), .out_4(Data));
  Reg_8Bit reg_8bit_61 (.in_1(Data), .Setter(and_182_out), .Enable(and_183_out), .out_4(Data));
  Reg_8Bit reg_8bit_62 (.in_1(Data), .Setter(and_185_out), .Enable(and_186_out), .out_4(Data));
  Reg_8Bit reg_8bit_63 (.in_1(Data), .Setter(and_188_out), .Enable(and_189_out), .out_4(Data));
  Reg_8Bit reg_8bit_64 (.in_1(Data), .Setter(and_191_out), .Enable(and_192_out), .out_4(Data));
  and and_193 (and_193_out, deco_4x16_2_output_11, deco_4x16_1_output_0);
  and and_194 (and_194_out, Write_Data, and_193_out);
  and and_195 (and_195_out, and_193_out, Enable_Data);
  and and_196 (and_196_out, deco_4x16_2_output_11, deco_4x16_1_output_1);
  and and_197 (and_197_out, Write_Data, and_196_out);
  and and_198 (and_198_out, and_196_out, Enable_Data);
  buf and_199 (and_199_out, deco_4x16_2_output_11);  // AND_Gate
  and and_200 (and_200_out, Write_Data, and_199_out);
  and and_201 (and_201_out, and_199_out, Enable_Data);
  and and_202 (and_202_out, deco_4x16_2_output_11, deco_4x16_1_output_3);
  and and_203 (and_203_out, Write_Data, and_202_out);
  and and_204 (and_204_out, and_202_out, Enable_Data);
  and and_205 (and_205_out, deco_4x16_2_output_11, deco_4x16_1_output_4);
  and and_206 (and_206_out, Write_Data, and_205_out);
  and and_207 (and_207_out, and_205_out, Enable_Data);
  and and_208 (and_208_out, deco_4x16_2_output_11, deco_4x16_1_output_5);
  and and_209 (and_209_out, Write_Data, and_208_out);
  and and_210 (and_210_out, and_208_out, Enable_Data);
  and and_211 (and_211_out, deco_4x16_2_output_11, deco_4x16_1_output_6);
  and and_212 (and_212_out, Write_Data, and_211_out);
  and and_213 (and_213_out, and_211_out, Enable_Data);
  and and_214 (and_214_out, deco_4x16_2_output_11, deco_4x16_1_output_7);
  and and_215 (and_215_out, Write_Data, and_214_out);
  and and_216 (and_216_out, and_214_out, Enable_Data);
  and and_217 (and_217_out, deco_4x16_2_output_11, deco_4x16_1_output_8);
  and and_218 (and_218_out, Write_Data, and_217_out);
  and and_219 (and_219_out, and_217_out, Enable_Data);
  and and_220 (and_220_out, deco_4x16_2_output_11, deco_4x16_1_output_9);
  and and_221 (and_221_out, Write_Data, and_220_out);
  and and_222 (and_222_out, and_220_out, Enable_Data);
  buf and_223 (and_223_out, deco_4x16_2_output_11);  // AND_Gate
  and and_224 (and_224_out, Write_Data, and_223_out);
  and and_225 (and_225_out, and_223_out, Enable_Data);
  and and_226 (and_226_out, deco_4x16_2_output_11, deco_4x16_1_output_11);
  and and_227 (and_227_out, Write_Data, and_226_out);
  and and_228 (and_228_out, and_226_out, Enable_Data);
  and and_229 (and_229_out, deco_4x16_2_output_11, deco_4x16_1_output_12);
  and and_230 (and_230_out, Write_Data, and_229_out);
  and and_231 (and_231_out, and_229_out, Enable_Data);
  and and_232 (and_232_out, deco_4x16_2_output_11, deco_4x16_1_output_13);
  and and_233 (and_233_out, Write_Data, and_232_out);
  and and_234 (and_234_out, and_232_out, Enable_Data);
  and and_235 (and_235_out, deco_4x16_2_output_11, deco_4x16_1_output_14);
  and and_236 (and_236_out, Write_Data, and_235_out);
  and and_237 (and_237_out, and_235_out, Enable_Data);
  and and_238 (and_238_out, deco_4x16_2_output_11, deco_4x16_1_output_15);
  and and_239 (and_239_out, Write_Data, and_238_out);
  and and_240 (and_240_out, and_238_out, Enable_Data);
  and and_241 (and_241_out, deco_4x16_2_output_10, deco_4x16_1_output_0);
  Reg_8Bit reg_8bit_65 (.in_1(Data), .Setter(and_194_out), .Enable(and_195_out), .out_4(Data));
  and and_242 (and_242_out, deco_4x16_2_output_10, deco_4x16_1_output_1);
  Reg_8Bit reg_8bit_66 (.in_1(Data), .Setter(and_197_out), .Enable(and_198_out), .out_4(Data));
  buf and_243 (and_243_out, deco_4x16_2_output_10);  // AND_Gate
  Reg_8Bit reg_8bit_67 (.in_1(Data), .Setter(and_200_out), .Enable(and_201_out), .out_4(Data));
  and and_244 (and_244_out, deco_4x16_2_output_10, deco_4x16_1_output_3);
  Reg_8Bit reg_8bit_68 (.in_1(Data), .Setter(and_203_out), .Enable(and_204_out), .out_4(Data));
  and and_245 (and_245_out, deco_4x16_2_output_10, deco_4x16_1_output_4);
  Reg_8Bit reg_8bit_69 (.in_1(Data), .Setter(and_206_out), .Enable(and_207_out), .out_4(Data));
  and and_246 (and_246_out, deco_4x16_2_output_10, deco_4x16_1_output_5);
  Reg_8Bit reg_8bit_70 (.in_1(Data), .Setter(and_209_out), .Enable(and_210_out), .out_4(Data));
  and and_247 (and_247_out, deco_4x16_2_output_10, deco_4x16_1_output_6);
  Reg_8Bit reg_8bit_71 (.in_1(Data), .Setter(and_212_out), .Enable(and_213_out), .out_4(Data));
  and and_248 (and_248_out, deco_4x16_2_output_10, deco_4x16_1_output_7);
  Reg_8Bit reg_8bit_72 (.in_1(Data), .Setter(and_215_out), .Enable(and_216_out), .out_4(Data));
  and and_249 (and_249_out, deco_4x16_2_output_10, deco_4x16_1_output_8);
  Reg_8Bit reg_8bit_73 (.in_1(Data), .Setter(and_218_out), .Enable(and_219_out), .out_4(Data));
  and and_250 (and_250_out, deco_4x16_2_output_10, deco_4x16_1_output_9);
  Reg_8Bit reg_8bit_74 (.in_1(Data), .Setter(and_221_out), .Enable(and_222_out), .out_4(Data));
  buf and_251 (and_251_out, deco_4x16_2_output_10);  // AND_Gate
  Reg_8Bit reg_8bit_75 (.in_1(Data), .Setter(and_224_out), .Enable(and_225_out), .out_4(Data));
  and and_252 (and_252_out, deco_4x16_2_output_10, deco_4x16_1_output_11);
  Reg_8Bit reg_8bit_76 (.in_1(Data), .Setter(and_227_out), .Enable(and_228_out), .out_4(Data));
  and and_253 (and_253_out, deco_4x16_2_output_10, deco_4x16_1_output_12);
  Reg_8Bit reg_8bit_77 (.in_1(Data), .Setter(and_230_out), .Enable(and_231_out), .out_4(Data));
  and and_254 (and_254_out, deco_4x16_2_output_10, deco_4x16_1_output_13);
  Reg_8Bit reg_8bit_78 (.in_1(Data), .Setter(and_233_out), .Enable(and_234_out), .out_4(Data));
  and and_255 (and_255_out, deco_4x16_2_output_10, deco_4x16_1_output_14);
  Reg_8Bit reg_8bit_79 (.in_1(Data), .Setter(and_236_out), .Enable(and_237_out), .out_4(Data));
  and and_256 (and_256_out, deco_4x16_2_output_10, deco_4x16_1_output_15);
  Reg_8Bit reg_8bit_80 (.in_1(Data), .Setter(and_239_out), .Enable(and_240_out), .out_4(Data));
  and and_257 (and_257_out, Write_Data, and_241_out);
  Reg_8Bit reg_8bit_81 (.in_1(Data), .Setter(and_257_out), .Enable(and_258_out), .out_4(Data));
  and and_258 (and_258_out, and_241_out, Enable_Data);
  and and_259 (and_259_out, Write_Data, and_242_out);
  Reg_8Bit reg_8bit_82 (.in_1(Data), .Setter(and_259_out), .Enable(and_260_out), .out_4(Data));
  and and_260 (and_260_out, and_242_out, Enable_Data);
  and and_261 (and_261_out, Write_Data, and_243_out);
  Reg_8Bit reg_8bit_83 (.in_1(Data), .Setter(and_261_out), .Enable(and_262_out), .out_4(Data));
  and and_262 (and_262_out, and_243_out, Enable_Data);
  and and_263 (and_263_out, Write_Data, and_244_out);
  Reg_8Bit reg_8bit_84 (.in_1(Data), .Setter(and_263_out), .Enable(and_264_out), .out_4(Data));
  and and_264 (and_264_out, and_244_out, Enable_Data);
  and and_265 (and_265_out, Write_Data, and_245_out);
  Reg_8Bit reg_8bit_85 (.in_1(Data), .Setter(and_265_out), .Enable(and_266_out), .out_4(Data));
  and and_266 (and_266_out, and_245_out, Enable_Data);
  and and_267 (and_267_out, Write_Data, and_246_out);
  Reg_8Bit reg_8bit_86 (.in_1(Data), .Setter(and_267_out), .Enable(and_268_out), .out_4(Data));
  and and_268 (and_268_out, and_246_out, Enable_Data);
  and and_269 (and_269_out, Write_Data, and_247_out);
  Reg_8Bit reg_8bit_87 (.in_1(Data), .Setter(and_269_out), .Enable(and_270_out), .out_4(Data));
  and and_270 (and_270_out, and_247_out, Enable_Data);
  and and_271 (and_271_out, Write_Data, and_248_out);
  Reg_8Bit reg_8bit_88 (.in_1(Data), .Setter(and_271_out), .Enable(and_272_out), .out_4(Data));
  and and_272 (and_272_out, and_248_out, Enable_Data);
  and and_273 (and_273_out, Write_Data, and_249_out);
  Reg_8Bit reg_8bit_89 (.in_1(Data), .Setter(and_273_out), .Enable(and_274_out), .out_4(Data));
  and and_274 (and_274_out, and_249_out, Enable_Data);
  and and_275 (and_275_out, Write_Data, and_250_out);
  Reg_8Bit reg_8bit_90 (.in_1(Data), .Setter(and_275_out), .Enable(and_276_out), .out_4(Data));
  and and_276 (and_276_out, and_250_out, Enable_Data);
  and and_277 (and_277_out, Write_Data, and_251_out);
  Reg_8Bit reg_8bit_91 (.in_1(Data), .Setter(and_277_out), .Enable(and_278_out), .out_4(Data));
  and and_278 (and_278_out, and_251_out, Enable_Data);
  and and_279 (and_279_out, Write_Data, and_252_out);
  Reg_8Bit reg_8bit_92 (.in_1(Data), .Setter(and_279_out), .Enable(and_280_out), .out_4(Data));
  and and_280 (and_280_out, and_252_out, Enable_Data);
  and and_281 (and_281_out, Write_Data, and_253_out);
  Reg_8Bit reg_8bit_93 (.in_1(Data), .Setter(and_281_out), .Enable(and_282_out), .out_4(Data));
  and and_282 (and_282_out, and_253_out, Enable_Data);
  and and_283 (and_283_out, Write_Data, and_254_out);
  Reg_8Bit reg_8bit_94 (.in_1(Data), .Setter(and_283_out), .Enable(and_284_out), .out_4(Data));
  and and_284 (and_284_out, and_254_out, Enable_Data);
  and and_285 (and_285_out, Write_Data, and_255_out);
  Reg_8Bit reg_8bit_95 (.in_1(Data), .Setter(and_285_out), .Enable(and_286_out), .out_4(Data));
  and and_286 (and_286_out, and_255_out, Enable_Data);
  and and_287 (and_287_out, Write_Data, and_256_out);
  Reg_8Bit reg_8bit_96 (.in_1(Data), .Setter(and_287_out), .Enable(and_288_out), .out_4(Data));
  and and_288 (and_288_out, and_256_out, Enable_Data);
  and and_289 (and_289_out, deco_4x16_2_output_9, deco_4x16_1_output_0);
  and and_290 (and_290_out, deco_4x16_2_output_9, deco_4x16_1_output_1);
  buf and_291 (and_291_out, deco_4x16_2_output_9);  // AND_Gate
  and and_292 (and_292_out, deco_4x16_2_output_9, deco_4x16_1_output_3);
  and and_293 (and_293_out, deco_4x16_2_output_9, deco_4x16_1_output_4);
  and and_294 (and_294_out, deco_4x16_2_output_9, deco_4x16_1_output_5);
  and and_295 (and_295_out, deco_4x16_2_output_9, deco_4x16_1_output_6);
  and and_296 (and_296_out, deco_4x16_2_output_9, deco_4x16_1_output_7);
  and and_297 (and_297_out, deco_4x16_2_output_9, deco_4x16_1_output_8);
  and and_298 (and_298_out, deco_4x16_2_output_9, deco_4x16_1_output_9);
  buf and_299 (and_299_out, deco_4x16_2_output_9);  // AND_Gate
  and and_300 (and_300_out, deco_4x16_2_output_9, deco_4x16_1_output_11);
  and and_301 (and_301_out, deco_4x16_2_output_9, deco_4x16_1_output_12);
  and and_302 (and_302_out, deco_4x16_2_output_9, deco_4x16_1_output_13);
  and and_303 (and_303_out, deco_4x16_2_output_9, deco_4x16_1_output_14);
  and and_304 (and_304_out, deco_4x16_2_output_9, deco_4x16_1_output_15);
  and and_305 (and_305_out, Write_Data, and_289_out);
  Reg_8Bit reg_8bit_97 (.in_1(Data), .Setter(and_305_out), .Enable(and_306_out), .out_4(Data));
  and and_306 (and_306_out, and_289_out, Enable_Data);
  and and_307 (and_307_out, Write_Data, and_290_out);
  Reg_8Bit reg_8bit_98 (.in_1(Data), .Setter(and_307_out), .Enable(and_308_out), .out_4(Data));
  and and_308 (and_308_out, and_290_out, Enable_Data);
  and and_309 (and_309_out, Write_Data, and_291_out);
  Reg_8Bit reg_8bit_99 (.in_1(Data), .Setter(and_309_out), .Enable(and_310_out), .out_4(Data));
  and and_310 (and_310_out, and_291_out, Enable_Data);
  and and_311 (and_311_out, Write_Data, and_292_out);
  Reg_8Bit reg_8bit_100 (.in_1(Data), .Setter(and_311_out), .Enable(and_312_out), .out_4(Data));
  and and_312 (and_312_out, and_292_out, Enable_Data);
  and and_313 (and_313_out, Write_Data, and_293_out);
  Reg_8Bit reg_8bit_101 (.in_1(Data), .Setter(and_313_out), .Enable(and_314_out), .out_4(Data));
  and and_314 (and_314_out, and_293_out, Enable_Data);
  and and_315 (and_315_out, Write_Data, and_294_out);
  Reg_8Bit reg_8bit_102 (.in_1(Data), .Setter(and_315_out), .Enable(and_316_out), .out_4(Data));
  and and_316 (and_316_out, and_294_out, Enable_Data);
  and and_317 (and_317_out, Write_Data, and_295_out);
  Reg_8Bit reg_8bit_103 (.in_1(Data), .Setter(and_317_out), .Enable(and_318_out), .out_4(Data));
  and and_318 (and_318_out, and_295_out, Enable_Data);
  and and_319 (and_319_out, Write_Data, and_296_out);
  Reg_8Bit reg_8bit_104 (.in_1(Data), .Setter(and_319_out), .Enable(and_320_out), .out_4(Data));
  and and_320 (and_320_out, and_296_out, Enable_Data);
  and and_321 (and_321_out, Write_Data, and_297_out);
  Reg_8Bit reg_8bit_105 (.in_1(Data), .Setter(and_321_out), .Enable(and_322_out), .out_4(Data));
  and and_322 (and_322_out, and_297_out, Enable_Data);
  and and_323 (and_323_out, Write_Data, and_298_out);
  Reg_8Bit reg_8bit_106 (.in_1(Data), .Setter(and_323_out), .Enable(and_324_out), .out_4(Data));
  and and_324 (and_324_out, and_298_out, Enable_Data);
  and and_325 (and_325_out, Write_Data, and_299_out);
  Reg_8Bit reg_8bit_107 (.in_1(Data), .Setter(and_325_out), .Enable(and_326_out), .out_4(Data));
  and and_326 (and_326_out, and_299_out, Enable_Data);
  and and_327 (and_327_out, Write_Data, and_300_out);
  Reg_8Bit reg_8bit_108 (.in_1(Data), .Setter(and_327_out), .Enable(and_328_out), .out_4(Data));
  and and_328 (and_328_out, and_300_out, Enable_Data);
  and and_329 (and_329_out, Write_Data, and_301_out);
  Reg_8Bit reg_8bit_109 (.in_1(Data), .Setter(and_329_out), .Enable(and_330_out), .out_4(Data));
  and and_330 (and_330_out, and_301_out, Enable_Data);
  and and_331 (and_331_out, Write_Data, and_302_out);
  Reg_8Bit reg_8bit_110 (.in_1(Data), .Setter(and_331_out), .Enable(and_332_out), .out_4(Data));
  and and_332 (and_332_out, and_302_out, Enable_Data);
  and and_333 (and_333_out, Write_Data, and_303_out);
  Reg_8Bit reg_8bit_111 (.in_1(Data), .Setter(and_333_out), .Enable(and_334_out), .out_4(Data));
  and and_334 (and_334_out, and_303_out, Enable_Data);
  and and_335 (and_335_out, Write_Data, and_304_out);
  Reg_8Bit reg_8bit_112 (.in_1(Data), .Setter(and_335_out), .Enable(and_336_out), .out_4(Data));
  and and_336 (and_336_out, and_304_out, Enable_Data);
  Deco_4x16 deco_4x16_2 (
    .Input_0(memory_8bit_1_out_3[0]), .Input_1(memory_8bit_1_out_3[1]), .Input_2(memory_8bit_1_out_3[2]),
    .Input_3(memory_8bit_1_out_3[3]), .Output_0(deco_4x16_2_output_0), .Output_1(deco_4x16_2_output_1),
    .Output_2(deco_4x16_2_output_2), .Output_3(deco_4x16_2_output_3), .Output_4(deco_4x16_2_output_4),
    .Output_5(deco_4x16_2_output_5), .Output_6(deco_4x16_2_output_6), .Output_7(deco_4x16_2_output_7),
    .Output_8(deco_4x16_2_output_8), .Output_9(deco_4x16_2_output_9), .Output_10(deco_4x16_2_output_10),
    .Output_11(deco_4x16_2_output_11), .Output_12(deco_4x16_2_output_12), .Output_13(deco_4x16_2_output_13),
    .Output_14(deco_4x16_2_output_14), .Output_15(deco_4x16_1_output_15));
  and and_337 (and_337_out, deco_4x16_2_output_8, deco_4x16_1_output_0);
  and and_338 (and_338_out, Write_Data, and_337_out);
  and and_339 (and_339_out, and_337_out, Enable_Data);
  and and_340 (and_340_out, deco_4x16_2_output_8, deco_4x16_1_output_1);
  and and_341 (and_341_out, Write_Data, and_340_out);
  and and_342 (and_342_out, and_340_out, Enable_Data);
  and and_343 (and_343_out, deco_4x16_2_output_8, deco_4x16_1_output_2);
  and and_344 (and_344_out, Write_Data, and_343_out);
  and and_345 (and_345_out, and_343_out, Enable_Data);
  and and_346 (and_346_out, deco_4x16_2_output_8, deco_4x16_1_output_3);
  and and_347 (and_347_out, Write_Data, and_346_out);
  and and_348 (and_348_out, and_346_out, Enable_Data);
  and and_349 (and_349_out, deco_4x16_2_output_8, deco_4x16_1_output_4);
  and and_350 (and_350_out, Write_Data, and_349_out);
  and and_351 (and_351_out, and_349_out, Enable_Data);
  and and_352 (and_352_out, deco_4x16_2_output_8, deco_4x16_1_output_5);
  and and_353 (and_353_out, Write_Data, and_352_out);
  and and_354 (and_354_out, and_352_out, Enable_Data);
  and and_355 (and_355_out, deco_4x16_2_output_8, deco_4x16_1_output_6);
  and and_356 (and_356_out, Write_Data, and_355_out);
  and and_357 (and_357_out, and_355_out, Enable_Data);
  and and_358 (and_358_out, deco_4x16_2_output_8, deco_4x16_1_output_7);
  and and_359 (and_359_out, Write_Data, and_358_out);
  and and_360 (and_360_out, and_358_out, Enable_Data);
  and and_361 (and_361_out, deco_4x16_2_output_8, deco_4x16_1_output_8);
  and and_362 (and_362_out, Write_Data, and_361_out);
  and and_363 (and_363_out, and_361_out, Enable_Data);
  and and_364 (and_364_out, deco_4x16_2_output_8, deco_4x16_1_output_9);
  and and_365 (and_365_out, Write_Data, and_364_out);
  and and_366 (and_366_out, and_364_out, Enable_Data);
  and and_367 (and_367_out, deco_4x16_2_output_8, deco_4x16_1_output_10);
  and and_368 (and_368_out, Write_Data, and_367_out);
  and and_369 (and_369_out, and_367_out, Enable_Data);
  and and_370 (and_370_out, deco_4x16_2_output_8, deco_4x16_1_output_11);
  and and_371 (and_371_out, Write_Data, and_370_out);
  and and_372 (and_372_out, and_370_out, Enable_Data);
  and and_373 (and_373_out, deco_4x16_2_output_8, deco_4x16_1_output_12);
  and and_374 (and_374_out, Write_Data, and_373_out);
  and and_375 (and_375_out, and_373_out, Enable_Data);
  and and_376 (and_376_out, deco_4x16_2_output_8, deco_4x16_1_output_13);
  and and_377 (and_377_out, Write_Data, and_376_out);
  and and_378 (and_378_out, and_376_out, Enable_Data);
  and and_379 (and_379_out, deco_4x16_2_output_8, deco_4x16_1_output_14);
  and and_380 (and_380_out, Write_Data, and_379_out);
  and and_381 (and_381_out, and_379_out, Enable_Data);
  and and_382 (and_382_out, deco_4x16_2_output_8, deco_4x16_1_output_15);
  and and_383 (and_383_out, Write_Data, and_382_out);
  and and_384 (and_384_out, and_382_out, Enable_Data);
  Reg_8Bit reg_8bit_113 (.in_1(Data), .Setter(and_338_out), .Enable(and_339_out), .out_4(Data));
  Reg_8Bit reg_8bit_114 (.in_1(Data), .Setter(and_341_out), .Enable(and_342_out), .out_4(Data));
  Reg_8Bit reg_8bit_115 (.in_1(Data), .Setter(and_344_out), .Enable(and_345_out), .out_4(Data));
  Reg_8Bit reg_8bit_116 (.in_1(Data), .Setter(and_347_out), .Enable(and_348_out), .out_4(Data));
  Reg_8Bit reg_8bit_117 (.in_1(Data), .Setter(and_350_out), .Enable(and_351_out), .out_4(Data));
  Reg_8Bit reg_8bit_118 (.in_1(Data), .Setter(and_353_out), .Enable(and_354_out), .out_4(Data));
  Reg_8Bit reg_8bit_119 (.in_1(Data), .Setter(and_356_out), .Enable(and_357_out), .out_4(Data));
  Reg_8Bit reg_8bit_120 (.in_1(Data), .Setter(and_359_out), .Enable(and_360_out), .out_4(Data));
  Reg_8Bit reg_8bit_121 (.in_1(Data), .Setter(and_362_out), .Enable(and_363_out), .out_4(Data));
  Reg_8Bit reg_8bit_122 (.in_1(Data), .Setter(and_365_out), .Enable(and_366_out), .out_4(Data));
  Reg_8Bit reg_8bit_123 (.in_1(Data), .Setter(and_368_out), .Enable(and_369_out), .out_4(Data));
  Reg_8Bit reg_8bit_124 (.in_1(Data), .Setter(and_371_out), .Enable(and_372_out), .out_4(Data));
  Reg_8Bit reg_8bit_125 (.in_1(Data), .Setter(and_374_out), .Enable(and_375_out), .out_4(Data));
  Reg_8Bit reg_8bit_126 (.in_1(Data), .Setter(and_377_out), .Enable(and_378_out), .out_4(Data));
  Reg_8Bit reg_8bit_127 (.in_1(Data), .Setter(and_380_out), .Enable(and_381_out), .out_4(Data));
  Reg_8Bit reg_8bit_128 (.in_1(Data), .Setter(and_383_out), .Enable(and_384_out), .out_4(Data));
  and and_385 (and_385_out, deco_4x16_2_output_7, deco_4x16_1_output_0);
  and and_386 (and_386_out, Write_Data, and_385_out);
  and and_387 (and_387_out, and_385_out, Enable_Data);
  buf and_388 (and_388_out, deco_4x16_2_output_7);  // AND_Gate
  and and_389 (and_389_out, Write_Data, and_388_out);
  and and_390 (and_390_out, and_388_out, Enable_Data);
  buf and_391 (and_391_out, deco_4x16_2_output_7);  // AND_Gate
  and and_392 (and_392_out, Write_Data, and_391_out);
  and and_393 (and_393_out, and_391_out, Enable_Data);
  buf and_394 (and_394_out, deco_4x16_2_output_7);  // AND_Gate
  and and_395 (and_395_out, Write_Data, and_394_out);
  and and_396 (and_396_out, and_394_out, Enable_Data);
  buf and_397 (and_397_out, deco_4x16_2_output_7);  // AND_Gate
  and and_398 (and_398_out, Write_Data, and_397_out);
  and and_399 (and_399_out, and_397_out, Enable_Data);
  buf and_400 (and_400_out, deco_4x16_2_output_7);  // AND_Gate
  and and_401 (and_401_out, Write_Data, and_400_out);
  and and_402 (and_402_out, and_400_out, Enable_Data);
  buf and_403 (and_403_out, deco_4x16_2_output_7);  // AND_Gate
  and and_404 (and_404_out, Write_Data, and_403_out);
  and and_405 (and_405_out, and_403_out, Enable_Data);
  buf and_406 (and_406_out, deco_4x16_2_output_7);  // AND_Gate
  and and_407 (and_407_out, Write_Data, and_406_out);
  and and_408 (and_408_out, and_406_out, Enable_Data);
  buf and_409 (and_409_out, deco_4x16_2_output_7);  // AND_Gate
  and and_410 (and_410_out, Write_Data, and_409_out);
  and and_411 (and_411_out, and_409_out, Enable_Data);
  buf and_412 (and_412_out, deco_4x16_2_output_7);  // AND_Gate
  and and_413 (and_413_out, Write_Data, and_412_out);
  and and_414 (and_414_out, and_412_out, Enable_Data);
  buf and_415 (and_415_out, deco_4x16_2_output_7);  // AND_Gate
  and and_416 (and_416_out, Write_Data, and_415_out);
  and and_417 (and_417_out, and_415_out, Enable_Data);
  buf and_418 (and_418_out, deco_4x16_2_output_7);  // AND_Gate
  and and_419 (and_419_out, Write_Data, and_418_out);
  and and_420 (and_420_out, and_418_out, Enable_Data);
  buf and_421 (and_421_out, deco_4x16_2_output_7);  // AND_Gate
  and and_422 (and_422_out, Write_Data, and_421_out);
  and and_423 (and_423_out, and_421_out, Enable_Data);
  buf and_424 (and_424_out, deco_4x16_2_output_7);  // AND_Gate
  and and_425 (and_425_out, Write_Data, and_424_out);
  and and_426 (and_426_out, and_424_out, Enable_Data);
  buf and_427 (and_427_out, deco_4x16_2_output_7);  // AND_Gate
  and and_428 (and_428_out, Write_Data, and_427_out);
  and and_429 (and_429_out, and_427_out, Enable_Data);
  and and_430 (and_430_out, deco_4x16_2_output_7, deco_4x16_1_output_15);
  and and_431 (and_431_out, Write_Data, and_430_out);
  and and_432 (and_432_out, and_430_out, Enable_Data);
  and and_433 (and_433_out, deco_4x16_2_output_6, deco_4x16_1_output_0);
  Reg_8Bit reg_8bit_129 (.in_1(Data), .Setter(and_386_out), .Enable(and_387_out), .out_4(Data));
  and and_434 (and_434_out, deco_4x16_2_output_6, deco_4x16_1_output_1);
  Reg_8Bit reg_8bit_130 (.in_1(Data), .Setter(and_389_out), .Enable(and_390_out), .out_4(Data));
  and and_435 (and_435_out, deco_4x16_2_output_6, deco_4x16_1_output_2);
  Reg_8Bit reg_8bit_131 (.in_1(Data), .Setter(and_392_out), .Enable(and_393_out), .out_4(Data));
  and and_436 (and_436_out, deco_4x16_2_output_6, deco_4x16_1_output_3);
  Reg_8Bit reg_8bit_132 (.in_1(Data), .Setter(and_395_out), .Enable(and_396_out), .out_4(Data));
  and and_437 (and_437_out, deco_4x16_2_output_6, deco_4x16_1_output_4);
  Reg_8Bit reg_8bit_133 (.in_1(Data), .Setter(and_398_out), .Enable(and_399_out), .out_4(Data));
  and and_438 (and_438_out, deco_4x16_2_output_6, deco_4x16_1_output_5);
  Reg_8Bit reg_8bit_134 (.in_1(Data), .Setter(and_401_out), .Enable(and_402_out), .out_4(Data));
  and and_439 (and_439_out, deco_4x16_2_output_6, deco_4x16_1_output_6);
  Reg_8Bit reg_8bit_135 (.in_1(Data), .Setter(and_404_out), .Enable(and_405_out), .out_4(Data));
  and and_440 (and_440_out, deco_4x16_2_output_6, deco_4x16_1_output_7);
  Reg_8Bit reg_8bit_136 (.in_1(Data), .Setter(and_407_out), .Enable(and_408_out), .out_4(Data));
  and and_441 (and_441_out, deco_4x16_2_output_6, deco_4x16_1_output_8);
  Reg_8Bit reg_8bit_137 (.in_1(Data), .Setter(and_410_out), .Enable(and_411_out), .out_4(Data));
  and and_442 (and_442_out, deco_4x16_2_output_6, deco_4x16_1_output_9);
  Reg_8Bit reg_8bit_138 (.in_1(Data), .Setter(and_413_out), .Enable(and_414_out), .out_4(Data));
  and and_443 (and_443_out, deco_4x16_2_output_6, deco_4x16_1_output_10);
  Reg_8Bit reg_8bit_139 (.in_1(Data), .Setter(and_416_out), .Enable(and_417_out), .out_4(Data));
  and and_444 (and_444_out, deco_4x16_2_output_6, deco_4x16_1_output_11);
  Reg_8Bit reg_8bit_140 (.in_1(Data), .Setter(and_419_out), .Enable(and_420_out), .out_4(Data));
  and and_445 (and_445_out, deco_4x16_2_output_6, deco_4x16_1_output_12);
  Reg_8Bit reg_8bit_141 (.in_1(Data), .Setter(and_422_out), .Enable(and_423_out), .out_4(Data));
  and and_446 (and_446_out, deco_4x16_2_output_6, deco_4x16_1_output_13);
  Reg_8Bit reg_8bit_142 (.in_1(Data), .Setter(and_425_out), .Enable(and_426_out), .out_4(Data));
  and and_447 (and_447_out, deco_4x16_2_output_6, deco_4x16_1_output_14);
  Reg_8Bit reg_8bit_143 (.in_1(Data), .Setter(and_428_out), .Enable(and_429_out), .out_4(Data));
  and and_448 (and_448_out, deco_4x16_2_output_6, deco_4x16_1_output_15);
  Reg_8Bit reg_8bit_144 (.in_1(Data), .Setter(and_431_out), .Enable(and_432_out), .out_4(Data));
  and and_449 (and_449_out, Write_Data, and_433_out);
  Reg_8Bit reg_8bit_145 (.in_1(Data), .Setter(and_449_out), .Enable(and_450_out), .out_4(Data));
  and and_450 (and_450_out, and_433_out, Enable_Data);
  and and_451 (and_451_out, Write_Data, and_434_out);
  Reg_8Bit reg_8bit_146 (.in_1(Data), .Setter(and_451_out), .Enable(and_452_out), .out_4(Data));
  and and_452 (and_452_out, and_434_out, Enable_Data);
  and and_453 (and_453_out, Write_Data, and_435_out);
  Reg_8Bit reg_8bit_147 (.in_1(Data), .Setter(and_453_out), .Enable(and_454_out), .out_4(Data));
  and and_454 (and_454_out, and_435_out, Enable_Data);
  and and_455 (and_455_out, Write_Data, and_436_out);
  Reg_8Bit reg_8bit_148 (.in_1(Data), .Setter(and_455_out), .Enable(and_456_out), .out_4(Data));
  and and_456 (and_456_out, and_436_out, Enable_Data);
  and and_457 (and_457_out, Write_Data, and_437_out);
  Reg_8Bit reg_8bit_149 (.in_1(Data), .Setter(and_457_out), .Enable(and_458_out), .out_4(Data));
  and and_458 (and_458_out, and_437_out, Enable_Data);
  and and_459 (and_459_out, Write_Data, and_438_out);
  Reg_8Bit reg_8bit_150 (.in_1(Data), .Setter(and_459_out), .Enable(and_460_out), .out_4(Data));
  and and_460 (and_460_out, and_438_out, Enable_Data);
  and and_461 (and_461_out, Write_Data, and_439_out);
  Reg_8Bit reg_8bit_151 (.in_1(Data), .Setter(and_461_out), .Enable(and_462_out), .out_4(Data));
  and and_462 (and_462_out, and_439_out, Enable_Data);
  and and_463 (and_463_out, Write_Data, and_440_out);
  Reg_8Bit reg_8bit_152 (.in_1(Data), .Setter(and_463_out), .Enable(and_464_out), .out_4(Data));
  and and_464 (and_464_out, and_440_out, Enable_Data);
  and and_465 (and_465_out, Write_Data, and_441_out);
  Reg_8Bit reg_8bit_153 (.in_1(Data), .Setter(and_465_out), .Enable(and_466_out), .out_4(Data));
  and and_466 (and_466_out, and_441_out, Enable_Data);
  and and_467 (and_467_out, Write_Data, and_442_out);
  Reg_8Bit reg_8bit_154 (.in_1(Data), .Setter(and_467_out), .Enable(and_468_out), .out_4(Data));
  and and_468 (and_468_out, and_442_out, Enable_Data);
  and and_469 (and_469_out, Write_Data, and_443_out);
  Reg_8Bit reg_8bit_155 (.in_1(Data), .Setter(and_469_out), .Enable(and_470_out), .out_4(Data));
  and and_470 (and_470_out, and_443_out, Enable_Data);
  and and_471 (and_471_out, Write_Data, and_444_out);
  Reg_8Bit reg_8bit_156 (.in_1(Data), .Setter(and_471_out), .Enable(and_472_out), .out_4(Data));
  and and_472 (and_472_out, and_444_out, Enable_Data);
  and and_473 (and_473_out, Write_Data, and_445_out);
  Reg_8Bit reg_8bit_157 (.in_1(Data), .Setter(and_473_out), .Enable(and_474_out), .out_4(Data));
  and and_474 (and_474_out, and_445_out, Enable_Data);
  and and_475 (and_475_out, Write_Data, and_446_out);
  Reg_8Bit reg_8bit_158 (.in_1(Data), .Setter(and_475_out), .Enable(and_476_out), .out_4(Data));
  and and_476 (and_476_out, and_446_out, Enable_Data);
  and and_477 (and_477_out, Write_Data, and_447_out);
  Reg_8Bit reg_8bit_159 (.in_1(Data), .Setter(and_477_out), .Enable(and_478_out), .out_4(Data));
  and and_478 (and_478_out, and_447_out, Enable_Data);
  and and_479 (and_479_out, Write_Data, and_448_out);
  Reg_8Bit reg_8bit_160 (.in_1(Data), .Setter(and_479_out), .Enable(and_480_out), .out_4(Data));
  and and_480 (and_480_out, and_448_out, Enable_Data);
  and and_481 (and_481_out, deco_4x16_2_output_5, deco_4x16_1_output_0);
  and and_482 (and_482_out, deco_4x16_2_output_5, deco_4x16_1_output_1);
  buf and_483 (and_483_out, deco_4x16_2_output_5);  // AND_Gate
  and and_484 (and_484_out, deco_4x16_2_output_5, deco_4x16_1_output_3);
  and and_485 (and_485_out, deco_4x16_2_output_5, deco_4x16_1_output_4);
  and and_486 (and_486_out, deco_4x16_2_output_5, deco_4x16_1_output_5);
  and and_487 (and_487_out, deco_4x16_2_output_5, deco_4x16_1_output_6);
  and and_488 (and_488_out, deco_4x16_2_output_5, deco_4x16_1_output_7);
  and and_489 (and_489_out, deco_4x16_2_output_5, deco_4x16_1_output_8);
  and and_490 (and_490_out, deco_4x16_2_output_5, deco_4x16_1_output_9);
  buf and_491 (and_491_out, deco_4x16_2_output_5);  // AND_Gate
  and and_492 (and_492_out, deco_4x16_2_output_5, deco_4x16_1_output_11);
  and and_493 (and_493_out, deco_4x16_2_output_5, deco_4x16_1_output_12);
  and and_494 (and_494_out, deco_4x16_2_output_5, deco_4x16_1_output_13);
  and and_495 (and_495_out, deco_4x16_2_output_5, deco_4x16_1_output_14);
  and and_496 (and_496_out, deco_4x16_2_output_5, deco_4x16_1_output_15);
  and and_497 (and_497_out, Write_Data, and_481_out);
  Reg_8Bit reg_8bit_161 (.in_1(Data), .Setter(and_497_out), .Enable(and_498_out), .out_4(Data));
  and and_498 (and_498_out, and_481_out, Enable_Data);
  and and_499 (and_499_out, Write_Data, and_482_out);
  Reg_8Bit reg_8bit_162 (.in_1(Data), .Setter(and_499_out), .Enable(and_500_out), .out_4(Data));
  and and_500 (and_500_out, and_482_out, Enable_Data);
  and and_501 (and_501_out, Write_Data, and_483_out);
  Reg_8Bit reg_8bit_163 (.in_1(Data), .Setter(and_501_out), .Enable(and_502_out), .out_4(Data));
  and and_502 (and_502_out, and_483_out, Enable_Data);
  and and_503 (and_503_out, Write_Data, and_484_out);
  Reg_8Bit reg_8bit_164 (.in_1(Data), .Setter(and_503_out), .Enable(and_504_out), .out_4(Data));
  and and_504 (and_504_out, and_484_out, Enable_Data);
  and and_505 (and_505_out, Write_Data, and_485_out);
  Reg_8Bit reg_8bit_165 (.in_1(Data), .Setter(and_505_out), .Enable(and_506_out), .out_4(Data));
  and and_506 (and_506_out, and_485_out, Enable_Data);
  and and_507 (and_507_out, Write_Data, and_486_out);
  Reg_8Bit reg_8bit_166 (.in_1(Data), .Setter(and_507_out), .Enable(and_508_out), .out_4(Data));
  and and_508 (and_508_out, and_486_out, Enable_Data);
  and and_509 (and_509_out, Write_Data, and_487_out);
  Reg_8Bit reg_8bit_167 (.in_1(Data), .Setter(and_509_out), .Enable(and_510_out), .out_4(Data));
  and and_510 (and_510_out, and_487_out, Enable_Data);
  and and_511 (and_511_out, Write_Data, and_488_out);
  Reg_8Bit reg_8bit_168 (.in_1(Data), .Setter(and_511_out), .Enable(and_512_out), .out_4(Data));
  and and_512 (and_512_out, and_488_out, Enable_Data);
  and and_513 (and_513_out, Write_Data, and_489_out);
  Reg_8Bit reg_8bit_169 (.in_1(Data), .Setter(and_513_out), .Enable(and_514_out), .out_4(Data));
  and and_514 (and_514_out, and_489_out, Enable_Data);
  and and_515 (and_515_out, Write_Data, and_490_out);
  Reg_8Bit reg_8bit_170 (.in_1(Data), .Setter(and_515_out), .Enable(and_516_out), .out_4(Data));
  and and_516 (and_516_out, and_490_out, Enable_Data);
  and and_517 (and_517_out, Write_Data, and_491_out);
  Reg_8Bit reg_8bit_171 (.in_1(Data), .Setter(and_517_out), .Enable(and_518_out), .out_4(Data));
  and and_518 (and_518_out, and_491_out, Enable_Data);
  and and_519 (and_519_out, Write_Data, and_492_out);
  Reg_8Bit reg_8bit_172 (.in_1(Data), .Setter(and_519_out), .Enable(and_520_out), .out_4(Data));
  and and_520 (and_520_out, and_492_out, Enable_Data);
  and and_521 (and_521_out, Write_Data, and_493_out);
  Reg_8Bit reg_8bit_173 (.in_1(Data), .Setter(and_521_out), .Enable(and_522_out), .out_4(Data));
  and and_522 (and_522_out, and_493_out, Enable_Data);
  and and_523 (and_523_out, Write_Data, and_494_out);
  Reg_8Bit reg_8bit_174 (.in_1(Data), .Setter(and_523_out), .Enable(and_524_out), .out_4(Data));
  and and_524 (and_524_out, and_494_out, Enable_Data);
  and and_525 (and_525_out, Write_Data, and_495_out);
  Reg_8Bit reg_8bit_175 (.in_1(Data), .Setter(and_525_out), .Enable(and_526_out), .out_4(Data));
  and and_526 (and_526_out, and_495_out, Enable_Data);
  and and_527 (and_527_out, Write_Data, and_496_out);
  Reg_8Bit reg_8bit_176 (.in_1(Data), .Setter(and_527_out), .Enable(and_528_out), .out_4(Data));
  and and_528 (and_528_out, and_496_out, Enable_Data);
  and and_529 (and_529_out, deco_4x16_2_output_4, deco_4x16_1_output_0);
  and and_530 (and_530_out, Write_Data, and_529_out);
  and and_531 (and_531_out, and_529_out, Enable_Data);
  and and_532 (and_532_out, deco_4x16_2_output_4, deco_4x16_1_output_1);
  and and_533 (and_533_out, Write_Data, and_532_out);
  and and_534 (and_534_out, and_532_out, Enable_Data);
  buf and_535 (and_535_out, deco_4x16_2_output_4);  // AND_Gate
  and and_536 (and_536_out, Write_Data, and_535_out);
  and and_537 (and_537_out, and_535_out, Enable_Data);
  and and_538 (and_538_out, deco_4x16_2_output_4, deco_4x16_1_output_3);
  and and_539 (and_539_out, Write_Data, and_538_out);
  and and_540 (and_540_out, and_538_out, Enable_Data);
  and and_541 (and_541_out, deco_4x16_2_output_4, deco_4x16_1_output_4);
  and and_542 (and_542_out, Write_Data, and_541_out);
  and and_543 (and_543_out, and_541_out, Enable_Data);
  and and_544 (and_544_out, deco_4x16_2_output_4, deco_4x16_1_output_5);
  and and_545 (and_545_out, Write_Data, and_544_out);
  and and_546 (and_546_out, and_544_out, Enable_Data);
  and and_547 (and_547_out, deco_4x16_2_output_4, deco_4x16_1_output_6);
  and and_548 (and_548_out, Write_Data, and_547_out);
  and and_549 (and_549_out, and_547_out, Enable_Data);
  and and_550 (and_550_out, deco_4x16_2_output_4, deco_4x16_1_output_7);
  and and_551 (and_551_out, Write_Data, and_550_out);
  and and_552 (and_552_out, and_550_out, Enable_Data);
  and and_553 (and_553_out, deco_4x16_2_output_4, deco_4x16_1_output_8);
  and and_554 (and_554_out, Write_Data, and_553_out);
  and and_555 (and_555_out, and_553_out, Enable_Data);
  and and_556 (and_556_out, deco_4x16_2_output_4, deco_4x16_1_output_9);
  and and_557 (and_557_out, Write_Data, and_556_out);
  and and_558 (and_558_out, and_556_out, Enable_Data);
  buf and_559 (and_559_out, deco_4x16_2_output_4);  // AND_Gate
  and and_560 (and_560_out, Write_Data, and_559_out);
  and and_561 (and_561_out, and_559_out, Enable_Data);
  and and_562 (and_562_out, deco_4x16_2_output_4, deco_4x16_1_output_11);
  and and_563 (and_563_out, Write_Data, and_562_out);
  and and_564 (and_564_out, and_562_out, Enable_Data);
  and and_565 (and_565_out, deco_4x16_2_output_4, deco_4x16_1_output_12);
  and and_566 (and_566_out, Write_Data, and_565_out);
  and and_567 (and_567_out, and_565_out, Enable_Data);
  and and_568 (and_568_out, deco_4x16_2_output_4, deco_4x16_1_output_13);
  and and_569 (and_569_out, Write_Data, and_568_out);
  and and_570 (and_570_out, and_568_out, Enable_Data);
  and and_571 (and_571_out, deco_4x16_2_output_4, deco_4x16_1_output_14);
  and and_572 (and_572_out, Write_Data, and_571_out);
  and and_573 (and_573_out, and_571_out, Enable_Data);
  and and_574 (and_574_out, deco_4x16_2_output_4, deco_4x16_1_output_15);
  and and_575 (and_575_out, Write_Data, and_574_out);
  and and_576 (and_576_out, and_574_out, Enable_Data);
  Reg_8Bit reg_8bit_177 (.in_1(Data), .Setter(and_530_out), .Enable(and_531_out), .out_4(Data));
  Reg_8Bit reg_8bit_178 (.in_1(Data), .Setter(and_533_out), .Enable(and_534_out), .out_4(Data));
  Reg_8Bit reg_8bit_179 (.in_1(Data), .Setter(and_536_out), .Enable(and_537_out), .out_4(Data));
  Reg_8Bit reg_8bit_180 (.in_1(Data), .Setter(and_539_out), .Enable(and_540_out), .out_4(Data));
  Reg_8Bit reg_8bit_181 (.in_1(Data), .Setter(and_542_out), .Enable(and_543_out), .out_4(Data));
  Reg_8Bit reg_8bit_182 (.in_1(Data), .Setter(and_545_out), .Enable(and_546_out), .out_4(Data));
  Reg_8Bit reg_8bit_183 (.in_1(Data), .Setter(and_548_out), .Enable(and_549_out), .out_4(Data));
  Reg_8Bit reg_8bit_184 (.in_1(Data), .Setter(and_551_out), .Enable(and_552_out), .out_4(Data));
  Reg_8Bit reg_8bit_185 (.in_1(Data), .Setter(and_554_out), .Enable(and_555_out), .out_4(Data));
  Reg_8Bit reg_8bit_186 (.in_1(Data), .Setter(and_557_out), .Enable(and_558_out), .out_4(Data));
  Reg_8Bit reg_8bit_187 (.in_1(Data), .Setter(and_560_out), .Enable(and_561_out), .out_4(Data));
  Reg_8Bit reg_8bit_188 (.in_1(Data), .Setter(and_563_out), .Enable(and_564_out), .out_4(Data));
  Reg_8Bit reg_8bit_189 (.in_1(Data), .Setter(and_566_out), .Enable(and_567_out), .out_4(Data));
  Reg_8Bit reg_8bit_190 (.in_1(Data), .Setter(and_569_out), .Enable(and_570_out), .out_4(Data));
  Reg_8Bit reg_8bit_191 (.in_1(Data), .Setter(and_572_out), .Enable(and_573_out), .out_4(Data));
  Reg_8Bit reg_8bit_192 (.in_1(Data), .Setter(and_575_out), .Enable(and_576_out), .out_4(Data));
  and and_577 (and_577_out, deco_4x16_2_output_3, deco_4x16_1_output_0);
  and and_578 (and_578_out, Write_Data, and_577_out);
  and and_579 (and_579_out, and_577_out, Enable_Data);
  and and_580 (and_580_out, deco_4x16_2_output_3, deco_4x16_1_output_1);
  and and_581 (and_581_out, Write_Data, and_580_out);
  and and_582 (and_582_out, and_580_out, Enable_Data);
  buf and_583 (and_583_out, deco_4x16_2_output_3);  // AND_Gate
  and and_584 (and_584_out, Write_Data, and_583_out);
  and and_585 (and_585_out, and_583_out, Enable_Data);
  and and_586 (and_586_out, deco_4x16_2_output_3, deco_4x16_1_output_3);
  and and_587 (and_587_out, Write_Data, and_586_out);
  and and_588 (and_588_out, and_586_out, Enable_Data);
  and and_589 (and_589_out, deco_4x16_2_output_3, deco_4x16_1_output_4);
  and and_590 (and_590_out, Write_Data, and_589_out);
  and and_591 (and_591_out, and_589_out, Enable_Data);
  and and_592 (and_592_out, deco_4x16_2_output_3, deco_4x16_1_output_5);
  and and_593 (and_593_out, Write_Data, and_592_out);
  and and_594 (and_594_out, and_592_out, Enable_Data);
  and and_595 (and_595_out, deco_4x16_2_output_3, deco_4x16_1_output_6);
  and and_596 (and_596_out, Write_Data, and_595_out);
  and and_597 (and_597_out, and_595_out, Enable_Data);
  and and_598 (and_598_out, deco_4x16_2_output_3, deco_4x16_1_output_7);
  and and_599 (and_599_out, Write_Data, and_598_out);
  and and_600 (and_600_out, and_598_out, Enable_Data);
  and and_601 (and_601_out, deco_4x16_2_output_3, deco_4x16_1_output_8);
  and and_602 (and_602_out, Write_Data, and_601_out);
  and and_603 (and_603_out, and_601_out, Enable_Data);
  and and_604 (and_604_out, deco_4x16_2_output_3, deco_4x16_1_output_9);
  and and_605 (and_605_out, Write_Data, and_604_out);
  and and_606 (and_606_out, and_604_out, Enable_Data);
  buf and_607 (and_607_out, deco_4x16_2_output_3);  // AND_Gate
  and and_608 (and_608_out, Write_Data, and_607_out);
  and and_609 (and_609_out, and_607_out, Enable_Data);
  and and_610 (and_610_out, deco_4x16_2_output_3, deco_4x16_1_output_11);
  and and_611 (and_611_out, Write_Data, and_610_out);
  and and_612 (and_612_out, and_610_out, Enable_Data);
  and and_613 (and_613_out, deco_4x16_2_output_3, deco_4x16_1_output_12);
  and and_614 (and_614_out, Write_Data, and_613_out);
  and and_615 (and_615_out, and_613_out, Enable_Data);
  and and_616 (and_616_out, deco_4x16_2_output_3, deco_4x16_1_output_13);
  and and_617 (and_617_out, Write_Data, and_616_out);
  and and_618 (and_618_out, and_616_out, Enable_Data);
  and and_619 (and_619_out, deco_4x16_2_output_3, deco_4x16_1_output_14);
  and and_620 (and_620_out, Write_Data, and_619_out);
  and and_621 (and_621_out, and_619_out, Enable_Data);
  and and_622 (and_622_out, deco_4x16_2_output_3, deco_4x16_1_output_15);
  and and_623 (and_623_out, Write_Data, and_622_out);
  and and_624 (and_624_out, and_622_out, Enable_Data);
  and and_625 (and_625_out, deco_4x16_2_output_2, deco_4x16_1_output_0);
  Reg_8Bit reg_8bit_193 (.in_1(Data), .Setter(and_578_out), .Enable(and_579_out), .out_4(Data));
  and and_626 (and_626_out, deco_4x16_2_output_2, deco_4x16_1_output_1);
  Reg_8Bit reg_8bit_194 (.in_1(Data), .Setter(and_581_out), .Enable(and_582_out), .out_4(Data));
  buf and_627 (and_627_out, deco_4x16_2_output_2);  // AND_Gate
  Reg_8Bit reg_8bit_195 (.in_1(Data), .Setter(and_584_out), .Enable(and_585_out), .out_4(Data));
  and and_628 (and_628_out, deco_4x16_2_output_2, deco_4x16_1_output_3);
  Reg_8Bit reg_8bit_196 (.in_1(Data), .Setter(and_587_out), .Enable(and_588_out), .out_4(Data));
  and and_629 (and_629_out, deco_4x16_2_output_2, deco_4x16_1_output_4);
  Reg_8Bit reg_8bit_197 (.in_1(Data), .Setter(and_590_out), .Enable(and_591_out), .out_4(Data));
  and and_630 (and_630_out, deco_4x16_2_output_2, deco_4x16_1_output_5);
  Reg_8Bit reg_8bit_198 (.in_1(Data), .Setter(and_593_out), .Enable(and_594_out), .out_4(Data));
  and and_631 (and_631_out, deco_4x16_2_output_2, deco_4x16_1_output_6);
  Reg_8Bit reg_8bit_199 (.in_1(Data), .Setter(and_596_out), .Enable(and_597_out), .out_4(Data));
  and and_632 (and_632_out, deco_4x16_2_output_2, deco_4x16_1_output_7);
  Reg_8Bit reg_8bit_200 (.in_1(Data), .Setter(and_599_out), .Enable(and_600_out), .out_4(Data));
  and and_633 (and_633_out, deco_4x16_2_output_2, deco_4x16_1_output_8);
  Reg_8Bit reg_8bit_201 (.in_1(Data), .Setter(and_602_out), .Enable(and_603_out), .out_4(Data));
  and and_634 (and_634_out, deco_4x16_2_output_2, deco_4x16_1_output_9);
  Reg_8Bit reg_8bit_202 (.in_1(Data), .Setter(and_605_out), .Enable(and_606_out), .out_4(Data));
  buf and_635 (and_635_out, deco_4x16_2_output_2);  // AND_Gate
  Reg_8Bit reg_8bit_203 (.in_1(Data), .Setter(and_608_out), .Enable(and_609_out), .out_4(Data));
  and and_636 (and_636_out, deco_4x16_2_output_2, deco_4x16_1_output_11);
  Reg_8Bit reg_8bit_204 (.in_1(Data), .Setter(and_611_out), .Enable(and_612_out), .out_4(Data));
  and and_637 (and_637_out, deco_4x16_2_output_2, deco_4x16_1_output_12);
  Reg_8Bit reg_8bit_205 (.in_1(Data), .Setter(and_614_out), .Enable(and_615_out), .out_4(Data));
  and and_638 (and_638_out, deco_4x16_2_output_2, deco_4x16_1_output_13);
  Reg_8Bit reg_8bit_206 (.in_1(Data), .Setter(and_617_out), .Enable(and_618_out), .out_4(Data));
  and and_639 (and_639_out, deco_4x16_2_output_2, deco_4x16_1_output_14);
  Reg_8Bit reg_8bit_207 (.in_1(Data), .Setter(and_620_out), .Enable(and_621_out), .out_4(Data));
  and and_640 (and_640_out, deco_4x16_2_output_2, deco_4x16_1_output_15);
  Reg_8Bit reg_8bit_208 (.in_1(Data), .Setter(and_623_out), .Enable(and_624_out), .out_4(Data));
  and and_641 (and_641_out, Write_Data, and_625_out);
  Reg_8Bit reg_8bit_209 (.in_1(Data), .Setter(and_641_out), .Enable(and_642_out), .out_4(Data));
  and and_642 (and_642_out, and_625_out, Enable_Data);
  and and_643 (and_643_out, Write_Data, and_626_out);
  Reg_8Bit reg_8bit_210 (.in_1(Data), .Setter(and_643_out), .Enable(and_644_out), .out_4(Data));
  and and_644 (and_644_out, and_626_out, Enable_Data);
  and and_645 (and_645_out, Write_Data, and_627_out);
  Reg_8Bit reg_8bit_211 (.in_1(Data), .Setter(and_645_out), .Enable(and_646_out), .out_4(Data));
  and and_646 (and_646_out, and_627_out, Enable_Data);
  and and_647 (and_647_out, Write_Data, and_628_out);
  Reg_8Bit reg_8bit_212 (.in_1(Data), .Setter(and_647_out), .Enable(and_648_out), .out_4(Data));
  and and_648 (and_648_out, and_628_out, Enable_Data);
  and and_649 (and_649_out, Write_Data, and_629_out);
  Reg_8Bit reg_8bit_213 (.in_1(Data), .Setter(and_649_out), .Enable(and_650_out), .out_4(Data));
  and and_650 (and_650_out, and_629_out, Enable_Data);
  and and_651 (and_651_out, Write_Data, and_630_out);
  Reg_8Bit reg_8bit_214 (.in_1(Data), .Setter(and_651_out), .Enable(and_652_out), .out_4(Data));
  and and_652 (and_652_out, and_630_out, Enable_Data);
  and and_653 (and_653_out, Write_Data, and_631_out);
  Reg_8Bit reg_8bit_215 (.in_1(Data), .Setter(and_653_out), .Enable(and_654_out), .out_4(Data));
  and and_654 (and_654_out, and_631_out, Enable_Data);
  and and_655 (and_655_out, Write_Data, and_632_out);
  Reg_8Bit reg_8bit_216 (.in_1(Data), .Setter(and_655_out), .Enable(and_656_out), .out_4(Data));
  and and_656 (and_656_out, and_632_out, Enable_Data);
  and and_657 (and_657_out, Write_Data, and_633_out);
  Reg_8Bit reg_8bit_217 (.in_1(Data), .Setter(and_657_out), .Enable(and_658_out), .out_4(Data));
  and and_658 (and_658_out, and_633_out, Enable_Data);
  and and_659 (and_659_out, Write_Data, and_634_out);
  Reg_8Bit reg_8bit_218 (.in_1(Data), .Setter(and_659_out), .Enable(and_660_out), .out_4(Data));
  and and_660 (and_660_out, and_634_out, Enable_Data);
  and and_661 (and_661_out, Write_Data, and_635_out);
  Reg_8Bit reg_8bit_219 (.in_1(Data), .Setter(and_661_out), .Enable(and_662_out), .out_4(Data));
  and and_662 (and_662_out, and_635_out, Enable_Data);
  and and_663 (and_663_out, Write_Data, and_636_out);
  Reg_8Bit reg_8bit_220 (.in_1(Data), .Setter(and_663_out), .Enable(and_664_out), .out_4(Data));
  and and_664 (and_664_out, and_636_out, Enable_Data);
  and and_665 (and_665_out, Write_Data, and_637_out);
  Reg_8Bit reg_8bit_221 (.in_1(Data), .Setter(and_665_out), .Enable(and_666_out), .out_4(Data));
  and and_666 (and_666_out, and_637_out, Enable_Data);
  and and_667 (and_667_out, Write_Data, and_638_out);
  Reg_8Bit reg_8bit_222 (.in_1(Data), .Setter(and_667_out), .Enable(and_668_out), .out_4(Data));
  and and_668 (and_668_out, and_638_out, Enable_Data);
  and and_669 (and_669_out, Write_Data, and_639_out);
  Reg_8Bit reg_8bit_223 (.in_1(Data), .Setter(and_669_out), .Enable(and_670_out), .out_4(Data));
  and and_670 (and_670_out, and_639_out, Enable_Data);
  and and_671 (and_671_out, Write_Data, and_640_out);
  Reg_8Bit reg_8bit_224 (.in_1(Data), .Setter(and_671_out), .Enable(and_672_out), .out_4(Data));
  and and_672 (and_672_out, and_640_out, Enable_Data);
  and and_673 (and_673_out, deco_4x16_2_output_1, deco_4x16_1_output_0);
  and and_674 (and_674_out, deco_4x16_2_output_1, deco_4x16_1_output_1);
  buf and_675 (and_675_out, deco_4x16_2_output_1);  // AND_Gate
  and and_676 (and_676_out, deco_4x16_2_output_1, deco_4x16_1_output_3);
  and and_677 (and_677_out, deco_4x16_2_output_1, deco_4x16_1_output_4);
  and and_678 (and_678_out, deco_4x16_2_output_1, deco_4x16_1_output_5);
  and and_679 (and_679_out, deco_4x16_2_output_1, deco_4x16_1_output_6);
  and and_680 (and_680_out, deco_4x16_2_output_1, deco_4x16_1_output_7);
  and and_681 (and_681_out, deco_4x16_2_output_1, deco_4x16_1_output_8);
  and and_682 (and_682_out, deco_4x16_2_output_1, deco_4x16_1_output_9);
  buf and_683 (and_683_out, deco_4x16_2_output_1);  // AND_Gate
  and and_684 (and_684_out, deco_4x16_2_output_1, deco_4x16_1_output_11);
  and and_685 (and_685_out, deco_4x16_2_output_1, deco_4x16_1_output_12);
  and and_686 (and_686_out, deco_4x16_2_output_1, deco_4x16_1_output_13);
  and and_687 (and_687_out, deco_4x16_2_output_1, deco_4x16_1_output_14);
  and and_688 (and_688_out, deco_4x16_2_output_1, deco_4x16_1_output_15);
  and and_689 (and_689_out, Write_Data, and_673_out);
  Reg_8Bit reg_8bit_225 (.in_1(Data), .Setter(and_689_out), .Enable(and_690_out), .out_4(Data));
  and and_690 (and_690_out, and_673_out, Enable_Data);
  and and_691 (and_691_out, Write_Data, and_674_out);
  Reg_8Bit reg_8bit_226 (.in_1(Data), .Setter(and_691_out), .Enable(and_692_out), .out_4(Data));
  and and_692 (and_692_out, and_674_out, Enable_Data);
  and and_693 (and_693_out, Write_Data, and_675_out);
  Reg_8Bit reg_8bit_227 (.in_1(Data), .Setter(and_693_out), .Enable(and_694_out), .out_4(Data));
  and and_694 (and_694_out, and_675_out, Enable_Data);
  and and_695 (and_695_out, Write_Data, and_676_out);
  Reg_8Bit reg_8bit_228 (.in_1(Data), .Setter(and_695_out), .Enable(and_696_out), .out_4(Data));
  and and_696 (and_696_out, and_676_out, Enable_Data);
  and and_697 (and_697_out, Write_Data, and_677_out);
  Reg_8Bit reg_8bit_229 (.in_1(Data), .Setter(and_697_out), .Enable(and_698_out), .out_4(Data));
  and and_698 (and_698_out, and_677_out, Enable_Data);
  and and_699 (and_699_out, Write_Data, and_678_out);
  Reg_8Bit reg_8bit_230 (.in_1(Data), .Setter(and_699_out), .Enable(and_700_out), .out_4(Data));
  and and_700 (and_700_out, and_678_out, Enable_Data);
  and and_701 (and_701_out, Write_Data, and_679_out);
  Reg_8Bit reg_8bit_231 (.in_1(Data), .Setter(and_701_out), .Enable(and_702_out), .out_4(Data));
  and and_702 (and_702_out, and_679_out, Enable_Data);
  and and_703 (and_703_out, Write_Data, and_680_out);
  Reg_8Bit reg_8bit_232 (.in_1(Data), .Setter(and_703_out), .Enable(and_704_out), .out_4(Data));
  and and_704 (and_704_out, and_680_out, Enable_Data);
  and and_705 (and_705_out, Write_Data, and_681_out);
  Reg_8Bit reg_8bit_233 (.in_1(Data), .Setter(and_705_out), .Enable(and_706_out), .out_4(Data));
  and and_706 (and_706_out, and_681_out, Enable_Data);
  and and_707 (and_707_out, Write_Data, and_682_out);
  Reg_8Bit reg_8bit_234 (.in_1(Data), .Setter(and_707_out), .Enable(and_708_out), .out_4(Data));
  and and_708 (and_708_out, and_682_out, Enable_Data);
  and and_709 (and_709_out, Write_Data, and_683_out);
  Reg_8Bit reg_8bit_235 (.in_1(Data), .Setter(and_709_out), .Enable(and_710_out), .out_4(Data));
  and and_710 (and_710_out, and_683_out, Enable_Data);
  and and_711 (and_711_out, Write_Data, and_684_out);
  Reg_8Bit reg_8bit_236 (.in_1(Data), .Setter(and_711_out), .Enable(and_712_out), .out_4(Data));
  and and_712 (and_712_out, and_684_out, Enable_Data);
  and and_713 (and_713_out, Write_Data, and_685_out);
  Reg_8Bit reg_8bit_237 (.in_1(Data), .Setter(and_713_out), .Enable(and_714_out), .out_4(Data));
  and and_714 (and_714_out, and_685_out, Enable_Data);
  and and_715 (and_715_out, Write_Data, and_686_out);
  Reg_8Bit reg_8bit_238 (.in_1(Data), .Setter(and_715_out), .Enable(and_716_out), .out_4(Data));
  and and_716 (and_716_out, and_686_out, Enable_Data);
  and and_717 (and_717_out, Write_Data, and_687_out);
  Reg_8Bit reg_8bit_239 (.in_1(Data), .Setter(and_717_out), .Enable(and_718_out), .out_4(Data));
  and and_718 (and_718_out, and_687_out, Enable_Data);
  and and_719 (and_719_out, Write_Data, and_688_out);
  Reg_8Bit reg_8bit_240 (.in_1(Data), .Setter(and_719_out), .Enable(and_720_out), .out_4(Data));
  and and_720 (and_720_out, and_688_out, Enable_Data);
  and and_721 (and_721_out, deco_4x16_2_output_0, deco_4x16_1_output_0);
  and and_722 (and_722_out, Write_Data, and_721_out);
  and and_723 (and_723_out, and_721_out, Enable_Data);
  and and_724 (and_724_out, deco_4x16_2_output_0, deco_4x16_1_output_1);
  and and_725 (and_725_out, Write_Data, and_724_out);
  and and_726 (and_726_out, and_724_out, Enable_Data);
  and and_727 (and_727_out, deco_4x16_2_output_0, deco_4x16_1_output_2);
  and and_728 (and_728_out, Write_Data, and_727_out);
  and and_729 (and_729_out, and_727_out, Enable_Data);
  and and_730 (and_730_out, deco_4x16_2_output_0, deco_4x16_1_output_3);
  and and_731 (and_731_out, Write_Data, and_730_out);
  and and_732 (and_732_out, and_730_out, Enable_Data);
  and and_733 (and_733_out, deco_4x16_2_output_0, deco_4x16_1_output_4);
  and and_734 (and_734_out, Write_Data, and_733_out);
  and and_735 (and_735_out, and_733_out, Enable_Data);
  and and_736 (and_736_out, deco_4x16_2_output_0, deco_4x16_1_output_5);
  and and_737 (and_737_out, Write_Data, and_736_out);
  and and_738 (and_738_out, and_736_out, Enable_Data);
  and and_739 (and_739_out, deco_4x16_2_output_0, deco_4x16_1_output_6);
  and and_740 (and_740_out, Write_Data, and_739_out);
  and and_741 (and_741_out, and_739_out, Enable_Data);
  and and_742 (and_742_out, deco_4x16_2_output_0, deco_4x16_1_output_7);
  and and_743 (and_743_out, Write_Data, and_742_out);
  and and_744 (and_744_out, and_742_out, Enable_Data);
  and and_745 (and_745_out, deco_4x16_2_output_0, deco_4x16_1_output_8);
  and and_746 (and_746_out, Write_Data, and_745_out);
  and and_747 (and_747_out, and_745_out, Enable_Data);
  and and_748 (and_748_out, deco_4x16_2_output_0, deco_4x16_1_output_9);
  and and_749 (and_749_out, Write_Data, and_748_out);
  and and_750 (and_750_out, and_748_out, Enable_Data);
  and and_751 (and_751_out, deco_4x16_2_output_0, deco_4x16_1_output_10);
  and and_752 (and_752_out, Write_Data, and_751_out);
  and and_753 (and_753_out, and_751_out, Enable_Data);
  and and_754 (and_754_out, deco_4x16_2_output_0, deco_4x16_1_output_11);
  and and_755 (and_755_out, Write_Data, and_754_out);
  and and_756 (and_756_out, and_754_out, Enable_Data);
  and and_757 (and_757_out, deco_4x16_2_output_0, deco_4x16_1_output_12);
  and and_758 (and_758_out, Write_Data, and_757_out);
  and and_759 (and_759_out, and_757_out, Enable_Data);
  and and_760 (and_760_out, deco_4x16_2_output_0, deco_4x16_1_output_13);
  and and_761 (and_761_out, Write_Data, and_760_out);
  and and_762 (and_762_out, and_760_out, Enable_Data);
  and and_763 (and_763_out, deco_4x16_2_output_0, deco_4x16_1_output_14);
  and and_764 (and_764_out, Write_Data, and_763_out);
  and and_765 (and_765_out, and_763_out, Enable_Data);
  and and_766 (and_766_out, deco_4x16_2_output_0, deco_4x16_1_output_15);
  and and_767 (and_767_out, Write_Data, and_766_out);
  and and_768 (and_768_out, and_766_out, Enable_Data);
  Reg_8Bit reg_8bit_241 (.in_1(Data), .Setter(and_722_out), .Enable(and_723_out), .out_4(Data));
  Reg_8Bit reg_8bit_242 (.in_1(Data), .Setter(and_725_out), .Enable(and_726_out), .out_4(Data));
  Reg_8Bit reg_8bit_243 (.in_1(Data), .Setter(and_728_out), .Enable(and_729_out), .out_4(Data));
  Reg_8Bit reg_8bit_244 (.in_1(Data), .Setter(and_731_out), .Enable(and_732_out), .out_4(Data));
  Reg_8Bit reg_8bit_245 (.in_1(Data), .Setter(and_734_out), .Enable(and_735_out), .out_4(Data));
  Reg_8Bit reg_8bit_246 (.in_1(Data), .Setter(and_737_out), .Enable(and_738_out), .out_4(Data));
  Reg_8Bit reg_8bit_247 (.in_1(Data), .Setter(and_740_out), .Enable(and_741_out), .out_4(Data));
  Reg_8Bit reg_8bit_248 (.in_1(Data), .Setter(and_743_out), .Enable(and_744_out), .out_4(Data));
  Reg_8Bit reg_8bit_249 (.in_1(Data), .Setter(and_746_out), .Enable(and_747_out), .out_4(Data));
  Reg_8Bit reg_8bit_250 (.in_1(Data), .Setter(and_749_out), .Enable(and_750_out), .out_4(Data));
  Reg_8Bit reg_8bit_251 (.in_1(Data), .Setter(and_752_out), .Enable(and_753_out), .out_4(Data));
  Reg_8Bit reg_8bit_252 (.in_1(Data), .Setter(and_755_out), .Enable(and_756_out), .out_4(Data));
  Reg_8Bit reg_8bit_253 (.in_1(Data), .Setter(and_758_out), .Enable(and_759_out), .out_4(Data));
  Reg_8Bit reg_8bit_254 (.in_1(Data), .Setter(and_761_out), .Enable(and_762_out), .out_4(Data));
  Reg_8Bit reg_8bit_255 (.in_1(Data), .Setter(and_764_out), .Enable(and_765_out), .out_4(Data));
  Reg_8Bit reg_8bit_256 (.in_1(Data), .Setter(and_767_out), .Enable(and_768_out), .out_4(Data));

  // Other names for the same wires on the sheet: d[7:0] = Data; e = Enable_Data; s = Write_Data
endmodule

module L_Shift (
  input  [7:0] Input_data,
  input  c_in,
  output c_out,
  output [7:0] Output_data
);


  assign c_out = Input_data[7];
  assign Output_data = {Input_data[6:0], c_in};
endmodule

module R_Shift (
  input  c_in,
  input  [7:0] Input_data,
  output [7:0] Output_data,
  output c_out
);


  assign c_out = Input_data[0];
  assign Output_data = {c_in, Input_data[7:1]};
endmodule

module NOT_1Byte (
  input  [7:0] in_1,
  output [7:0] out_2
);

  assign out_2 = ~in_1;  // NOT_Gate not_1, 8 bits wide
endmodule

module AND_1Byte (
  input  [7:0] in_1,
  input  [7:0] in_2,
  output [7:0] out_3
);

  assign out_3 = in_1 & in_2;  // AND_Gate and_1, 8 bits wide
endmodule

module OR_1Byte (
  input  [7:0] in_1,
  input  [7:0] in_2,
  output [7:0] out_3
);

  assign out_3 = in_1 | in_2;  // OR_Gate or_1, 8 bits wide
endmodule

module XOR_1Byte (
  input  [7:0] in_1,
  input  [7:0] in_2,
  output [7:0] out_3
);

  assign out_3 = in_1 ^ in_2;  // XOR_Gate xor_1, 8 bits wide
endmodule

module ZERO_CMP (
  input  [7:0] in_1,
  output out_2
);

  nor nor_1 (out_2, in_1[0], in_1[1], in_1[2], in_1[3], in_1[4], in_1[5], in_1[6], in_1[7]);
endmodule

module CMP_1Byte (
  input  [7:0] B,
  input  [7:0] A,
  output [7:0] Difer,
  output Igual,
  output A_maior
);

  wire cmp_1bit_1_a_maior, cmp_1bit_1_igual, cmp_1bit_2_a_maior, cmp_1bit_2_igual, cmp_1bit_3_a_maior,
       cmp_1bit_3_igual, cmp_1bit_4_a_maior, cmp_1bit_4_igual, cmp_1bit_5_a_maior, cmp_1bit_5_igual,
       cmp_1bit_6_a_maior, cmp_1bit_6_igual, cmp_1bit_7_a_maior, cmp_1bit_7_igual;

  CMP_1Bit cmp_1bit_1 (
    .A(A[7]), .B(B[7]), .Ant_igual(1'b1), .Ant_A_maior(1'b0), .Igual(cmp_1bit_1_igual),
    .A_maior(cmp_1bit_1_a_maior), .Difer(Difer[7]));
  CMP_1Bit cmp_1bit_2 (
    .A(A[6]), .B(B[6]), .Ant_igual(cmp_1bit_1_igual), .Ant_A_maior(cmp_1bit_1_a_maior),
    .Igual(cmp_1bit_2_igual), .A_maior(cmp_1bit_2_a_maior), .Difer(Difer[6]));
  CMP_1Bit cmp_1bit_3 (
    .A(A[5]), .B(B[5]), .Ant_igual(cmp_1bit_2_igual), .Ant_A_maior(cmp_1bit_2_a_maior),
    .Igual(cmp_1bit_3_igual), .A_maior(cmp_1bit_3_a_maior), .Difer(Difer[5]));
  CMP_1Bit cmp_1bit_4 (
    .A(A[4]), .B(B[4]), .Ant_igual(cmp_1bit_3_igual), .Ant_A_maior(cmp_1bit_3_a_maior),
    .Igual(cmp_1bit_4_igual), .A_maior(cmp_1bit_4_a_maior), .Difer(Difer[4]));
  CMP_1Bit cmp_1bit_5 (
    .A(A[3]), .B(B[3]), .Ant_igual(cmp_1bit_4_igual), .Ant_A_maior(cmp_1bit_4_a_maior),
    .Igual(cmp_1bit_5_igual), .A_maior(cmp_1bit_5_a_maior), .Difer(Difer[3]));
  CMP_1Bit cmp_1bit_6 (
    .A(A[2]), .B(B[2]), .Ant_igual(cmp_1bit_5_igual), .Ant_A_maior(cmp_1bit_5_a_maior),
    .Igual(cmp_1bit_6_igual), .A_maior(cmp_1bit_6_a_maior), .Difer(Difer[2]));
  CMP_1Bit cmp_1bit_7 (
    .A(A[1]), .B(B[1]), .Ant_igual(cmp_1bit_6_igual), .Ant_A_maior(cmp_1bit_6_a_maior),
    .Igual(cmp_1bit_7_igual), .A_maior(cmp_1bit_7_a_maior), .Difer(Difer[1]));
  CMP_1Bit cmp_1bit_8 (
    .A(A[0]), .B(B[0]), .Ant_igual(cmp_1bit_7_igual), .Ant_A_maior(cmp_1bit_7_a_maior), .Igual(Igual),
    .A_maior(A_maior), .Difer(Difer[0]));
endmodule

module CMP_1Bit (
  input  Ant_igual,
  input  Ant_A_maior,
  input  A,
  input  B,
  output Difer,
  output Igual,
  output A_maior
);

  wire and_2_out;

  xor xor_1 (Difer, A, B);
  and and_1 (Igual, ~Difer, Ant_igual);  // AND_Gate
  and and_2 (and_2_out, A, Ant_igual, Difer);
  or or_1 (A_maior, and_2_out, Ant_A_maior);
endmodule

module ULA (
  input  [2:0] Op,
  input  c_in,
  input  [7:0] A,
  input  [7:0] B,
  output c_out,
  output [7:0] Res,
  output a_more_than_b,
  output a_equals_b,
  output res_zero
);

  wire adder_8bit_exp_1_c_out, l_shift_1_c_out, r_shift_1_c_out;
  wire [7:0] adder_8bit_exp_1_s0, and_1byte_1_out_3, l_shift_1_output_data, not_1byte_1_out_2,
       or_1byte_1_out_3, r_shift_1_output_data, xor_1byte_1_out_3;

  L_Shift l_shift_1 (.Input_data(A), .c_in(c_in), .c_out(l_shift_1_c_out), .Output_data(l_shift_1_output_data));
  R_Shift r_shift_1 (.c_in(c_in), .Input_data(A), .c_out(r_shift_1_c_out), .Output_data(r_shift_1_output_data));
  NOT_1Byte not_1byte_1 (.in_1(A), .out_2(not_1byte_1_out_2));
  AND_1Byte and_1byte_1 (.in_1(A), .in_2(B), .out_3(and_1byte_1_out_3));
  OR_1Byte or_1byte_1 (.in_1(A), .in_2(B), .out_3(or_1byte_1_out_3));
  XOR_1Byte xor_1byte_1 (.in_1(A), .in_2(B), .out_3(xor_1byte_1_out_3));
  CMP_1Byte cmp_1byte_1 (.B(B), .A(A), .Igual(a_equals_b), .A_maior(a_more_than_b));  // open: Difer
  Adder_8Bit_Exp adder_8bit_exp_1 (
    .A7(A[7]), .A2(A[2]), .A1(A[1]), .A0(A[0]), .B7(B[7]), .A6(A[6]), .B6(B[6]), .B5(B[5]), .B4(B[4]),
    .B3(B[3]), .B2(B[2]), .B1(B[1]), .B0(B[0]), .A5(A[5]), .A4(A[4]), .A3(A[3]),
    .C_out(adder_8bit_exp_1_c_out), .S0(adder_8bit_exp_1_s0[0]), .S1(adder_8bit_exp_1_s0[1]),
    .S2(adder_8bit_exp_1_s0[2]), .S3(adder_8bit_exp_1_s0[3]), .S4(adder_8bit_exp_1_s0[4]),
    .S5(adder_8bit_exp_1_s0[5]), .S6(adder_8bit_exp_1_s0[6]), .S7(adder_8bit_exp_1_s0[7]));
  Multiplexer #(.select(3), .width(8)) multiplexer_1 (
    .in0(adder_8bit_exp_1_s0), .in1(l_shift_1_output_data), .in2(r_shift_1_output_data),
    .in3(not_1byte_1_out_2), .in4(and_1byte_1_out_3), .in5(or_1byte_1_out_3), .in6(xor_1byte_1_out_3),
    .in7(A), .out(Res), .sel(Op));
  Multiplexer #(.select(3)) multiplexer_2 (
    .in0(adder_8bit_exp_1_c_out), .in1(l_shift_1_c_out), .in2(r_shift_1_c_out), .in3(1'b0), .in4(1'b0),
    .in5(1'b0), .in6(1'b0), .in7(1'b0), .out(c_out), .sel(Op));
  ZERO_CMP zero_cmp_1 (.in_1(Res), .out_2(res_zero));
  LED led_1 ();  // open: in
endmodule

module ULA_Exp (
  input  A7,
  input  A6,
  input  A5,
  input  A4,
  input  A3,
  input  A2,
  input  A1,
  input  A0,
  input  B7,
  input  B6,
  input  B5,
  input  B4,
  input  B3,
  input  B2,
  input  B1,
  input  B0,
  input  [2:0] Op,
  input  c_in,
  output c_out,
  output D0,
  output D1,
  output D2,
  output D3,
  output D4,
  output D5,
  output D6,
  output D7,
  output a_more_than_b,
  output a_equals_b,
  output res_zero
);

  wire adder_8bit_exp_1_c_out, demultiplexer_1_out0, demultiplexer_1_out1, demultiplexer_1_out2,
       demultiplexer_1_out3, demultiplexer_1_out4, demultiplexer_1_out5, demultiplexer_1_out6,
       demultiplexer_1_out7, l_shift_1_c_out, r_shift_1_c_out;
  wire [7:0] adder_8bit_exp_1_s0, and_1byte_1_out_3, l_shift_1_output_data, not_1byte_1_out_2,
       or_1byte_1_out_3, r_shift_1_output_data, xor_1byte_1_out_3;

  L_Shift l_shift_1 (
    .Input_data({A7, A6, A5, A4, A3, A2, A1, A0}), .c_in(c_in), .c_out(l_shift_1_c_out),
    .Output_data(l_shift_1_output_data));
  R_Shift r_shift_1 (
    .c_in(c_in), .Input_data({A7, A6, A5, A4, A3, A2, A1, A0}), .c_out(r_shift_1_c_out),
    .Output_data(r_shift_1_output_data));
  NOT_1Byte not_1byte_1 (.in_1({A7, A6, A5, A4, A3, A2, A1, A0}), .out_2(not_1byte_1_out_2));
  AND_1Byte and_1byte_1 (
    .in_1({A7, A6, A5, A4, A3, A2, A1, A0}), .in_2({B7, B6, B5, B4, B3, B2, B1, B0}),
    .out_3(and_1byte_1_out_3));
  OR_1Byte or_1byte_1 (
    .in_1({A7, A6, A5, A4, A3, A2, A1, A0}), .in_2({B7, B6, B5, B4, B3, B2, B1, B0}), .out_3(or_1byte_1_out_3));
  XOR_1Byte xor_1byte_1 (
    .in_1({A7, A6, A5, A4, A3, A2, A1, A0}), .in_2({B7, B6, B5, B4, B3, B2, B1, B0}),
    .out_3(xor_1byte_1_out_3));
  CMP_1Byte cmp_1byte_1 (
    .B({B7, B6, B5, B4, B3, B2, B1, B0}), .A({A7, A6, A5, A4, A3, A2, A1, A0}), .Igual(a_equals_b),
    .A_maior(a_more_than_b));  // open: Difer
  Adder_8Bit_Exp adder_8bit_exp_1 (
    .A7(A7), .A2(A2), .A1(A1), .A0(A0), .B7(B7), .A6(A6), .B6(B6), .B5(B5), .B4(B4), .B3(B3), .B2(B2),
    .B1(B1), .B0(B0), .A5(A5), .A4(A4), .A3(A3), .C_out(adder_8bit_exp_1_c_out), .S0(adder_8bit_exp_1_s0[0]),
    .S1(adder_8bit_exp_1_s0[1]), .S2(adder_8bit_exp_1_s0[2]), .S3(adder_8bit_exp_1_s0[3]),
    .S4(adder_8bit_exp_1_s0[4]), .S5(adder_8bit_exp_1_s0[5]), .S6(adder_8bit_exp_1_s0[6]),
    .S7(adder_8bit_exp_1_s0[7]));
  Multiplexer #(.select(3), .width(8)) multiplexer_1 (
    .in0(adder_8bit_exp_1_s0), .in1(l_shift_1_output_data), .in2(r_shift_1_output_data),
    .in3(not_1byte_1_out_2), .in4(and_1byte_1_out_3), .in5(or_1byte_1_out_3), .in6(xor_1byte_1_out_3),
    .in7({A7, A6, A5, A4, A3, A2, A1, A0}), .out({D7, D6, D5, D4, D3, D2, D1, D0}), .sel(Op));
  Demultiplexer #(.select(3)) demultiplexer_1 (
    .out0(demultiplexer_1_out0), .out1(demultiplexer_1_out1), .out2(demultiplexer_1_out2),
    .out3(demultiplexer_1_out3), .out4(demultiplexer_1_out4), .out5(demultiplexer_1_out5),
    .out6(demultiplexer_1_out6), .out7(demultiplexer_1_out7), .in(1'b1), .sel(Op));
  Multiplexer #(.select(3)) multiplexer_2 (
    .in0(adder_8bit_exp_1_c_out), .in1(l_shift_1_c_out), .in2(r_shift_1_c_out), .in3(1'b0), .in4(1'b0),
    .in5(1'b0), .in6(1'b0), .in7(1'b0), .out(c_out), .sel(Op));
  ZERO_CMP zero_cmp_1 (.in_1({D7, D6, D5, D4, D3, D2, D1, D0}), .out_2(res_zero));
  LED sum (.in(demultiplexer_1_out0));
  LED left (.in(demultiplexer_1_out1));
  LED right (.in(demultiplexer_1_out2));
  LED noter (.in(demultiplexer_1_out3));
  LED ander (.in(demultiplexer_1_out4));
  LED orer (.in(demultiplexer_1_out5));
  LED xorer (.in(demultiplexer_1_out6));
  LED ber (.in(demultiplexer_1_out7));
endmodule
