// Logisim project luiz_gabriel_antunes_sena_novo.circ as structural Verilog: 12 circuits, main circuit main
module main (
  input  in_1,
  input  in_2,
  input  in_3,
  input  in_4,
  input  in_5,
  input  in_6,
  input  in_7,
  input  in_8,
  input  in_9,
  input  in_10,
  input  in_11,
  input  in_12,
  input  in_13,
  input  in_14,
  input  [2:0] OP,
  input  in_16,
  input  in_17,
  input  in_18,
  output carry,
  output a_maior,
  output iguais,
  output zero
);

  wire or_1_out;
  wire [7:0] ACC_q, bus_2_out_3, controlled_buffer_1_out, IAR_q, IR_q, R0_q, R1_q, R2_q, R3_q, register_1_q,
       TMP_q, ula_1_s;

  // Probe on controlled_buffer_1_out
  assign controlled_buffer_1_out = in_8 ? R0_q : 8'bz;  // Controlled_Buffer controlled_buffer_1
  Register R0 (.D(controlled_buffer_1_out), .Q(R0_q), .clk(in_4));  // open: en, clr
  Register TMP (.D(controlled_buffer_1_out), .Q(TMP_q), .clk(in_18));  // open: en, clr
  assign controlled_buffer_1_out = in_9 ? R1_q : 8'bz;  // Controlled_Buffer controlled_buffer_2
  Register R1 (.D(controlled_buffer_1_out), .Q(R1_q), .clk(in_5));  // open: en, clr
  bus_1 bus_2 (.in_1(TMP_q), .out_3(bus_2_out_3));  // open: in_2
  assign controlled_buffer_1_out = in_10 ? R2_q : 8'bz;  // Controlled_Buffer controlled_buffer_3
  Register R2 (.D(controlled_buffer_1_out), .Q(R2_q), .clk(in_6));  // open: en, clr
  ula ula_1 (
    .A(controlled_buffer_1_out), .B(bus_2_out_3), .op(OP), .s(ula_1_s), .c_out(carry), .a_maior(a_maior),
    .iguais(iguais), .zero(zero));
  assign controlled_buffer_1_out = in_11 ? R3_q : 8'bz;  // Controlled_Buffer controlled_buffer_4
  Register R3 (.D(controlled_buffer_1_out), .Q(R3_q), .clk(in_7));  // open: en, clr
  Register ACC (.D(ula_1_s), .Q(ACC_q), .clk(in_16));  // open: en, clr
  assign controlled_buffer_1_out = in_17 ? ACC_q : 8'bz;  // Controlled_Buffer controlled_buffer_5
  RAM #(.databus("bidir")) ram_1 (.addr(register_1_q), .we(in_2), .oe(in_3), .clk(or_1_out));  // open: data
  Register register_1 (.D(controlled_buffer_1_out), .Q(register_1_q), .clk(in_1));  // open: en, clr
  or or_1 (or_1_out, in_2, in_3);
  Register IR (.D(controlled_buffer_1_out), .en(in_12), .Q(IR_q));  // open: clk, clr
  Register IAR (.D(controlled_buffer_1_out), .en(in_13), .Q(IAR_q));  // open: clk, clr
  assign controlled_buffer_1_out = in_14 ? IAR_q : 8'bz;  // Controlled_Buffer controlled_buffer_6
endmodule

module soma_1b (
  input  c_in,
  input  a,
  input  b,
  output s,
  output c_out
);

  wire and_1_out, and_2_out, and_3_out, xor_1_out;

  xor xor_1 (xor_1_out, a, b);
  and and_1 (and_1_out, a, b);
  and and_2 (and_2_out, c_in, a);
  and and_3 (and_3_out, c_in, b);
  xor xor_2 (s, xor_1_out, c_in);
  or or_1 (c_out, and_1_out, and_2_out, and_3_out);
endmodule

module soma_8b (
  input  [7:0] A,
  input  c_in,
  input  [7:0] B,
  output [7:0] S,
  output c_out
);

  wire soma_1b_1_c_out, soma_1b_2_c_out, soma_1b_3_c_out, soma_1b_4_c_out, soma_1b_5_c_out, soma_1b_6_c_out,
       soma_1b_7_c_out;

  soma_1b soma_1b_1 (.a(A[0]), .b(B[0]), .c_in(c_in), .c_out(soma_1b_1_c_out), .s(S[0]));
  soma_1b soma_1b_2 (.a(A[1]), .b(B[1]), .c_in(soma_1b_1_c_out), .c_out(soma_1b_2_c_out), .s(S[1]));
  soma_1b soma_1b_3 (.a(A[2]), .b(B[2]), .c_in(soma_1b_2_c_out), .c_out(soma_1b_3_c_out), .s(S[2]));
  soma_1b soma_1b_4 (.a(A[3]), .b(B[3]), .c_in(soma_1b_3_c_out), .c_out(soma_1b_4_c_out), .s(S[3]));
  soma_1b soma_1b_5 (.a(A[4]), .b(B[4]), .c_in(soma_1b_4_c_out), .c_out(soma_1b_5_c_out), .s(S[4]));
  soma_1b soma_1b_6 (.a(A[5]), .b(B[5]), .c_in(soma_1b_5_c_out), .c_out(soma_1b_6_c_out), .s(S[5]));
  soma_1b soma_1b_7 (.a(A[6]), .b(B[6]), .c_in(soma_1b_6_c_out), .c_out(soma_1b_7_c_out), .s(S[6]));
  soma_1b soma_1b_8 (.a(A[7]), .b(B[7]), .c_in(soma_1b_7_c_out), .c_out(c_out), .s(S[7]));
endmodule

module memoria_1b (
  input  i,
  input  s,
  output d
);

  wire nand_1_out, nand_2_out, nand_4_out;

  nand nand_1 (nand_1_out, i, s);
  nand nand_2 (nand_2_out, nand_1_out, s);
  nand nand_3 (d, nand_1_out, nand_4_out);
  nand nand_4 (nand_4_out, d, nand_2_out);
endmodule

module memoria_8b (
  input  [7:0] i,
  input  s,
  output [7:0] d
);

  memoria_1b memoria_1b_1 (.i(i[0]), .s(s), .d(d[0]));
  memoria_1b memoria_1b_2 (.i(i[1]), .s(s), .d(d[1]));
  memoria_1b memoria_1b_3 (.i(i[2]), .s(s), .d(d[2]));
  memoria_1b memoria_1b_4 (.i(i[3]), .s(s), .d(d[3]));
  memoria_1b memoria_1b_5 (.i(i[4]), .s(s), .d(d[4]));
  memoria_1b memoria_1b_6 (.i(i[5]), .s(s), .d(d[5]));
  memoria_1b memoria_1b_7 (.i(i[6]), .s(s), .d(d[6]));
  memoria_1b memoria_1b_8 (.i(i[7]), .s(s), .d(d[7]));
endmodule

module registrador_set_enable (
  input  [7:0] i,
  input  set,
  input  enable,
  output [7:0] d
);

  wire [7:0] bit_extender_1_out, memoria_8b_1_d;

  memoria_8b memoria_8b_1 (.i(i), .s(set), .d(memoria_8b_1_d));
  assign bit_extender_1_out = {{7{enable}}, enable};  // Bit_Extender bit_extender_1
  assign d = memoria_8b_1_d & bit_extender_1_out;  // AND_Gate and_1, 8 bits wide
endmodule

// ULA
module ula (
  input  [2:0] op,
  input  [7:0] A,
  input  [7:0] B,
  output [7:0] s,
  output c_out,
  output a_maior,
  output iguais,
  output zero
);

  wire shift_l_1_c_out, shift_r_1_c_out, soma_8b_1_c_out;
  wire [7:0] and_1_out, not_1_out, or_1_out, shift_l_1_d, shift_r_1_d, soma_8b_1_s, xor_1_out;

  assign not_1_out = ~B;  // NOT_Gate not_1, 8 bits wide
  soma_8b soma_8b_1 (.A(A), .B(B), .c_out(soma_8b_1_c_out), .S(soma_8b_1_s));  // open: c_in
  shift_r shift_r_1 (.i(B), .c_out(shift_r_1_c_out), .d(shift_r_1_d));  // open: c_in
  shift_l shift_l_1 (.i(B), .c_out(shift_l_1_c_out), .d(shift_l_1_d));  // open: c_in
  assign and_1_out = A & B;  // AND_Gate and_1, 8 bits wide
  assign or_1_out = A | B;  // OR_Gate or_1, 8 bits wide
  assign xor_1_out = A ^ B;  // XOR_Gate xor_1, 8 bits wide
  comp_8b comp_8b_1 (.A(A), .B(B), .a_maior(a_maior), .iguais(iguais));  // open: C
  Multiplexer #(.select(3), .width(8)) multiplexer_1 (
    .in0(soma_8b_1_s), .in1(shift_r_1_d), .in2(shift_l_1_d), .in3(not_1_out), .in4(and_1_out), .in5(B),
    .in6(or_1_out), .in7(xor_1_out), .out(s), .sel(op));
  Multiplexer #(.select(3)) multiplexer_2 (
    .in0(soma_8b_1_c_out), .in1(shift_r_1_c_out), .in2(shift_l_1_c_out), .in3(1'b0), .in4(1'b0), .in5(1'b0),
    .in6(1'b0), .in7(1'b0), .out(c_out), .sel(op));
  nor nor_1 (zero, s[0], s[1], s[2], s[3], s[4], s[5], s[6], s[7]);
endmodule

module shift_r (
  input  [7:0] i,
  input  c_in,
  output [7:0] d,
  output c_out
);


  assign c_out = i[0];
  assign d = {c_in, i[7:1]};
endmodule

module shift_l (
  input  c_in,
  input  [7:0] i,
  output [7:0] d,
  output c_out
);


  assign c_out = i[7];
  assign d = {i[6:0], c_in};
endmodule

module comp_1b (
  input  iguais_ant,
  input  a_maior_ant,
  input  a,
  input  b,
  output c,
  output iguais,
  output a_maior
);

  wire and_2_out;

  xor xor_1 (c, a, b);
  and and_1 (iguais, ~c, iguais_ant);  // AND_Gate
  and and_2 (and_2_out, a, iguais_ant, c);
  or or_1 (a_maior, and_2_out, a_maior_ant);
endmodule

module comp_8b (
  input  [7:0] A,
  input  [7:0] B,
  output [7:0] C,
  output a_maior,
  output iguais
);

  wire comp_1b_1_a_maior, comp_1b_1_iguais, comp_1b_2_a_maior, comp_1b_2_iguais, comp_1b_3_a_maior,
       comp_1b_3_iguais, comp_1b_4_a_maior, comp_1b_4_iguais, comp_1b_5_a_maior, comp_1b_5_iguais,
       comp_1b_6_a_maior, comp_1b_6_iguais, comp_1b_7_a_maior, comp_1b_7_iguais;

  comp_1b comp_1b_1 (
    .a(A[0]), .b(B[0]), .iguais_ant(1'b1), .a_maior_ant(1'b0), .iguais(comp_1b_1_iguais),
    .a_maior(comp_1b_1_a_maior), .c(C[0]));
  comp_1b comp_1b_2 (
    .a(A[1]), .b(B[1]), .iguais_ant(comp_1b_1_iguais), .a_maior_ant(comp_1b_1_a_maior),
    .iguais(comp_1b_2_iguais), .a_maior(comp_1b_2_a_maior), .c(C[1]));
  comp_1b comp_1b_3 (
    .a(A[2]), .b(B[2]), .iguais_ant(comp_1b_2_iguais), .a_maior_ant(comp_1b_2_a_maior),
    .iguais(comp_1b_3_iguais), .a_maior(comp_1b_3_a_maior), .c(C[2]));
  comp_1b comp_1b_4 (
    .a(A[3]), .b(B[3]), .iguais_ant(comp_1b_3_iguais), .a_maior_ant(comp_1b_3_a_maior),
    .iguais(comp_1b_4_iguais), .a_maior(comp_1b_4_a_maior), .c(C[3]));
  comp_1b comp_1b_5 (
    .a(A[4]), .b(B[4]), .iguais_ant(comp_1b_4_iguais), .a_maior_ant(comp_1b_4_a_maior),
    .iguais(comp_1b_5_iguais), .a_maior(comp_1b_5_a_maior), .c(C[4]));
  comp_1b comp_1b_6 (
    .a(A[5]), .b(B[5]), .iguais_ant(comp_1b_5_iguais), .a_maior_ant(comp_1b_5_a_maior),
    .iguais(comp_1b_6_iguais), .a_maior(comp_1b_6_a_maior), .c(C[5]));
  comp_1b comp_1b_7 (
    .a(A[6]), .b(B[6]), .iguais_ant(comp_1b_6_iguais), .a_maior_ant(comp_1b_6_a_maior),
    .iguais(comp_1b_7_iguais), .a_maior(comp_1b_7_a_maior), .c(C[6]));
  comp_1b comp_1b_8 (
    .a(A[7]), .b(B[7]), .iguais_ant(comp_1b_7_iguais), .a_maior_ant(comp_1b_7_a_maior), .iguais(iguais),
    .a_maior(a_maior), .c(C[7]));
endmodule

module bus_1 (
  input  [7:0] in_1,
  input  in_2,
  output [7:0] out_3
);

  Multiplexer #(.width(8)) multiplexer_1 (.in0(in_1), .in1(8'h1), .out(out_3), .sel(in_2));
endmodule
